// Logisim project tparq grupo 26 v2.2 operaciones.circ as structural Verilog
module Main (
);

  wire _0, _1, _1_t, _1a0, _1a1, _1a2, _1a3, _1b0, _1b1, _1b2, _1b3, _1c0, _1c1, _1c2, _1c3, _1cero, _1er_N,
       _2, _02_Divisor, _2_t, _2a0, _2a1, _2a2, _2a3, _2b0, _2b1, _2b2, _2b3, _2c0, _2c1, _2c2, _2c3, _2cero,
       _2do_N, _3, _3_t, _4, _5, _6, _7, _8, _9, _15_9, _15_9_1, _15_9_2, Ac, and_2_out, and_3_out,
       and_4_out, and_8_out, and_9_out, button_2_out, button_out, cdf0, cdf1, cdf2, cdf3, cero, ck,
       cnt_on_off, contador_0_15_1__2_0, contador_0_15_1__2_1, contador_0_15_1__2_2, contador_0_15_2__2_0,
       contador_0_15_2__2_1, display_1_a, display_1_b, display_1_c, display_1_d, display_1_e, display_1_f,
       display_1_g, display_2_a, display_2_b, display_2_c, display_2_d, display_2_e, display_2_f,
       display_2_g, display_3_a, display_3_b, display_3_c, display_3_d, display_3_e, display_3_f,
       display_3_g, division_1_s1, division_1_s2, division_1_s3, division_1_s4, division_1_s5, division_1_s6,
       float, mantener_r_1_out_5, not_1_out, op_x_1__1a0, op_x_1__1a1_2, op_x_1__1a2_2, op_x_1__1a3_2,
       op_x_1__1a4_2, op_x_1__2a0, op_x_1__2a1_2, op_x_1__2a2_2, op_x_1__2a3_2, op_x_1__2a4_2, op_x_2__1a0,
       op_x_2__1a1_2, op_x_2__1a2_2, op_x_2__1a3_2, op_x_2__1a4_2, op_x_2__2a0, op_x_2__2a1_2, op_x_2__2a2_2,
       op_x_2__2a3_2, op_x_2__2a4_2, or_1_out, or_2_out, part_1_r_plus_minus, part_1_rc0, part_1_rc1,
       part_1_rc2, part_1_rc3, part_1_rd0, part_1_rd1, part_1_rd2, part_1_rd3, part_1_ru0, part_1_ru1,
       part_1_ru2, part_1_ru3, proceso, pulso, R, R___a0, R___a1, R___a2, R___a3, R___b0, R___b1, R___b2,
       R___b3, R___c0, R___c1, R___c2, R___c3, R_a0, R_a1, R_a2, R_b0, R_b1, R_b2, R_b3, R_overflow, R_X,
       Ra0, Ra1, Ra2, Ra3, Rb0, Rb1, Rb2, Rb3, Rc0, Rc1, Rc2, Rc3, Rst, Rx, Rxa0, Rxa1, Rxa2, Rxb0, Rxb1,
       Rxb2, Rxb3, Rxc0, Rxoverflow, s_r_ff_2_q, s_r_ff_5_q, s_r_ff_6_q, SR_y_minus, Srx, tunnel, tunnel_t,
       tunnel_t_t, tunnel_t_t_t, tunnel_t_t_t_t, tunnel_t_t_t_t_t, x, x_multiplicacion_1_b2,
       x_multiplicacion_1_b3, x_multiplicacion_1_b4, x_multiplicacion_1_b5, x_multiplicacion_1_b6,
       x_multiplicacion_1_b7, xor_1_out, xor_2_out, xor_3_out;

  Clock clock_1 (.out(ck));
  xor xor_1 (xor_1_out, _2do_N, _1er_N);
  xor xor_2 (xor_2_out, R_X, tunnel_t_t_t_t_t);
  or or_1 (or_1_out, _15_9, Rxoverflow, R_overflow);
  and and_1 (Srx, xor_1_out, xor_2_out, ~cero);  // AND_Gate
  xor xor_3 (xor_3_out, SR_y_minus, Srx);
  or or_2 (or_2_out, or_1_out, xor_3_out);
  _7_Segment_Display u_7_segment_display_1 (
    .g(or_2_out), .f(or_1_out), .a(or_1_out), .e(or_1_out), .d(or_1_out));  // open: b, c, dp
  _7_Segment_Display u_7_segment_display_2 (
    .g(display_1_g), .f(display_1_a), .a(display_1_b), .b(display_1_c), .e(display_1_d), .d(display_1_f),
    .c(display_1_e));  // open: dp
  // Probe on proceso
  Button button (.out(button_out));
  signos_numeros signos_numeros_1 (.in_1(button_out), .Ac(Ac), .signo(_1er_N));
  Button button_2 (.out(button_2_out));
  signos_numeros signos_numeros_2 (.in_1(button_2_out), .Ac(Ac), .signo(_2do_N));
  display display_1 (
    .b3(Ra3), .b2(Ra2), .b1(Ra1), .b0(Ra0), .in_5(or_1_out), .a(display_1_a), .b(display_1_b),
    .c(display_1_c), .d(display_1_d), .e(display_1_e), .f(display_1_f), .g(display_1_g));
  Button u__9 (.out(_9));
  Button u__8 (.out(_8));
  Button u__6 (.out(_6));
  Button u__5 (.out(_5));
  Button u__3 (.out(_3_t));
  Button u__2 (.out(_2_t));
  Button u__0 (.out(_0));
  display display_2 (
    .b3(Rb3), .b2(Rb2), .b1(Rb1), .b0(Rb0), .in_5(or_1_out), .a(display_2_a), .b(display_2_b),
    .c(display_2_c), .d(display_2_d), .e(display_2_e), .f(display_2_f), .g(display_2_g));
  _7_Segment_Display u_7_segment_display_3 (
    .g(display_2_g), .f(display_2_a), .a(display_2_b), .b(display_2_c), .e(display_2_d), .d(display_2_f),
    .c(display_2_e), .dp(1'b1));
  Button u__7 (.out(_7));
  Button u__4 (.out(_4));
  Button u__1 (.out(_1_t));
  // Probe on cnt_on_off
  Button button_3 (.out(tunnel_t_t_t));
  Button u_x (.out(x));
  Button u_Ac (.out(Ac));
  Button button_4 (.out(tunnel_t_t));
  Button button_5 (.out(tunnel_t));
  Button button_6 (.out(tunnel_t_t_t_t));
  Button button_7 (.out(tunnel));
  display display_3 (
    .b3(Rc3), .b2(Rc2), .b1(Rc1), .b0(Rc0), .in_5(or_1_out), .a(display_3_a), .b(display_3_b),
    .c(display_3_c), .d(display_3_d), .e(display_3_e), .f(display_3_f), .g(display_3_g));
  _7_Segment_Display u_7_segment_display_4 (
    .g(display_3_g), .f(display_3_a), .a(display_3_b), .b(display_3_c), .e(display_3_d), .d(display_3_f),
    .c(display_3_e));  // open: dp
  // Probe on cdf3
  codificador_bcdn codificador_bcdn_1 (
    .n9(_9), .n8(_8), .n7(_7), .n6(_6), .n5(_5), .n4(_4), .n3(_3_t), .n2(_2_t), .n1(_1_t), .n0(_0),
    .cont_on_off(cnt_on_off), .Rst(Rst), .b3(cdf3), .b2(cdf2), .b1(cdf1), .b0(cdf0));
  // Probe on cdf0
  // Probe on cdf1
  // Probe on cdf2
  and and_2 (and_2_out, proceso, tunnel_t_t_t_t_t);
  and and_3 (and_3_out, proceso, tunnel_t_t_t_t_t);
  and and_4 (and_4_out, proceso, tunnel_t_t_t_t_t);
  R_unico r_unico_1 (
    .Rx3(Rxb3), .Rx2(Rxb2), .Rx1(Rxb1), .Rx0(Rxb0), .x(R_X), .R___3(R___b3), .R___2(R___b2), .R___1(R___b1),
    .R___0(R___b0), .r(R), .R_3(R_b3), .R_2(R_b2), .R_1(R_b1), .R_0(R_b0), .in_15(and_2_out), .Ac(Ac),
    .Ra3(Rb3), .Ra2(Rb2), .Ra1(Rb1), .Ra0(Rb0));
  R_unico r_unico_2 (
    .Rx3(1'b0), .Rx2(Rxc0), .Rx1(1'b0), .Rx0(Rxc0), .x(R_X), .R___3(R___c3), .R___2(R___c2), .R___1(R___c1),
    .R___0(R___c0), .r(R), .R_3(1'b0), .R_2(float), .R_1(1'b0), .R_0(float), .in_15(and_3_out), .Ac(Ac),
    .Ra3(Rc3), .Ra2(Rc2), .Ra1(Rc1), .Ra0(Rc0));
  R_unico r_unico_3 (
    .Rx3(1'b0), .Rx2(Rxa2), .Rx1(Rxa1), .Rx0(Rxa0), .x(R_X), .R___3(R___a3), .R___2(R___a2), .R___1(R___a1),
    .R___0(R___a0), .r(R), .R_3(1'b0), .R_2(R_a2), .R_1(R_a1), .R_0(R_a0), .in_15(and_4_out), .Ac(Ac),
    .Ra3(Ra3), .Ra2(Ra2), .Ra1(Ra1), .Ra0(Ra0));
  _15_9 u_15_9_1 (
    .a3(_1a3), .a2(_1a2), .a1(_1a1), .a0(_1a0), .b3(_1b3), .b2(_1b2), .b1(_1b1), .b0(_1b0), .overflow(_15_9_1));
  DIR_I_D dir_i_d_1 (
    .Dir(tunnel_t_t_t), .ck(ck), .Rst(Ac), .PulsoOn(pulso), .a3(cdf3), .a2(cdf2), .a1(cdf1), .a0(cdf0),
    .s23(_1a3), .s22(_1a2), .s21(_1a1), .s20(_1a0), .s19(_1b3), .s18(_1b2), .s17(_1b1), .s16(_1b0),
    .s15(_1c3), .s14(_1c2), .s13(_1c1), .s12(_1c0), .s11(_2a3), .s10(_2a2), .s9(_2a1), .s8(_2a0), .s7(_2b3),
    .s6(_2b2), .s5(_2b1), .s4(_2b0), .s3(_2c3), .s2(_2c2), .s1(_2c1), .s0(_2c0));
  or or_3 (_15_9, _15_9_1, _15_9_2);
  _15_9 u_15_9_2 (
    .a3(_2a3), .a2(_2a2), .a1(_2a1), .a0(_2a0), .b3(_2b3), .b2(_2b2), .b1(_2b1), .b0(_2b0), .overflow(_15_9_2));
  contador_0_15 contador_0_15_1 (
    .Ck(ck), .On(pulso), .estatus_contador(cnt_on_off), .Off(Rst), ._2_0(contador_0_15_1__2_0),
    ._2_1(contador_0_15_1__2_1), ._2_2(contador_0_15_1__2_2));  // open: _2, _2_3
  and and_5 (Rst, ~contador_0_15_1__2_0, ~contador_0_15_1__2_1, contador_0_15_1__2_2);  // AND_Gate
  cero cero_1 (
    .a3(_1a3), .a2(_1a2), .a1(_1a1), .a0(_1a0), .b3(_1b3), .b2(_1b2), .b1(_1b1), .b0(_1b0), .c3(_1c3),
    .c2(_1c2), .c1(_1c1), .c0(_1c0), ._0(_1cero));
  and and_6 (cero, _1cero, _2cero);
  pulso pulso_1 (
    ._9(_9), ._8(_8), ._7(_7), ._6(_6), ._5(_5), ._4(_4), ._3(_3_t), ._2(_2_t), ._1(_1_t), ._0(_0),
    .cnt_on_off(cnt_on_off), .pulso(pulso));
  // Probe on pulso
  cero cero_2 (
    .a3(_2a3), .a2(_2a2), .a1(_2a1), .a0(_2a0), .b3(_2b3), .b2(_2b2), .b1(_2b1), .b0(_2b0), .c3(_2c3),
    .c2(_2c2), .c1(_2c1), .c0(_2c0), ._0(_2cero));
  S_R_Flip_Flop s_r_ff_1 (.Q(Rx), .preset(x), .reset(Ac));  // open: S, clk, R, Qn, en
  S_R_Flip_Flop s_r_ff_2 (.Q(s_r_ff_2_q), .preset(tunnel_t_t_t_t), .reset(Ac));  // open: S, clk, R, Qn, en
  and and_7 (R_X, s_r_ff_2_q, Rx, ~_15_9);  // AND_Gate
  mantener_R mantener_r_1 (
    .in_1(tunnel), .in_2(tunnel_t), .in_3(tunnel_t_t_t_t), .AC(Ac), .out_5(mantener_r_1_out_5), .out_6(R));
  op_x op_x_1 (
    .condicion_1(R_X), .ac(Ac), ._1a4(_1b3), ._1a3(_1b2), ._1a2(_1b1), ._1a1(_1b0), ._1b3(_1a0), ._1c3(_1c3),
    ._1c2(_1c2), ._1c1(_1c1), ._1c0(_1c0), ._2a4(_2b3), ._2a3(_2b2), ._2a2(_2b1), ._2a1(_2b0), ._2b3(_2a0),
    ._2c3(_2c3), ._2c2(_2c2), ._2c1(_2c1), ._2c0(_2c0), ._1a4_2(op_x_1__1a4_2), ._1a3_2(op_x_1__1a3_2),
    ._1a2_2(op_x_1__1a2_2), ._1a1_2(op_x_1__1a1_2), ._1a0(op_x_1__1a0), ._2a4_2(op_x_1__2a4_2),
    ._2a3_2(op_x_1__2a3_2), ._2a2_2(op_x_1__2a2_2), ._2a1_2(op_x_1__2a1_2), ._2a0(op_x_1__2a0));
  X_multiplicacion x_multiplicacion_1 (
    ._1a4(op_x_1__1a4_2), ._1a3(op_x_1__1a3_2), ._1a2(op_x_1__1a2_2), ._1a1(op_x_1__1a1_2),
    ._1a0(op_x_1__1a0), ._2a4(op_x_1__2a4_2), ._2a3(op_x_1__2a3_2), ._2a2(op_x_1__2a2_2),
    ._2a1(op_x_1__2a1_2), ._2a0(op_x_1__2a0), .Error(Rxoverflow), .b7(x_multiplicacion_1_b7),
    .b6(x_multiplicacion_1_b6), .b5(x_multiplicacion_1_b5), .b4(x_multiplicacion_1_b4),
    .b3(x_multiplicacion_1_b3), .b2(x_multiplicacion_1_b2), .flotante(Rxc0));
  paso_resultado paso_resultado_1 (
    .c0(part_1_rc0), .c1(part_1_rc1), .c2(part_1_rc2), .c3(part_1_rc3), .b0(part_1_ru0), .b1(part_1_ru1),
    .b2(part_1_ru2), .b3(part_1_ru3), .a0(part_1_rd0), .a1(part_1_rd1), .a2(part_1_rd2), .a3(part_1_rd3),
    .igual(R), .c0_2(R___c0), .c1_2(R___c1), .c2_2(R___c2), .c3_2(R___c3), .b0_2(R___b0), .b1_2(R___b1),
    .b2_2(R___b2), .b3_2(R___b3), .a0_2(R___a0), .a1_2(R___a1), .a2_2(R___a2), .a3_2(R___a3));
  codificador_binario_bcdn cod_bn_BCD (
    .s5(x_multiplicacion_1_b7), .s4(x_multiplicacion_1_b6), .s3(x_multiplicacion_1_b5),
    .s2(x_multiplicacion_1_b4), .s1(x_multiplicacion_1_b3), .s0(x_multiplicacion_1_b2), .bcd6(Rxa2),
    .bcd5(Rxa1), .bcd4(Rxa0), .bcd3(Rxb3), .bcd2(Rxb2), .bcd1(Rxb1), .bcd0(Rxb0));
  circuit_2 part_1 (
    .signo_1(_1er_N), .signo_2(_2do_N), .o_minus(mantener_r_1_out_5), ._1a3(_1a3), ._1a2(_1a2), ._1a1(_1a1),
    ._1a0(_1a0), ._2a3(_2a3), ._2a2(_2a2), ._2a1(_2a1), ._2a0(_2a0), ._1b3(_1b3), ._1b2(_1b2), ._1b1(_1b1),
    ._1b0(_1b0), ._2b3(_2b3), ._2b2(_2b2), ._2b1(_2b1), ._2b0(_2b0), ._1c3(_1c3), ._1c2(_1c2), ._1c1(_1c1),
    ._1c0(_1c0), ._2c3(_2c3), ._2c2(_2c2), ._2c1(_2c1), ._2c0(_2c0), .Rd3(part_1_rd3), .Rd2(part_1_rd2),
    .Rd1(part_1_rd1), .Rd0(part_1_rd0), .Ru3(part_1_ru3), .Ru2(part_1_ru2), .Ru1(part_1_ru1),
    .Ru0(part_1_ru0), .Rc3(part_1_rc3), .Rc2(part_1_rc2), .Rc1(part_1_rc1), .Rc0(part_1_rc0),
    .R_plus_minus(part_1_r_plus_minus));
  and and_8 (and_8_out, part_1_r_plus_minus, R);
  S_R_Flip_Flop s_r_ff_3 (.Q(SR_y_minus), .preset(and_8_out), .reset(Ac));  // open: S, clk, R, Qn, en
  S_R_Flip_Flop s_r_ff_4 (.Q(tunnel_t_t_t_t_t), .preset(_3), .reset(Ac));  // open: S, clk, R, Qn, en
  S_R_Flip_Flop s_r_ff_5 (.Q(s_r_ff_5_q), .preset(tunnel_t_t_t_t), .reset(_3));  // open: S, clk, R, Qn, en
  S_R_Flip_Flop s_r_ff_6 (.Q(s_r_ff_6_q), .preset(tunnel_t_t), .reset(Ac));  // open: S, clk, R, Qn, en
  and and_9 (and_9_out, s_r_ff_5_q, s_r_ff_6_q, ~_15_9);  // AND_Gate
  contador_0_15 contador_0_15_2 (
    .Ck(ck), .On(and_9_out), .Off(_3), ._2_0(contador_0_15_2__2_0), ._2_1(contador_0_15_2__2_1));  // open: _2, estatus_contador, _2_2, _2_3
  and and_10 (_3, contador_0_15_2__2_0, contador_0_15_2__2_1);
  and and_11 (_1, contador_0_15_2__2_0, ~contador_0_15_2__2_1);  // AND_Gate
  and and_12 (_2, ~contador_0_15_2__2_0, contador_0_15_2__2_1);  // AND_Gate
  op_x op_x_2 (
    .condicion_1(and_9_out), .ac(Ac), ._1a4(_1b3), ._1a3(_1b2), ._1a2(_1b1), ._1a1(_1b0), ._1b3(_1a0),
    ._1c3(_1c3), ._1c2(_1c2), ._1c1(_1c1), ._1c0(_1c0), ._2a4(_2b3), ._2a3(_2b2), ._2a2(_2b1), ._2a1(_2b0),
    ._2b3(_2a0), ._2c3(_2c3), ._2c2(_2c2), ._2c1(_2c1), ._2c0(_2c0), ._1a4_2(op_x_2__1a4_2),
    ._1a3_2(op_x_2__1a3_2), ._1a2_2(op_x_2__1a2_2), ._1a1_2(op_x_2__1a1_2), ._1a0(op_x_2__1a0),
    ._2a4_2(op_x_2__2a4_2), ._2a3_2(op_x_2__2a3_2), ._2a2_2(op_x_2__2a2_2), ._2a1_2(op_x_2__2a1_2),
    ._2a0(op_x_2__2a0));
  division division_1 (
    .ac(Ac), .in_12(_2), .in_13(_1), .condicion(not_1_out), .ck(ck), .dd4(op_x_2__1a4_2),
    .dd3(op_x_2__1a3_2), .dd2(op_x_2__1a2_2), .dd1(op_x_2__1a1_2), .dd0(op_x_2__1a0), .d4(op_x_2__2a4_2),
    .d3(op_x_2__2a3_2), .d2(op_x_2__2a2_2), .d1(op_x_2__2a1_2), .d0(op_x_2__2a0), .s6(division_1_s6),
    .s5(division_1_s5), .s4(division_1_s4), .s3(division_1_s3), .s2(division_1_s2), .s1(division_1_s1),
    .Sfloat(float), .out_23(proceso), .ERR(R_overflow));
  not not_1 (not_1_out, _02_Divisor);
  codificador_binario_bcdn codificador_binario_bcdn_1 (
    .s5(division_1_s6), .s4(division_1_s5), .s3(division_1_s4), .s2(division_1_s3), .s1(division_1_s2),
    .s0(division_1_s1), .bcd6(R_a2), .bcd5(R_a1), .bcd4(R_a0), .bcd3(R_b3), .bcd2(R_b2), .bcd1(R_b1),
    .bcd0(R_b0));
  _0_divisor u_0_divisor_1 (
    .a4(op_x_2__2a4_2), .a3(op_x_2__2a3_2), .a2(op_x_2__2a2_2), .a1(op_x_2__2a1_2), .a0(op_x_2__2a0),
    ._0(_02_Divisor));

  // Other names for the same wires on the sheet: R_c0 = float; R_c2 = float; Rxc2 = Rxc0

  // Notes on the sheet:
  //   signo del 1er numero:
  //   signo del 2do numero:
  //   0: NO  
  //   1: SI  
endmodule

module circuit_2 (
  input  _1a3,
  input  _1b3,
  input  _1c3,
  input  signo_1,
  input  _1a2,
  input  _1b2,
  input  _1c2,
  input  signo_2,
  input  _1a1,
  input  _1b1,
  input  _1c1,
  input  o_minus,
  input  _1a0,
  input  _1b0,
  input  _1c0,
  input  _2b3,
  input  _2c3,
  input  _2a3,
  input  _2c2,
  input  _2a2,
  input  _2b2,
  input  _2c1,
  input  _2a1,
  input  _2b1,
  input  _2c0,
  input  _2a0,
  input  _2b0,
  output R_plus_minus,
  output Rc3,
  output Rc2,
  output Rc1,
  output Rc0,
  output Rd3,
  output Rd2,
  output Rd1,
  output Rd0,
  output Ru3,
  output Ru2,
  output Ru1,
  output Ru0
);

  A_6___A_5_O_y_1 a_6_a_5_o_y_1_1 (
    .signo_1(signo_1), .signo_2(signo_2), .o_minus(o_minus), ._1a3(_1a3), ._1a2(_1a2), ._1a1(_1a1),
    ._1a0(_1a0), ._2a3(_2a3), ._2a2(_2a2), ._2a1(_2a1), ._2a0(_2a0), ._1b3(_1b3), ._1b2(_1b2), ._1b1(_1b1),
    ._1b0(_1b0), ._2b3(_2b3), ._2b2(_2b2), ._2b1(_2b1), ._2b0(_2b0), ._1c3(_1c3), ._1c2(_1c2), ._1c1(_1c1),
    ._1c0(_1c0), ._2c3(_2c3), ._2c2(_2c2), ._2c1(_2c1), ._2c0(_2c0), .ar3(Rd3), .ar2(Rd2), .ar1(Rd1),
    .ar0(Rd0), .br3(Ru3), .br2(Ru2), .br1(Ru1), .br0(Ru0), .cr3(Rc3), .cr2(Rc2), .cr1(Rc1), .cr0(Rc0),
    .resultado(R_plus_minus));

  // Other names for the same wires on the sheet: sig_1 = signo_1; sig_2 = signo_2
endmodule

// X
module X_multiplicacion (
  input  _1a4,
  input  _2a4,
  input  _1a3,
  input  _2a3,
  input  _1a2,
  input  _2a2,
  input  _1a1,
  input  _2a1,
  input  _1a0,
  input  _2a0,
  output Error,
  output b7,
  output b6,
  output b5,
  output b4,
  output b3,
  output b2,
  output flotante
);

  wire and_1_out, and_2_out, and_3_out, and_4_out, and_5_out, and_6_out, and_7_out, and_8_out, and_9_out,
       and_10_out, and_11_out, and_12_out, and_13_out, and_14_out, and_15_out, and_16_out, and_17_out,
       and_18_out, and_19_out, and_20_out, and_21_out, and_22_out, and_23_out, and_24_out, and_25_out,
       x_multi_5bits_1_acarreo, x_multi_5bits_1_b1_2, x_multi_5bits_1_b2_2, x_multi_5bits_1_b3_2,
       x_multi_5bits_1_b4_2, x_multi_5bits_2_acarreo, x_multi_5bits_2_b4_2, x_multi_5bits_3_acarreo,
       x_multi_5bits_3_b1_2, x_multi_5bits_3_b2_2, x_multi_5bits_3_b3_2, x_multi_5bits_3_b4_2,
       x_multi_5bits_4_acarreo, x_multi_5bits_4_b1_2, x_multi_5bits_4_b2_2, x_multi_5bits_4_b3_2,
       x_multi_5bits_4_b4_2;

  and and_1 (and_1_out, _1a4, _2a3);
  and and_2 (and_2_out, _1a4, _2a4);
  and and_3 (and_3_out, _1a3, _2a1);
  and and_4 (and_4_out, _1a4, _2a1);
  and and_5 (and_5_out, _1a4, _2a2);
  and and_6 (and_6_out, _1a3, _2a2);
  and and_7 (and_7_out, _1a3, _2a3);
  and and_8 (and_8_out, _1a2, _2a3);
  and and_9 (and_9_out, _1a3, _2a4);
  and and_10 (and_10_out, _1a2, _2a4);
  and and_11 (and_11_out, _1a1, _2a1);
  and and_12 (and_12_out, _1a2, _2a1);
  and and_13 (and_13_out, _1a2, _2a2);
  and and_14 (and_14_out, _1a1, _2a2);
  and and_15 (and_15_out, _1a1, _2a3);
  and and_16 (and_16_out, _1a1, _2a4);
  and and_17 (and_17_out, _1a4, _2a0);
  and and_18 (and_18_out, _1a0, _2a1);
  and and_19 (and_19_out, _1a0, _2a2);
  and and_20 (and_20_out, _1a0, _2a3);
  X_multi_5bits x_multi_5bits_1 (
    .a4(and_1_out), .a3(and_7_out), .a2(and_8_out), .a1(and_15_out), .a0(and_20_out),
    .b4(x_multi_5bits_4_acarreo), .b3(x_multi_5bits_4_b4_2), .b2(x_multi_5bits_4_b3_2),
    .b1(x_multi_5bits_4_b2_2), .b0(x_multi_5bits_4_b1_2), .acarreo_0(1'b0),
    .acarreo(x_multi_5bits_1_acarreo), .b4_2(x_multi_5bits_1_b4_2), .b3_2(x_multi_5bits_1_b3_2),
    .b2_2(x_multi_5bits_1_b2_2), .b1_2(x_multi_5bits_1_b1_2), .b0_2(b3));
  and and_21 (and_21_out, _1a0, _2a4);
  X_multi_5bits x_multi_5bits_2 (
    .a4(and_2_out), .a3(and_9_out), .a2(and_10_out), .a1(and_16_out), .a0(and_21_out),
    .b4(x_multi_5bits_1_acarreo), .b3(x_multi_5bits_1_b4_2), .b2(x_multi_5bits_1_b3_2),
    .b1(x_multi_5bits_1_b2_2), .b0(x_multi_5bits_1_b1_2), .acarreo_0(1'b0),
    .acarreo(x_multi_5bits_2_acarreo), .b4_2(x_multi_5bits_2_b4_2), .b3_2(b7), .b2_2(b6), .b1_2(b5), .b0_2(b4));
  or or_1 (Error, x_multi_5bits_2_acarreo, x_multi_5bits_2_b4_2);
  and and_22 (and_22_out, _1a3, _2a0);
  and and_23 (and_23_out, _1a2, _2a0);
  X_multi_5bits x_multi_5bits_3 (
    .a4(and_4_out), .a3(and_3_out), .a2(and_12_out), .a1(and_11_out), .a0(and_18_out), .b4(1'b0),
    .b3(and_17_out), .b2(and_22_out), .b1(and_23_out), .b0(and_24_out), .acarreo_0(1'b0),
    .acarreo(x_multi_5bits_3_acarreo), .b4_2(x_multi_5bits_3_b4_2), .b3_2(x_multi_5bits_3_b3_2),
    .b2_2(x_multi_5bits_3_b2_2), .b1_2(x_multi_5bits_3_b1_2), .b0_2(flotante));
  X_multi_5bits x_multi_5bits_4 (
    .a4(and_5_out), .a3(and_6_out), .a2(and_13_out), .a1(and_14_out), .a0(and_19_out),
    .b4(x_multi_5bits_3_acarreo), .b3(x_multi_5bits_3_b4_2), .b2(x_multi_5bits_3_b3_2),
    .b1(x_multi_5bits_3_b2_2), .b0(x_multi_5bits_3_b1_2), .acarreo_0(1'b0),
    .acarreo(x_multi_5bits_4_acarreo), .b4_2(x_multi_5bits_4_b4_2), .b3_2(x_multi_5bits_4_b3_2),
    .b2_2(x_multi_5bits_4_b2_2), .b1_2(x_multi_5bits_4_b1_2), .b0_2(b2));
  and and_24 (and_24_out, _1a1, _2a0);
  and and_25 (and_25_out, _1a0, _2a0);
  // Probe on and_25_out

  // Notes on the sheet:
  //   2A0
  //   2A1
endmodule

module signos_numeros (
  input  in_1,
  input  Ac,
  output signo
);

  S_R_Flip_Flop s_r_ff_1 (.Q(signo), .preset(in_1), .reset(Ac));  // open: S, clk, R, Qn, en
endmodule

// =R+-
module mantener_R (
  input  in_1,
  input  in_2,
  input  in_3,
  input  AC,
  output out_5,
  output out_6
);

  wire and_1_out, s_r_ff_1_q, xor_1_out;

  xor xor_1 (xor_1_out, in_1, in_2);
  S_R_Flip_Flop s_r_ff_1 (.Q(s_r_ff_1_q), .preset(xor_1_out), .reset(AC));  // open: S, clk, R, Qn, en
  S_R_Flip_Flop s_r_ff_2 (.Q(out_5), .preset(in_2), .reset(AC));  // open: S, clk, R, Qn, en
  S_R_Flip_Flop s_r_ff_3 (.Q(out_6), .preset(and_1_out), .reset(AC));  // open: S, clk, R, Qn, en
  and and_1 (and_1_out, s_r_ff_1_q, in_3);
endmodule

module R_unico (
  input  Rx3,
  input  Rx2,
  input  Rx1,
  input  Rx0,
  input  x,
  input  R___3,
  input  R___2,
  input  R___1,
  input  R___0,
  input  r,
  input  R_3,
  input  R_2,
  input  R_1,
  input  R_0,
  input  in_15,
  input  Ac,
  output Ra3,
  output Ra2,
  output Ra1,
  output Ra0
);

  wire and_1_out, and_2_out, and_3_out, exc1, exc2, exc3, habilitacion_1_s0, habilitacion_1_s1,
       habilitacion_1_s2, habilitacion_1_s3, habilitacion_2_s0, habilitacion_2_s1, habilitacion_2_s2,
       habilitacion_2_s3, habilitacion_3_s0, habilitacion_3_s1, habilitacion_3_s2, habilitacion_3_s3;

  and and_1 (and_1_out, x, ~exc2, ~exc1);  // AND_Gate
  and and_2 (and_2_out, in_15, ~exc3, ~exc1);  // AND_Gate
  habilitacion habilitacion_1 (
    .b0(Rx0), .b1(Rx1), .b2(Rx2), .b3(Rx3), .in_5(exc3), .s0(habilitacion_1_s0), .s1(habilitacion_1_s1),
    .s2(habilitacion_1_s2), .s3(habilitacion_1_s3));
  S_R_Flip_Flop s_r_ff_1 (.Q(exc3), .preset(and_1_out), .reset(Ac));  // open: S, clk, R, Qn, en
  S_R_Flip_Flop s_r_ff_2 (.Q(exc1), .preset(and_3_out), .reset(Ac));  // open: S, clk, R, Qn, en
  and and_3 (and_3_out, r, ~exc3, ~exc2);  // AND_Gate
  habilitacion habilitacion_2 (
    .b0(R_0), .b1(R_1), .b2(R_2), .b3(R_3), .in_5(exc2), .s0(habilitacion_2_s0), .s1(habilitacion_2_s1),
    .s2(habilitacion_2_s2), .s3(habilitacion_2_s3));
  S_R_Flip_Flop s_r_ff_3 (.Q(exc2), .preset(and_2_out), .reset(Ac));  // open: S, clk, R, Qn, en
  habilitacion habilitacion_3 (
    .b0(R___0), .b1(R___1), .b2(R___2), .b3(R___3), .in_5(exc1), .s0(habilitacion_3_s0),
    .s1(habilitacion_3_s1), .s2(habilitacion_3_s2), .s3(habilitacion_3_s3));
  ExactlyOne xor_1 (.out(Ra3), .in0(habilitacion_1_s3), .in1(habilitacion_3_s3), .in2(habilitacion_2_s3));
  ExactlyOne xor_2 (.out(Ra2), .in0(habilitacion_1_s2), .in1(habilitacion_3_s2), .in2(habilitacion_2_s2));
  ExactlyOne xor_3 (.out(Ra1), .in0(habilitacion_1_s1), .in1(habilitacion_3_s1), .in2(habilitacion_2_s1));
  ExactlyOne xor_4 (.out(Ra0), .in0(habilitacion_1_s0), .in1(habilitacion_3_s0), .in2(habilitacion_2_s0));
endmodule

// codif
module codificador_bcdn (
  input  n9,
  input  n8,
  input  n7,
  input  n6,
  input  n5,
  input  n4,
  input  Rst,
  input  cont_on_off,
  input  n3,
  input  n2,
  input  n1,
  input  n0,
  output b3,
  output b2,
  output b1,
  output b0
);

  wire and_1_out, and_2_out, and_3_out, and_4_out, or_1_out, or_2_out, or_3_out, or_4_out;

  or or_1 (or_1_out, n8, n9);
  or or_2 (or_2_out, n4, n5, n6, n7);
  or or_3 (or_3_out, n2, n3, n6, n7);
  or or_4 (or_4_out, n1, n3, n5, n7, n9);
  and and_1 (and_1_out, or_1_out, ~cont_on_off);  // AND_Gate
  and and_2 (and_2_out, or_2_out, ~cont_on_off);  // AND_Gate
  and and_3 (and_3_out, or_3_out, ~cont_on_off);  // AND_Gate
  and and_4 (and_4_out, or_4_out, ~cont_on_off);  // AND_Gate
  S_R_Flip_Flop s_r_ff_1 (.Q(b3), .preset(and_1_out), .reset(Rst));  // open: S, clk, R, Qn, en
  S_R_Flip_Flop s_r_ff_2 (.Q(b2), .preset(and_2_out), .reset(Rst));  // open: S, clk, R, Qn, en
  S_R_Flip_Flop s_r_ff_3 (.Q(b1), .preset(and_3_out), .reset(Rst));  // open: S, clk, R, Qn, en
  S_R_Flip_Flop s_r_ff_4 (.Q(b0), .preset(and_4_out), .reset(Rst));  // open: S, clk, R, Qn, en
endmodule

module decodificador_bcdn (
  input  a3,
  input  a2,
  input  a1,
  input  a0,
  output s9,
  output s8,
  output s7,
  output s6,
  output s5,
  output s4,
  output s3,
  output s2,
  output s1,
  output s0
);

  wire not_1_out, not_2_out, not_3_out, not_4_out, not_5_out, not_6_out, not_7_out, not_8_out, not_9_out,
       not_10_out, not_11_out, not_12_out, not_13_out, not_14_out, not_15_out;

  and and_1 (s9, a3, a0);
  and and_2 (s8, a3, not_1_out);
  not not_1 (not_1_out, a0);
  and and_3 (s7, a2, a1, a0);
  and and_4 (s6, a2, a1, not_2_out);
  not not_2 (not_2_out, a0);
  not not_3 (not_3_out, a1);
  and and_5 (s5, a2, not_3_out, a0);
  not not_4 (not_4_out, a1);
  and and_6 (s4, a2, not_4_out, not_5_out);
  not not_5 (not_5_out, a0);
  not not_6 (not_6_out, a2);
  and and_7 (s3, not_6_out, a1, a0);
  not not_7 (not_7_out, a2);
  and and_8 (s2, not_7_out, a1, not_8_out);
  not not_8 (not_8_out, a0);
  not not_9 (not_9_out, a3);
  not not_10 (not_10_out, a2);
  not not_11 (not_11_out, a1);
  not not_12 (not_12_out, a3);
  not not_13 (not_13_out, a2);
  not not_14 (not_14_out, a1);
  not not_15 (not_15_out, a0);
  and and_9 (s1, not_9_out, not_10_out, not_11_out, a0);
  and and_10 (s0, not_12_out, not_13_out, not_14_out, not_15_out);
endmodule

// cod bn-BCD
module codificador_binario_bcdn (
  input  s5,
  input  s4,
  input  s3,
  input  s2,
  input  s1,
  input  s0,
  output bcd6,
  output bcd5,
  output bcd4,
  output bcd3,
  output bcd2,
  output bcd1,
  output bcd0
);

  wire and_1_out, and_2_out, and_3_out, and_4_out, and_5_out, and_6_out, and_7_out, and_8_out, and_9_out,
       and_10_out, and_11_out, and_12_out, and_13_out, and_14_out, and_15_out, and_16_out, and_17_out,
       and_18_out, and_19_out, and_20_out, and_21_out, and_22_out, and_23_out, and_24_out, and_25_out,
       and_26_out, and_27_out, and_28_out, and_29_out, and_30_out, and_31_out, and_32_out, and_33_out,
       and_34_out, and_35_out, and_36_out, and_37_out, and_38_out, not_1_out, not_2_out, not_3_out,
       not_4_out, not_5_out, not_6_out, not_7_out, not_8_out, not_9_out, not_10_out, not_11_out, not_12_out,
       not_13_out, not_14_out, not_15_out, not_16_out, not_17_out, not_18_out, not_19_out, not_20_out,
       not_21_out, not_22_out, not_23_out, not_24_out, not_25_out, not_26_out, not_27_out, not_28_out,
       not_29_out, not_30_out, not_31_out, not_32_out, not_33_out, not_34_out, not_35_out, not_36_out,
       not_37_out, not_38_out, not_39_out, not_40_out, not_41_out, not_42_out, not_43_out, not_44_out,
       not_45_out, not_46_out, not_47_out, not_48_out, not_49_out, not_50_out, not_51_out, not_52_out,
       not_53_out, not_54_out, not_55_out, not_56_out, not_57_out, not_58_out, not_59_out, not_60_out,
       not_61_out, not_62_out, not_63_out, not_64_out, not_65_out, not_66_out, not_67_out, not_68_out,
       not_69_out, not_70_out, not_71_out;

  and and_1 (and_1_out, s5, s3);
  and and_2 (and_2_out, s5, s4);
  not not_1 (not_1_out, s5);
  not not_2 (not_2_out, s5);
  not not_3 (not_3_out, s4);
  not not_4 (not_4_out, s3);
  not not_5 (not_5_out, s5);
  not not_6 (not_6_out, s4);
  not not_7 (not_7_out, s5);
  not not_8 (not_8_out, s4);
  not not_9 (not_9_out, s5);
  not not_10 (not_10_out, s5);
  not not_11 (not_11_out, s3);
  not not_12 (not_12_out, s2);
  not not_13 (not_13_out, s4);
  not not_14 (not_14_out, s3);
  not not_15 (not_15_out, s3);
  not not_16 (not_16_out, s3);
  not not_17 (not_17_out, s2);
  not not_18 (not_18_out, s5);
  not not_19 (not_19_out, s4);
  not not_20 (not_20_out, s2);
  not not_21 (not_21_out, s1);
  not not_22 (not_22_out, s5);
  not not_23 (not_23_out, s3);
  not not_24 (not_24_out, s2);
  not not_25 (not_25_out, s5);
  not not_26 (not_26_out, s1);
  not not_27 (not_27_out, s4);
  not not_28 (not_28_out, s3);
  not not_29 (not_29_out, s3);
  not not_30 (not_30_out, s2);
  not not_31 (not_31_out, s1);
  not not_32 (not_32_out, s2);
  not not_33 (not_33_out, s4);
  not not_34 (not_34_out, s3);
  not not_35 (not_35_out, s1);
  not not_36 (not_36_out, s5);
  not not_37 (not_37_out, s4);
  not not_38 (not_38_out, s5);
  not not_39 (not_39_out, s2);
  not not_40 (not_40_out, s1);
  not not_41 (not_41_out, s5);
  not not_42 (not_42_out, s2);
  not not_43 (not_43_out, s2);
  not not_44 (not_44_out, s1);
  not not_45 (not_45_out, s4);
  not not_46 (not_46_out, s3);
  not not_47 (not_47_out, s2);
  not not_48 (not_48_out, s4);
  not not_49 (not_49_out, s3);
  not not_50 (not_50_out, s5);
  not not_51 (not_51_out, s4);
  not not_52 (not_52_out, s3);
  not not_53 (not_53_out, s5);
  not not_54 (not_54_out, s3);
  not not_55 (not_55_out, s5);
  not not_56 (not_56_out, s4);
  not not_57 (not_57_out, s1);
  not not_58 (not_58_out, s5);
  not not_59 (not_59_out, s3);
  not not_60 (not_60_out, s2);
  not not_61 (not_61_out, s1);
  not not_62 (not_62_out, s5);
  not not_63 (not_63_out, s2);
  not not_64 (not_64_out, s4);
  not not_65 (not_65_out, s3);
  not not_66 (not_66_out, s1);
  not not_67 (not_67_out, s3);
  not not_68 (not_68_out, s1);
  not not_69 (not_69_out, s4);
  not not_70 (not_70_out, s2);
  not not_71 (not_71_out, s1);
  or or_1 (bcd6, and_1_out, and_2_out);
  and and_3 (and_3_out, not_1_out, s4, s2);
  and and_4 (and_4_out, not_2_out, s4, s3);
  and and_5 (and_5_out, s4, s3, s2);
  and and_6 (and_6_out, s5, not_3_out, not_4_out);
  and and_7 (and_7_out, not_5_out, not_6_out, s3, s1);
  and and_8 (and_8_out, not_7_out, not_8_out, s3, s2);
  and and_9 (and_9_out, not_9_out, s3, s2, s1);
  and and_10 (and_10_out, not_10_out, s4, not_11_out, not_12_out);
  and and_11 (and_11_out, s5, not_13_out, not_14_out);
  and and_12 (and_12_out, s5, not_15_out, s1);
  and and_13 (and_13_out, s5, not_16_out, s2);
  and and_14 (and_14_out, s5, s4, s3, not_17_out);
  and and_15 (and_15_out, not_18_out, not_19_out, s3, not_20_out, not_21_out);
  and and_16 (and_16_out, not_22_out, s4, not_23_out, not_24_out, s1);
  and and_17 (and_17_out, not_25_out, s4, s3, s2, not_26_out);
  and and_18 (and_18_out, s5, not_27_out, not_28_out, s2, s1);
  and and_19 (and_19_out, s5, s4, not_29_out, not_30_out, not_31_out);
  and and_20 (and_20_out, s5, s4, s3, not_32_out, s1);
  and and_21 (and_21_out, not_33_out, not_34_out, s2, not_35_out);
  and and_22 (and_22_out, not_36_out, not_37_out, s2, s1);
  and and_23 (and_23_out, not_38_out, s4, not_39_out, not_40_out);
  and and_24 (and_24_out, not_41_out, s4, s3, not_42_out);
  and and_25 (and_25_out, s4, s3, not_43_out, not_44_out);
  and and_26 (and_26_out, s5, not_45_out, not_46_out, not_47_out, s1);
  and and_27 (and_27_out, s5, not_48_out, s3, s2);
  and and_28 (and_28_out, s5, s4, not_49_out, s2, s1);
  and and_29 (and_29_out, not_50_out, not_51_out, not_52_out, s1);
  and and_30 (and_30_out, not_53_out, not_54_out, s2, s1);
  and and_31 (and_31_out, not_55_out, not_56_out, s3, s2, not_57_out);
  and and_32 (and_32_out, not_58_out, s4, not_59_out, not_60_out, not_61_out);
  and and_33 (and_33_out, not_62_out, s4, s3, not_63_out, s1);
  and and_34 (and_34_out, s5, not_64_out, not_65_out, not_66_out);
  and and_35 (and_35_out, s5, not_67_out, s2, not_68_out);
  and and_36 (and_36_out, s5, not_69_out, s3, s1);
  and and_37 (and_37_out, s5, s3, s2, s1);
  and and_38 (and_38_out, s5, s4, s3, not_70_out, not_71_out);
  or or_2 (bcd5, and_3_out, and_4_out, and_5_out, and_6_out);
  or or_3 (bcd4, and_7_out, and_8_out, and_9_out, and_10_out, and_11_out, and_12_out, and_13_out, and_14_out);
  or or_4 (bcd3, and_15_out, and_16_out, and_17_out, and_18_out, and_19_out, and_20_out);
  or or_5 (bcd2, and_21_out, and_22_out, and_23_out, and_24_out, and_25_out, and_26_out, and_27_out, and_28_out);
  or or_6 (bcd1, and_29_out, and_30_out, and_31_out, and_32_out, and_33_out, and_34_out, and_35_out, and_36_out, and_37_out, and_38_out);

  assign bcd0 = s0;
endmodule

// Codf
module codificador_bcd_a_binario (
  input  a4,
  input  a3,
  input  a2,
  input  a1,
  input  a0,
  output s3,
  output s2,
  output s1,
  output s0
);

  wire and_1_out, and_2_out, and_3_out, and_4_out, and_5_out, and_6_out, and_7_out, and_8_out, and_9_out,
       and_10_out, and_11_out, and_12_out, not_1_out, not_2_out, not_3_out, not_4_out, not_5_out, not_6_out,
       not_7_out, not_8_out, not_9_out, not_10_out, not_11_out, not_12_out, not_13_out, not_14_out,
       not_15_out, not_16_out, not_17_out, not_18_out, not_19_out, not_20_out, not_21_out, not_22_out,
       not_23_out, not_24_out, not_25_out, not_26_out;

  not not_1 (not_1_out, a4);
  not not_2 (not_2_out, a2);
  not not_3 (not_3_out, a1);
  not not_4 (not_4_out, a3);
  not not_5 (not_5_out, a2);
  not not_6 (not_6_out, a3);
  not not_7 (not_7_out, a1);
  not not_8 (not_8_out, a4);
  not not_9 (not_9_out, a3);
  not not_10 (not_10_out, a3);
  not not_11 (not_11_out, a1);
  not not_12 (not_12_out, a3);
  not not_13 (not_13_out, a2);
  not not_14 (not_14_out, a4);
  not not_15 (not_15_out, a3);
  not not_16 (not_16_out, a3);
  not not_17 (not_17_out, a1);
  not not_18 (not_18_out, a4);
  not not_19 (not_19_out, a3);
  not not_20 (not_20_out, a4);
  not not_21 (not_21_out, a2);
  not not_22 (not_22_out, a1);
  not not_23 (not_23_out, a3);
  not not_24 (not_24_out, a2);
  not not_25 (not_25_out, a3);
  not not_26 (not_26_out, a1);
  and and_1 (and_1_out, not_1_out, a3, not_2_out, not_3_out);
  and and_2 (and_2_out, a4, not_4_out, not_5_out);
  and and_3 (and_3_out, a4, not_6_out, not_7_out);
  and and_4 (and_4_out, not_8_out, not_9_out, a2);
  and and_5 (and_5_out, not_10_out, a2, not_11_out);
  and and_6 (and_6_out, a4, not_12_out, not_13_out, a1);
  and and_7 (and_7_out, not_14_out, not_15_out, a1);
  and and_8 (and_8_out, a4, not_16_out, not_17_out);
  and and_9 (and_9_out, not_18_out, not_19_out, a0);
  and and_10 (and_10_out, not_20_out, not_21_out, not_22_out, a0);
  and and_11 (and_11_out, not_23_out, not_24_out, a0);
  and and_12 (and_12_out, not_25_out, not_26_out, a0);
  or or_1 (s3, and_1_out, and_2_out, and_3_out);
  or or_2 (s2, and_4_out, and_5_out, and_6_out);
  or or_3 (s1, and_7_out, and_8_out);
  or or_4 (s0, and_9_out, and_10_out, and_11_out, and_12_out);
endmodule

// flotante
module codificador_flotante (
  input  b0,
  input  b1,
  input  b2,
  input  b3,
  output flotante
);

  wire and_1_out, and_2_out;

  and and_1 (and_1_out, b1, b2);
  and and_2 (and_2_out, b0, b2);
  or or_1 (flotante, b3, and_1_out, and_2_out);
endmodule

// Sumador bcdn
module A_Sumador_BCDN (
  input  _1a3,
  input  _1a2,
  input  _1a1,
  input  _1a0,
  input  _1b3,
  input  _1b2,
  input  _1b0,
  input  _1c3,
  input  _1c2,
  input  _1c1,
  input  _1c0,
  input  _1b1,
  input  _2a3,
  input  _2a2,
  input  _2a1,
  input  _2a0,
  input  _2b3,
  input  _2b2,
  input  _2b1,
  input  _2b0,
  input  _2c3,
  input  _2c2,
  input  _2c1,
  input  _2c0,
  output br3,
  output br2,
  output br1,
  output br0,
  output cr3,
  output cr2,
  output cr1,
  output cr0,
  output ar3,
  output ar2,
  output ar1,
  output ar0
);

  wire b_suma_bcd_1_acarreo, b_suma_bcd_1_r0, b_suma_bcd_1_r1, b_suma_bcd_1_r2, b_suma_bcd_1_r3,
       b_suma_bcd_3_acarreo, b_suma_bcd_3_r0, b_suma_bcd_3_r1, b_suma_bcd_3_r2, b_suma_bcd_3_r3,
       b_suma_bcd_4_acarreo, b_suma_bcd_5_acarreo, b_suma_bcd_5_r0, b_suma_bcd_5_r1, b_suma_bcd_5_r2,
       b_suma_bcd_5_r3, b_suma_bcd_6_acarreo;

  B_suma_bcd b_suma_bcd_1 (
    .a3(_1a3), .b3(_2a3), .a2(_1a2), .b2(_2a2), .a1(_1a1), .b1(_2a1), .a0(_1a0), .b0(_2a0),
    .acarreo_0(b_suma_bcd_3_acarreo), .R3(b_suma_bcd_1_r3), .R2(b_suma_bcd_1_r2), .R1(b_suma_bcd_1_r1),
    .R0(b_suma_bcd_1_r0), .acarreo(b_suma_bcd_1_acarreo));
  B_suma_bcd b_suma_bcd_2 (
    .a3(b_suma_bcd_1_r3), .b3(1'b0), .a2(b_suma_bcd_1_r2), .b2(1'b0), .a1(b_suma_bcd_1_r1), .b1(1'b0),
    .a0(b_suma_bcd_1_r0), .b0(1'b0), .acarreo_0(b_suma_bcd_4_acarreo), .R3(ar3), .R2(ar2), .R1(ar1), .R0(ar0));  // open: acarreo
  B_suma_bcd b_suma_bcd_3 (
    .a3(_1b3), .b3(_2b3), .a2(_1b2), .b2(_2b2), .a1(_1b1), .b1(_2b1), .a0(_1b0), .b0(_2b0),
    .acarreo_0(b_suma_bcd_5_acarreo), .R3(b_suma_bcd_3_r3), .R2(b_suma_bcd_3_r2), .R1(b_suma_bcd_3_r1),
    .R0(b_suma_bcd_3_r0), .acarreo(b_suma_bcd_3_acarreo));
  B_suma_bcd b_suma_bcd_4 (
    .a3(b_suma_bcd_3_r3), .b3(1'b0), .a2(b_suma_bcd_3_r2), .b2(1'b0), .a1(b_suma_bcd_3_r1), .b1(1'b0),
    .a0(b_suma_bcd_3_r0), .b0(1'b0), .acarreo_0(b_suma_bcd_6_acarreo), .R3(br3), .R2(br2), .R1(br1),
    .R0(br0), .acarreo(b_suma_bcd_4_acarreo));
  B_suma_bcd b_suma_bcd_5 (
    .a3(_1c3), .b3(_2c3), .a2(_1c2), .b2(_2c2), .a1(_1c1), .b1(_2c1), .a0(_1c0), .b0(_2c0), .acarreo_0(1'b0),
    .R3(b_suma_bcd_5_r3), .R2(b_suma_bcd_5_r2), .R1(b_suma_bcd_5_r1), .R0(b_suma_bcd_5_r0),
    .acarreo(b_suma_bcd_5_acarreo));
  B_suma_bcd b_suma_bcd_6 (
    .a3(b_suma_bcd_5_r3), .b3(1'b0), .a2(b_suma_bcd_5_r2), .b2(1'b0), .a1(b_suma_bcd_5_r1), .b1(1'b0),
    .a0(b_suma_bcd_5_r0), .b0(1'b0), .acarreo_0(b_suma_bcd_1_acarreo), .R3(cr3), .R2(cr2), .R1(cr1),
    .R0(cr0), .acarreo(b_suma_bcd_6_acarreo));
endmodule

// A.1 igual
module A_1_A_B (
  input  comparar,
  input  a3,
  input  b3,
  input  a2,
  input  b2,
  input  a1,
  input  b1,
  input  a0,
  input  b0,
  output igual
);

  wire xnor_1_out, xnor_2_out, xnor_3_out, xnor_4_out;

  xnor xnor_1 (xnor_1_out, a3, b3);
  xnor xnor_2 (xnor_2_out, a2, b2);
  xnor xnor_3 (xnor_3_out, a1, b1);
  xnor xnor_4 (xnor_4_out, a0, b0);
  and and_1 (igual, comparar, xnor_1_out, xnor_2_out, xnor_3_out, xnor_4_out);
endmodule

// A.2 mayor
module A_2_A_B (
  input  igual0,
  input  a1,
  input  a0,
  input  b1,
  input  b0,
  output mayor,
  output menor
);

  wire and_1_out, and_2_out, and_3_out, and_4_out, and_5_out, and_6_out, not_1_out, not_2_out, not_3_out,
       not_4_out, not_5_out, not_6_out, not_7_out, not_8_out;

  not not_1 (not_1_out, b1);
  not not_2 (not_2_out, b0);
  not not_3 (not_3_out, b1);
  not not_4 (not_4_out, b0);
  not not_5 (not_5_out, a1);
  not not_6 (not_6_out, a0);
  not not_7 (not_7_out, a1);
  not not_8 (not_8_out, a0);
  and and_1 (and_1_out, igual0, a0, not_1_out, not_2_out);
  and and_2 (and_2_out, igual0, a1, not_3_out);
  and and_3 (and_3_out, igual0, a1, a0, not_4_out);
  and and_4 (and_4_out, igual0, not_5_out, not_6_out, b0);
  and and_5 (and_5_out, igual0, not_7_out, b1);
  and and_6 (and_6_out, igual0, not_8_out, b1, b0);
  or or_1 (mayor, and_1_out, and_2_out, and_3_out);
  or or_2 (menor, and_4_out, and_5_out, and_6_out);
endmodule

module A_3___A__B__4bits (
  input  comparar,
  input  a3,
  input  b3,
  input  a2,
  input  b2,
  input  a1,
  input  b1,
  input  a0,
  input  b0,
  output M_mayor,
  output I_igual
);

  wire a_2_a_b_1_mayor, a_2_a_b_1_menor, a_2_a_b_2_mayor, and_1_out, and_2_out, not_1_out, not_2_out;

  A_1_A_B a_1_a_b_1 (
    .comparar(comparar), .a3(a3), .b3(b3), .a2(a2), .b2(b2), .a1(a1), .b1(b1), .a0(a0), .b0(b0),
    .igual(I_igual));
  A_2_A_B a_2_a_b_1 (
    .igual0(and_1_out), .a1(a3), .a0(a2), .b1(b3), .b0(b2), .mayor(a_2_a_b_1_mayor), .menor(a_2_a_b_1_menor));
  not not_1 (not_1_out, a_2_a_b_1_menor);
  not not_2 (not_2_out, a_2_a_b_1_mayor);
  and and_1 (and_1_out, ~I_igual, comparar);  // AND_Gate
  and and_2 (and_2_out, and_1_out, not_2_out, not_1_out);
  or or_1 (M_mayor, a_2_a_b_1_mayor, a_2_a_b_2_mayor);
  A_2_A_B a_2_a_b_2 (.igual0(and_2_out), .a1(a1), .a0(a0), .b1(b1), .b0(b0), .mayor(a_2_a_b_2_mayor));  // open: menor

  // Other names for the same wires on the sheet: com = comparar

  // Notes on the sheet:
  //   si comparar es 0 no me interesa saber si es mayor o igual ya que no es indispensable para el resultado de la suma o resta 
  //   si es mayor debo tener en cuenta para el resultado no siempre 
endmodule

// R+ o R-
module A_4_Resultado___o (
  input  signo1,
  input  signo2,
  input  mayor,
  input  igual,
  output signoResultado,
  output Complemento
);

  wire and_1_out, and_2_out, and_3_out, and_4_out, and_5_out, and_6_out, not_1_out, not_2_out, not_3_out,
       not_4_out;

  not not_1 (not_1_out, mayor);
  and and_1 (and_1_out, signo2, not_1_out, not_2_out);
  not not_2 (not_2_out, igual);
  and and_2 (and_2_out, signo1, mayor, not_3_out);
  not not_3 (not_3_out, igual);
  and and_3 (and_3_out, signo1, signo2);
  and and_4 (and_4_out, signo2, not_4_out);
  not not_4 (not_4_out, mayor);
  and and_5 (and_5_out, signo1, igual);
  and and_6 (and_6_out, signo1, mayor);
  or or_1 (signoResultado, and_1_out, and_2_out, and_3_out);
  or or_2 (Complemento, and_4_out, and_5_out, and_6_out);
endmodule

// A.5 R+o- y Acarr
module A_5__A_3_4_bits_3_veces_y_da_Resultado_o_Acarreo (
  input  _1a3,
  input  _1b3,
  input  _1c3,
  input  signo_1,
  input  _1a2,
  input  _1b2,
  input  _1c2,
  input  signo_2,
  input  _1a1,
  input  _1b1,
  input  _1c1,
  input  o_minus,
  input  _1a0,
  input  _1b0,
  input  _1c0,
  input  _2b3,
  input  _2c3,
  input  _2a3,
  input  _2c2,
  input  _2a2,
  input  _2b2,
  input  _2c1,
  input  _2a1,
  input  _2b1,
  input  _2c0,
  input  _2a0,
  input  _2b0,
  output R,
  output complemento
);

  wire a_3_a_b_4bits_1_i_igual, a_3_a_b_4bits_1_m_mayor, a_3_a_b_4bits_2_i_igual, a_3_a_b_4bits_2_m_mayor,
       a_3_a_b_4bits_3_i_igual, a_3_a_b_4bits_3_m_mayor, and_1_out, or_1_out, xor_1_out, xor_2_out, xor_3_out;

  or or_1 (or_1_out, a_3_a_b_4bits_1_m_mayor, a_3_a_b_4bits_2_m_mayor, a_3_a_b_4bits_3_m_mayor);
  xor xor_1 (xor_1_out, signo_2, o_minus);
  xor xor_2 (xor_2_out, signo_2, o_minus);
  xor xor_3 (xor_3_out, signo_1, xor_2_out);
  A_3___A__B__4bits a_3_a_b_4bits_1 (
    .comparar(a_3_a_b_4bits_2_i_igual), .a3(_1c3), .b3(_2c3), .a2(_1c2), .b2(_2c2), .a1(_1c1), .b1(_2c1),
    .a0(_1c0), .b0(_2c0), .M_mayor(a_3_a_b_4bits_1_m_mayor), .I_igual(a_3_a_b_4bits_1_i_igual));
  A_3___A__B__4bits a_3_a_b_4bits_2 (
    .comparar(a_3_a_b_4bits_3_i_igual), .a3(_1b3), .b3(_2b3), .a2(_1b2), .b2(_2b2), .a1(_1b1), .b1(_2b1),
    .a0(_1b0), .b0(_2b0), .M_mayor(a_3_a_b_4bits_2_m_mayor), .I_igual(a_3_a_b_4bits_2_i_igual));
  A_3___A__B__4bits a_3_a_b_4bits_3 (
    .comparar(xor_3_out), .a3(_1a3), .b3(_2a3), .a2(_1a2), .b2(_2a2), .a1(_1a1), .b1(_2a1), .a0(_1a0),
    .b0(_2a0), .M_mayor(a_3_a_b_4bits_3_m_mayor), .I_igual(a_3_a_b_4bits_3_i_igual));
  A_4_Resultado___o a_4_resultado_o_1 (
    .signo1(signo_1), .signo2(xor_1_out), .mayor(or_1_out), .igual(and_1_out), .signoResultado(R),
    .Complemento(complemento));
  and and_1 (and_1_out, a_3_a_b_4bits_3_i_igual, a_3_a_b_4bits_2_i_igual, a_3_a_b_4bits_1_i_igual);

  // Other names for the same wires on the sheet: sig_1 = signo_1; sig_2 = signo_2
endmodule

// A.5.1
module A_5_1__complemento (
  input  signo_numero_1,
  input  _1a3,
  input  _1a2,
  input  _1a1,
  input  _1a0,
  input  _1b3,
  input  _1b2,
  input  _1b1,
  input  _1b0,
  input  _1c3,
  input  _1c2,
  input  _1c1,
  input  _1c0,
  input  complementar,
  input  _2a3,
  input  _2a2,
  input  _2a1,
  input  _2a0,
  input  _2b3,
  input  _2b2,
  input  _2b1,
  input  _2b0,
  input  _2c3,
  input  _2c2,
  input  _2c1,
  input  _2c0,
  output xa3,
  output xa2,
  output xa1,
  output xa0,
  output xb3,
  output xb2,
  output xb1,
  output xb0,
  output xc3,
  output xc2,
  output xc1,
  output xc0,
  output ya3,
  output ya2,
  output ya1,
  output ya0,
  output yb3,
  output yb2,
  output yb1,
  output yb0,
  output yc3,
  output yc2,
  output yc1,
  output yc0
);

  complemento_a_9 complemento_a_9_1 (
    .control(signo_numero_1), .a3(_1a3), .a2(_1a2), .a1(_1a1), .a0(_1a0), .b3(xa3), .b2(xa2), .b1(xa1),
    .b0(xa0));
  complemento_a_9 complemento_a_9_2 (
    .control(signo_numero_1), .a3(_1b3), .a2(_1b2), .a1(_1b1), .a0(_1b0), .b3(xb3), .b2(xb2), .b1(xb1),
    .b0(xb0));
  complemento_a_9 complemento_a_9_3 (
    .control(complementar), .a3(_2a3), .a2(_2a2), .a1(_2a1), .a0(_2a0), .b3(ya3), .b2(ya2), .b1(ya1), .b0(ya0));
  complemento_a_9 complemento_a_9_4 (
    .control(complementar), .a3(_2b3), .a2(_2b2), .a1(_2b1), .a0(_2b0), .b3(yb3), .b2(yb2), .b1(yb1), .b0(yb0));
  complemento_a_9 complemento_a_9_5 (
    .control(complementar), .a3(_2c3), .a2(_2c2), .a1(_2c1), .a0(_2c0), .b3(yc3), .b2(yc2), .b1(yc1), .b0(yc0));
  complemento_a_9 complemento_a_9_6 (
    .control(signo_numero_1), .a3(_1c3), .a2(_1c2), .a1(_1c1), .a0(_1c0), .b3(xc3), .b2(xc2), .b1(xc1),
    .b0(xc0));
endmodule

// A.6
module A_6___A_5_O_y_1 (
  input  _1a3,
  input  _1b3,
  input  _1c3,
  input  signo_1,
  input  _1a2,
  input  _1b2,
  input  _1c2,
  input  signo_2,
  input  _1a1,
  input  _1b1,
  input  _1c1,
  input  o_minus,
  input  _1a0,
  input  _1b0,
  input  _1c0,
  input  _2b3,
  input  _2c3,
  input  _2a3,
  input  _2c2,
  input  _2a2,
  input  _2b2,
  input  _2c1,
  input  _2a1,
  input  _2b1,
  input  _2c0,
  input  _2a0,
  input  _2b0,
  output resultado,
  output ar3,
  output ar2,
  output ar1,
  output ar0,
  output br3,
  output br2,
  output br1,
  output br0,
  output cr3,
  output cr2,
  output cr1,
  output cr0
);

  wire _1cero, _2cero, a_sumador_bcdn_1_ar0, a_sumador_bcdn_1_ar1, a_sumador_bcdn_1_ar2,
       a_sumador_bcdn_1_ar3, a_sumador_bcdn_1_br0, a_sumador_bcdn_1_br1, a_sumador_bcdn_1_br2,
       a_sumador_bcdn_1_br3, a_sumador_bcdn_1_cr0, a_sumador_bcdn_1_cr1, a_sumador_bcdn_1_cr2,
       a_sumador_bcdn_1_cr3, and_1_out, and_2_out, and_3_out, cero, complemento, xa0, xa1, xa2, xa3, xb0,
       xb1, xb2, xb3, xc0, xc1, xc2, xc3, xor_1_out, ya0, ya1, ya2, ya3, yb0, yb1, yb2, yb3, yc0, yc1, yc2,
       yc3;

  A_Sumador_BCDN a_sumador_bcdn_1 (
    ._1a3(xa3), ._2a3(ya3), ._1a2(xa2), ._2a2(ya2), ._1a1(xa1), ._2a1(ya1), ._1a0(xa0), ._2a0(ya0),
    ._1b3(xb3), ._2b3(yb3), ._1b2(xb2), ._2b2(yb2), ._1b1(xb1), ._2b1(yb1), ._1b0(xb0), ._2b0(yb0),
    ._1c3(xc3), ._2c3(yc3), ._1c2(xc2), ._2c2(yc2), ._1c1(xc1), ._2c1(yc1), ._1c0(xc0), ._2c0(yc0),
    .ar3(a_sumador_bcdn_1_ar3), .ar2(a_sumador_bcdn_1_ar2), .ar1(a_sumador_bcdn_1_ar1),
    .ar0(a_sumador_bcdn_1_ar0), .br3(a_sumador_bcdn_1_br3), .br2(a_sumador_bcdn_1_br2),
    .br1(a_sumador_bcdn_1_br1), .br0(a_sumador_bcdn_1_br0), .cr3(a_sumador_bcdn_1_cr3),
    .cr2(a_sumador_bcdn_1_cr2), .cr1(a_sumador_bcdn_1_cr1), .cr0(a_sumador_bcdn_1_cr0));
  and and_1 (and_1_out, ~cero, complemento);  // AND_Gate
  complemento_a_9 complemento_a_9_1 (
    .control(and_1_out), .a3(a_sumador_bcdn_1_ar3), .a2(a_sumador_bcdn_1_ar2), .a1(a_sumador_bcdn_1_ar1),
    .a0(a_sumador_bcdn_1_ar0), .b3(ar3), .b2(ar2), .b1(ar1), .b0(ar0));
  complemento_a_9 complemento_a_9_2 (
    .control(and_1_out), .a3(a_sumador_bcdn_1_br3), .a2(a_sumador_bcdn_1_br2), .a1(a_sumador_bcdn_1_br1),
    .a0(a_sumador_bcdn_1_br0), .b3(br3), .b2(br2), .b1(br1), .b0(br0));
  complemento_a_9 complemento_a_9_3 (
    .control(and_1_out), .a3(a_sumador_bcdn_1_cr3), .a2(a_sumador_bcdn_1_cr2), .a1(a_sumador_bcdn_1_cr1),
    .a0(a_sumador_bcdn_1_cr0), .b3(cr3), .b2(cr2), .b1(cr1), .b0(cr0));
  xor xor_1 (xor_1_out, signo_2, o_minus);
  and and_2 (and_2_out, xor_1_out, ~_2cero);  // AND_Gate
  A_5_1__complemento a_5_1_complemento_1 (
    .signo_numero_1(and_3_out), .complementar(and_2_out), ._2a3(_2a3), ._2a2(_2a2), ._2a1(_2a1), ._2a0(_2a0),
    ._2b3(_2b3), ._2b2(_2b2), ._2b1(_2b1), ._2b0(_2b0), ._2c3(_2c3), ._2c2(_2c2), ._2c1(_2c1), ._2c0(_2c0),
    .xa3(xa3), .xa2(xa2), .xa1(xa1), .xa0(xa0), .xb3(xb3), .xb2(xb2), .xb1(xb1), .xb0(xb0), .xc3(xc3),
    .xc2(xc2), .xc1(xc1), .xc0(xc0), .ya3(ya3), .ya2(ya2), .ya1(ya1), .ya0(ya0), .yb3(yb3), .yb2(yb2),
    .yb1(yb1), .yb0(yb0), .yc3(yc3), .yc2(yc2), .yc1(yc1), .yc0(yc0), ._1a3(_1a3), ._1a2(_1a2), ._1a1(_1a1),
    ._1a0(_1a0), ._1b3(_1b3), ._1b2(_1b2), ._1b1(_1b1), ._1b0(_1b0), ._1c3(_1c3), ._1c2(_1c2), ._1c1(_1c1),
    ._1c0(_1c0));
  and and_3 (and_3_out, signo_1, ~_1cero);  // AND_Gate
  cero cero_1 (
    .a3(_1a3), .a2(_1a2), .a1(_1a1), .a0(_1a0), .b3(_1b3), .b2(_1b2), .b1(_1b1), .b0(_1b0), .c3(_1c3),
    .c2(_1c2), .c1(_1c1), .c0(_1c0), ._0(_1cero));
  and and_4 (cero, _1cero, _2cero);
  cero cero_2 (
    .a3(_2a3), .a2(_2a2), .a1(_2a1), .a0(_2a0), .b3(_2b3), .b2(_2b2), .b1(_2b1), .b0(_2b0), .c3(_2c3),
    .c2(_2c2), .c1(_2c1), .c0(_2c0), ._0(_2cero));
  A_5__A_3_4_bits_3_veces_y_da_Resultado_o_Acarreo a_5_a_3_4_bits_3_veces_y_da_resultado_o_acarreo_1 (
    .signo_1(signo_1), .signo_2(signo_2), .o_minus(o_minus), ._1a3(_1a3), ._1a2(_1a2), ._1a1(_1a1),
    ._1a0(_1a0), ._2a3(_2a3), ._2a2(_2a2), ._2a1(_2a1), ._2a0(_2a0), ._1b3(_1b3), ._1b2(_1b2), ._1b1(_1b1),
    ._1b0(_1b0), ._2b3(_2b3), ._2b2(_2b2), ._2b1(_2b1), ._2b0(_2b0), ._1c3(_1c3), ._1c2(_1c2), ._1c1(_1c1),
    ._1c0(_1c0), ._2c3(_2c3), ._2c2(_2c2), ._2c1(_2c1), ._2c0(_2c0), .R(resultado), .complemento(complemento));

  // Other names for the same wires on the sheet: sig_1 = signo_1; sig_2 = signo_2
endmodule

module _15_9 (
  input  a3,
  input  a2,
  input  a1,
  input  a0,
  input  b3,
  input  b2,
  input  b1,
  input  b0,
  output overflow
);

  wire n1_1_error, n1_1_uno, n5_1_mayor;

  _1 u_1_1 (.s3(a3), .s2(a2), .s1(a1), .s0(a0), .error(n1_1_error), .uno(n1_1_uno));
  _5 u_5_1 (.c(n1_1_uno), .s3(b3), .s2(b2), .s1(b1), .s0(b0), .mayor(n5_1_mayor));
  or or_1 (overflow, n1_1_error, n5_1_mayor);
endmodule

module _1 (
  input  s3,
  input  s2,
  input  s1,
  input  s0,
  output error,
  output uno
);

  wire and_1_out, and_2_out, and_3_out, not_1_out, not_2_out, not_3_out, not_4_out, not_5_out, not_6_out,
       not_7_out;

  not not_1 (not_1_out, s3);
  and and_1 (and_1_out, not_1_out, s1);
  not not_2 (not_2_out, s3);
  and and_2 (and_2_out, not_2_out, s2);
  and and_3 (and_3_out, s3, not_3_out, not_4_out);
  not not_3 (not_3_out, s2);
  not not_4 (not_4_out, s1);
  not not_5 (not_5_out, s3);
  not not_6 (not_6_out, s2);
  not not_7 (not_7_out, s1);
  or or_1 (error, and_1_out, and_2_out, and_3_out);
  and and_4 (uno, not_5_out, not_6_out, not_7_out, s0);
endmodule

module _5 (
  input  c,
  input  s3,
  input  s2,
  input  s1,
  input  s0,
  output mayor
);

  wire and_1_out, and_2_out, not_1_out, not_2_out, not_3_out;

  not not_1 (not_1_out, s3);
  not not_2 (not_2_out, s2);
  not not_3 (not_3_out, s1);
  and and_1 (and_1_out, c, not_1_out, s2, s1);
  and and_2 (and_2_out, c, s3, not_2_out, not_3_out);
  or or_1 (mayor, and_1_out, and_2_out);
endmodule

// >9
module _9 (
  input  b0,
  input  b1,
  input  b2,
  input  b3,
  output mayor9
);

  wire and_1_out, and_2_out;

  and and_1 (and_1_out, b2, b3);
  and and_2 (and_2_out, b1, b3);
  or or_1 (mayor9, and_1_out, and_2_out);
endmodule

module es_cero (
  input  s3,
  input  s2,
  input  s1,
  input  s0,
  output R
);

  wire not_1_out, not_2_out, not_3_out, not_4_out;

  not not_1 (not_1_out, s3);
  not not_2 (not_2_out, s2);
  not not_3 (not_3_out, s1);
  not not_4 (not_4_out, s0);
  and and_1 (R, not_1_out, not_2_out, not_3_out, not_4_out);
endmodule

// 0?
module cero (
  input  a3,
  input  a2,
  input  a1,
  input  a0,
  input  b3,
  input  b2,
  input  b1,
  input  b0,
  input  c3,
  input  c2,
  input  c1,
  input  c0,
  output _0
);

  wire es_cero_1_r, es_cero_2_r, es_cero_3_r;

  es_cero es_cero_1 (.s3(a3), .s2(a2), .s1(a1), .s0(a0), .R(es_cero_1_r));
  es_cero es_cero_2 (.s3(b3), .s2(b2), .s1(b1), .s0(b0), .R(es_cero_2_r));
  es_cero es_cero_3 (.s3(c3), .s2(c2), .s1(c1), .s0(c0), .R(es_cero_3_r));
  and and_1 (_0, es_cero_1_r, es_cero_2_r, es_cero_3_r);
endmodule

// B
module B_suma_bcd (
  input  a3,
  input  b3,
  input  a2,
  input  b2,
  input  a1,
  input  b1,
  input  a0,
  input  b0,
  input  acarreo_0,
  output R3,
  output R2,
  output R1,
  output R0,
  output acarreo
);

  wire c_suma_sin_ajuste_1_acarreo, c_suma_sin_ajuste_1_b0_2, c_suma_sin_ajuste_1_b1_2,
       c_suma_sin_ajuste_1_b2_2, c_suma_sin_ajuste_1_b3_2, c_suma_sin_ajuste_2_acarreo,
       e_mayor_que_9_1_mayor__que_nueve, or_1_out;

  C_suma_sin_ajuste c_suma_sin_ajuste_1 (
    .a3(a3), .b3(b3), .a2(a2), .b2(b2), .a1(a1), .b1(b1), .a0(a0), .b0(b0), .acarreo_0(acarreo_0),
    .acarreo(c_suma_sin_ajuste_1_acarreo), .b3_2(c_suma_sin_ajuste_1_b3_2), .b2_2(c_suma_sin_ajuste_1_b2_2),
    .b1_2(c_suma_sin_ajuste_1_b1_2), .b0_2(c_suma_sin_ajuste_1_b0_2));
  E_mayor_que_9 e_mayor_que_9_1 (
    .b3(c_suma_sin_ajuste_1_b3_2), .b2(c_suma_sin_ajuste_1_b2_2), .b1(c_suma_sin_ajuste_1_b1_2),
    .b0(c_suma_sin_ajuste_1_b0_2), .mayor__que_nueve(e_mayor_que_9_1_mayor__que_nueve));
  or or_1 (or_1_out, c_suma_sin_ajuste_1_acarreo, e_mayor_que_9_1_mayor__que_nueve);
  C_suma_sin_ajuste c_suma_sin_ajuste_2 (
    .a3(c_suma_sin_ajuste_1_b3_2), .b3(1'b0), .a2(c_suma_sin_ajuste_1_b2_2), .b2(or_1_out),
    .a1(c_suma_sin_ajuste_1_b1_2), .b1(or_1_out), .a0(c_suma_sin_ajuste_1_b0_2), .b0(1'b0), .acarreo_0(1'b0),
    .acarreo(c_suma_sin_ajuste_2_acarreo), .b3_2(R3), .b2_2(R2), .b1_2(R1), .b0_2(R0));
  or or_2 (acarreo, c_suma_sin_ajuste_2_acarreo, or_1_out);

  // Notes on the sheet:
  //   suma
  //   mayor que 9 ?
  //   ajuste si o no?
  //   si hay acarreo o mayor que 9 suma 0110
  //   ajuste
  //   d1 y d2
  //   ingresan los dos numeros de cuatro bits
  //   resultado con ajuste
  //   acarreo definitivo
endmodule

// C
module C_suma_sin_ajuste (
  input  acarreo_0,
  input  a3,
  input  b3,
  input  a2,
  input  b2,
  input  a1,
  input  b1,
  input  a0,
  input  b0,
  output acarreo,
  output b3_2,
  output b2_2,
  output b1_2,
  output b0_2
);

  wire d_sumadorde3_2_acarreo, d_sumadorde3_3_acarreo, d_sumadorde3_4_acarreo;

  D_sumadorde3 d_sumadorde3_1 (.C(d_sumadorde3_2_acarreo), .A(a3), .B(b3), .acarreo(acarreo), .Sum(b3_2));
  D_sumadorde3 d_sumadorde3_2 (
    .C(d_sumadorde3_3_acarreo), .A(a2), .B(b2), .acarreo(d_sumadorde3_2_acarreo), .Sum(b2_2));
  D_sumadorde3 d_sumadorde3_3 (
    .C(d_sumadorde3_4_acarreo), .A(a1), .B(b1), .acarreo(d_sumadorde3_3_acarreo), .Sum(b1_2));
  D_sumadorde3 d_sumadorde3_4 (.C(acarreo_0), .A(a0), .B(b0), .acarreo(d_sumadorde3_4_acarreo), .Sum(b0_2));
endmodule

// D
module D_sumadorde3 (
  input  A,
  input  B,
  input  C,
  output acarreo,
  output Sum
);

  wire aca0_out, aca1_out, Sum0_out;

  xor Sum0 (Sum0_out, A, B);
  and aca0 (aca0_out, B, A);
  and aca1 (aca1_out, C, Sum0_out);
  xor Sum1 (Sum, Sum0_out, C);
  or or_1 (acarreo, aca0_out, aca1_out);

  // Notes on the sheet:
  //   acarreo de sumatoria de anterior columna
  //   suma de primer numero con segundo
endmodule

module semisumadores_base (
  input  A,
  input  B,
  output acarreo,
  output Sum
);

  and u_Acarreo (acarreo, B, A);
  xor Suma (Sum, A, B);
endmodule

// E >9
module E_mayor_que_9 (
  input  b3,
  input  b2,
  input  b1,
  input  b0,
  output mayor__que_nueve
);

  wire and_1_out, and_2_out;

  and and_1 (and_1_out, b3, b2);
  or or_1 (mayor__que_nueve, and_1_out, and_2_out);
  and and_2 (and_2_out, b1, b3);
endmodule

// C9
module complemento_a_9 (
  input  control,
  input  a3,
  input  a2,
  input  a1,
  input  a0,
  output b3,
  output b2,
  output b1,
  output b0
);

  wire and_1_out, and_2_out, and_3_out, and_4_out, and_5_out, and_6_out, and_7_out, not_1_out, not_2_out,
       not_3_out, not_4_out, not_5_out, not_6_out, not_7_out, not_8_out, not_9_out;

  not not_1 (not_1_out, control);
  not not_2 (not_2_out, a3);
  not not_3 (not_3_out, a2);
  not not_4 (not_4_out, a1);
  not not_5 (not_5_out, control);
  not not_6 (not_6_out, a1);
  not not_7 (not_7_out, a2);
  not not_8 (not_8_out, control);
  not not_9 (not_9_out, a0);
  and and_1 (and_1_out, not_1_out, a3);
  and and_2 (and_2_out, control, not_2_out, not_3_out, not_4_out);
  and and_3 (and_3_out, not_5_out, a2);
  and and_4 (and_4_out, a2, not_6_out);
  and and_5 (and_5_out, control, not_7_out, a1);
  and and_6 (and_6_out, not_8_out, a0);
  and and_7 (and_7_out, control, not_9_out);
  or or_1 (b3, and_1_out, and_2_out);
  or or_2 (b2, and_3_out, and_4_out, and_5_out);
  or or_3 (b0, and_6_out, and_7_out);

  assign b1 = a1;
endmodule

module _7_segmentos (
  input  b3,
  input  b2,
  input  b1,
  input  b0
);

  wire display_1_a, display_1_b, display_1_c, display_1_d, display_1_e, display_1_f, display_1_g;

  display display_1 (
    .b3(b3), .b2(b2), .b1(b1), .b0(b0), .a(display_1_a), .b(display_1_b), .c(display_1_c), .d(display_1_d),
    .e(display_1_e), .f(display_1_f), .g(display_1_g));  // open: in_5
  _7_Segment_Display u_7_segment_display_1 (
    .g(display_1_g), .f(display_1_a), .a(display_1_b), .b(display_1_c), .e(display_1_d), .d(display_1_f),
    .c(display_1_e));  // open: dp
endmodule

// 7segme
module display (
  input  b3,
  input  b2,
  input  b1,
  input  b0,
  input  in_5,
  output a,
  output b,
  output c,
  output d,
  output e,
  output f,
  output g
);

  wire and_1_out, and_2_out, and_3_out, and_4_out, and_5_out, and_6_out, and_7_out, and_8_out, and_9_out,
       and_10_out, and_11_out, and_12_out, and_13_out, and_14_out, and_15_out, and_16_out, and_17_out,
       and_18_out, and_19_out, and_20_out, and_21_out, and_22_out, and_23_out, and_24_out, and_25_out,
       and_26_out, and_27_out, and_28_out, not_1_out, not_2_out, not_3_out, not_4_out, not_5_out, not_6_out,
       not_7_out, not_8_out, not_9_out, not_10_out, not_11_out, not_12_out, not_13_out, not_14_out,
       not_15_out, not_16_out, not_17_out, not_18_out, not_19_out, or_1_out, or_2_out, or_3_out, or_4_out,
       or_5_out, or_6_out, or_7_out;

  not not_1 (not_1_out, b1);
  not not_2 (not_2_out, b0);
  not not_3 (not_3_out, b2);
  not not_4 (not_4_out, b0);
  not not_5 (not_5_out, b1);
  not not_6 (not_6_out, b0);
  not not_7 (not_7_out, b2);
  not not_8 (not_8_out, b0);
  not not_9 (not_9_out, b0);
  not not_10 (not_10_out, b1);
  not not_11 (not_11_out, b2);
  not not_12 (not_12_out, b0);
  not not_13 (not_13_out, b2);
  not not_14 (not_14_out, b0);
  not not_15 (not_15_out, b1);
  not not_16 (not_16_out, b2);
  not not_17 (not_17_out, b1);
  not not_18 (not_18_out, b0);
  and and_1 (and_1_out, not_1_out, not_2_out);
  and and_2 (and_2_out, not_3_out, not_4_out);
  and and_3 (and_3_out, b2, b0);
  not not_19 (not_19_out, b2);
  and and_4 (and_4_out, not_5_out, not_6_out);
  and and_5 (and_5_out, b1, b0);
  and and_6 (and_6_out, not_7_out, not_8_out);
  and and_7 (and_7_out, b1, not_9_out);
  or or_1 (or_1_out, not_10_out, b0, b2);
  and and_8 (and_8_out, not_11_out, not_12_out);
  and and_9 (and_9_out, not_13_out, b1);
  and and_10 (and_10_out, b1, not_14_out);
  and and_11 (and_11_out, b2, not_15_out, b0);
  and and_12 (and_12_out, not_16_out, b1);
  and and_13 (and_13_out, b2, not_17_out);
  and and_14 (and_14_out, b2, not_18_out);
  or or_2 (or_2_out, and_1_out, b2, b3);
  or or_3 (or_3_out, and_2_out, b1, and_3_out, b3);
  or or_4 (or_4_out, not_19_out, and_4_out, and_5_out);
  or or_5 (or_5_out, and_6_out, and_7_out);
  or or_6 (or_6_out, and_8_out, and_9_out, and_10_out, and_11_out);
  or or_7 (or_7_out, and_12_out, and_13_out, and_14_out, b3);
  and and_15 (and_15_out, or_2_out, ~in_5);  // AND_Gate
  or or_8 (a, and_15_out, and_16_out);
  and and_16 (and_16_out, 1'b1, in_5);
  and and_17 (and_17_out, or_3_out, ~in_5);  // AND_Gate
  or or_9 (b, and_17_out, and_18_out);
  and and_18 (and_18_out, 1'b1, in_5);
  and and_19 (and_19_out, or_4_out, ~in_5);  // AND_Gate
  or or_10 (c, and_19_out, and_20_out);
  and and_20 (and_20_out, 1'b0, in_5);
  and and_21 (and_21_out, or_5_out, ~in_5);  // AND_Gate
  or or_11 (d, and_21_out, and_22_out);
  and and_22 (and_22_out, 1'b1, in_5);
  and and_23 (and_23_out, or_1_out, ~in_5);  // AND_Gate
  or or_12 (e, and_23_out, and_24_out);
  and and_24 (and_24_out, 1'b0, in_5);
  and and_25 (and_25_out, or_6_out, ~in_5);  // AND_Gate
  or or_13 (f, and_25_out, and_26_out);
  and and_26 (and_26_out, 1'b0, in_5);
  and and_27 (and_27_out, or_7_out, ~in_5);  // AND_Gate
  or or_14 (g, and_27_out, and_28_out);
  and and_28 (and_28_out, 1'b0, in_5);
endmodule

module pulso (
  input  _9,
  input  _8,
  input  _7,
  input  _6,
  input  _5,
  input  cnt_on_off,
  input  _4,
  input  _3,
  input  _2,
  input  _1,
  input  _0,
  output pulso
);

  wire xor_1_out;

  ExactlyOne xor_1 (
    .out(xor_1_out), .in0(_9), .in1(_8), .in2(_7), .in3(_6), .in4(_5), .in5(_4), .in6(_3), .in7(_2),
    .in8(_1), .in9(_0));
  and and_1 (pulso, xor_1_out, ~cnt_on_off);  // AND_Gate
endmodule

// contador
module contador_0_15 (
  input  On,
  input  Ck,
  input  Off,
  input  _2,
  output estatus_contador,
  output _2_3,
  output _2_0,
  output _2_1,
  output _2_2
);

  wire and_1_out, and_2_out, and_3_out, or_1_out;

  or or_1 (or_1_out, _2, Off);
  S_R_Flip_Flop s_r_ff_1 (.Q(estatus_contador), .preset(On), .reset(or_1_out));  // open: S, clk, R, Qn, en
  J_K_Flip_Flop j_k_ff_1 (
    .J(estatus_contador), .clk(Ck), .K(estatus_contador), .Q(_2_0), .reset(Off));  // open: Qn, preset, en
  and and_1 (and_1_out, estatus_contador, _2_0);
  J_K_Flip_Flop j_k_ff_2 (.J(and_1_out), .clk(Ck), .K(and_1_out), .Q(_2_1), .reset(Off));  // open: Qn, preset, en
  and and_2 (and_2_out, and_1_out, _2_1);
  J_K_Flip_Flop j_k_ff_3 (.J(and_2_out), .clk(Ck), .K(and_2_out), .Q(_2_2), .reset(Off));  // open: Qn, preset, en
  and and_3 (and_3_out, and_2_out, _2_2);
  J_K_Flip_Flop j_k_ff_4 (.J(and_3_out), .clk(Ck), .K(and_3_out), .Q(_2_3), .reset(Off));  // open: Qn, preset, en
endmodule

module contador_ampliado_63 (
  input  On,
  input  Ck,
  input  Off,
  input  _2,
  output estatus_contador,
  output _2_5,
  output _2_6,
  output _2_0,
  output _2_1,
  output _2_2,
  output _2_3,
  output _2_4
);

  wire and_1_out, and_2_out, and_3_out, and_4_out, and_5_out, and_6_out, or_1_out;

  or or_1 (or_1_out, _2, Off);
  S_R_Flip_Flop s_r_ff_1 (.Q(estatus_contador), .preset(On), .reset(or_1_out));  // open: S, clk, R, Qn, en
  J_K_Flip_Flop j_k_ff_1 (
    .J(estatus_contador), .clk(Ck), .K(estatus_contador), .Q(_2_0), .reset(Off));  // open: Qn, preset, en
  and and_1 (and_1_out, estatus_contador, _2_0);
  J_K_Flip_Flop j_k_ff_2 (.J(and_1_out), .clk(Ck), .K(and_1_out), .Q(_2_1), .reset(Off));  // open: Qn, preset, en
  and and_2 (and_2_out, and_1_out, _2_1);
  J_K_Flip_Flop j_k_ff_3 (.J(and_2_out), .clk(Ck), .K(and_2_out), .Q(_2_2), .reset(Off));  // open: Qn, preset, en
  and and_3 (and_3_out, and_2_out, _2_2);
  J_K_Flip_Flop j_k_ff_4 (.J(and_3_out), .clk(Ck), .K(and_3_out), .Q(_2_3), .reset(Off));  // open: Qn, preset, en
  and and_4 (and_4_out, and_3_out, _2_3);
  J_K_Flip_Flop j_k_ff_5 (.J(and_4_out), .clk(Ck), .K(and_4_out), .Q(_2_4), .reset(Off));  // open: Qn, preset, en
  and and_5 (and_5_out, and_4_out, _2_4);
  J_K_Flip_Flop j_k_ff_6 (.J(and_5_out), .clk(Ck), .K(and_5_out), .Q(_2_5), .reset(Off));  // open: Qn, preset, en
  and and_6 (and_6_out, and_5_out, _2_5);
  J_K_Flip_Flop j_k_ff_7 (.J(and_6_out), .clk(Ck), .K(and_6_out), .Q(_2_6), .reset(Off));  // open: Qn, preset, en
endmodule

// X multi
module X_multi_5bits (
  input  a4,
  input  a3,
  input  a2,
  input  a1,
  input  a0,
  input  b4,
  input  b3,
  input  b2,
  input  b1,
  input  b0,
  input  acarreo_0,
  output acarreo,
  output b4_2,
  output b3_2,
  output b2_2,
  output b1_2,
  output b0_2
);

  wire d_sumadorde3_2_acarreo, d_sumadorde3_3_acarreo, d_sumadorde3_4_acarreo, d_sumadorde3_5_acarreo;

  D_sumadorde3 d_sumadorde3_1 (.C(d_sumadorde3_2_acarreo), .A(a4), .B(b4), .acarreo(acarreo), .Sum(b4_2));
  D_sumadorde3 d_sumadorde3_2 (
    .C(d_sumadorde3_3_acarreo), .A(a3), .B(b3), .acarreo(d_sumadorde3_2_acarreo), .Sum(b3_2));
  D_sumadorde3 d_sumadorde3_3 (
    .C(d_sumadorde3_4_acarreo), .A(a2), .B(b2), .acarreo(d_sumadorde3_3_acarreo), .Sum(b2_2));
  D_sumadorde3 d_sumadorde3_4 (
    .C(d_sumadorde3_5_acarreo), .A(a1), .B(b1), .acarreo(d_sumadorde3_4_acarreo), .Sum(b1_2));
  D_sumadorde3 d_sumadorde3_5 (.C(acarreo_0), .A(a0), .B(b0), .acarreo(d_sumadorde3_5_acarreo), .Sum(b0_2));
endmodule

// >=
module y_paso (
  input  b0,
  input  b1,
  input  b2,
  input  b3,
  input  b4,
  input  habiltacion,
  output b0_2,
  output b1_2,
  output b2_2,
  output b3_2,
  output b4_2
);

  and and_1 (b0_2, b0, habiltacion);
  and and_2 (b1_2, b1, habiltacion);
  and and_3 (b2_2, b2, habiltacion);
  and and_4 (b3_2, b3, habiltacion);
  and and_5 (b4_2, b4, habiltacion);
endmodule

// paso
module habilitacion (
  input  b0,
  input  b1,
  input  b2,
  input  b3,
  input  in_5,
  output s0,
  output s1,
  output s2,
  output s3
);

  and and_1 (s0, in_5, b0);
  and and_2 (s1, in_5, b1);
  and and_3 (s2, in_5, b2);
  and and_4 (s3, in_5, b3);
endmodule

// =
module paso_resultado (
  input  c0,
  input  c1,
  input  c2,
  input  c3,
  input  b0,
  input  b1,
  input  b2,
  input  b3,
  input  a0,
  input  a1,
  input  a2,
  input  a3,
  input  igual,
  output c0_2,
  output c1_2,
  output c2_2,
  output c3_2,
  output b0_2,
  output b1_2,
  output b2_2,
  output b3_2,
  output a0_2,
  output a1_2,
  output a2_2,
  output a3_2
);

  habilitacion habilitacion_1 (
    .b0(c0), .b1(c1), .b2(c2), .b3(c3), .in_5(igual), .s0(c0_2), .s1(c1_2), .s2(c2_2), .s3(c3_2));
  habilitacion habilitacion_2 (
    .b0(b0), .b1(b1), .b2(b2), .b3(b3), .in_5(igual), .s0(b0_2), .s1(b1_2), .s2(b2_2), .s3(b3_2));
  habilitacion habilitacion_3 (
    .b0(a0), .b1(a1), .b2(a2), .b3(a3), .in_5(igual), .s0(a0_2), .s1(a1_2), .s2(a2_2), .s3(a3_2));
endmodule

module op_x (
  input  _2c3,
  input  _2c2,
  input  _2c1,
  input  _2c0,
  input  _1a4,
  input  _1a3,
  input  _1a2,
  input  _1a1,
  input  _1b3,
  input  _1c3,
  input  _1c2,
  input  _1c1,
  input  _1c0,
  input  _2a4,
  input  _2a3,
  input  _2a2,
  input  _2a1,
  input  _2b3,
  input  condicion_1,
  input  ac,
  output _2a4_2,
  output _2a3_2,
  output _2a2_2,
  output _2a1_2,
  output _2a0,
  output _1a4_2,
  output _1a3_2,
  output _1a2_2,
  output _1a1_2,
  output _1a0
);

  wire codificador_bcd_a_binario_1_s0, codificador_bcd_a_binario_1_s1, codificador_bcd_a_binario_1_s2,
       codificador_bcd_a_binario_1_s3, codificador_bcd_a_binario_2_s0, codificador_bcd_a_binario_2_s1,
       codificador_bcd_a_binario_2_s2, codificador_bcd_a_binario_2_s3, codificador_flotante_1_flotante,
       codificador_flotante_2_flotante;

  codificador_bcd_a_binario codificador_bcd_a_binario_1 (
    .a4(_1b3), .a3(_1a4), .a2(_1a3), .a1(_1a2), .a0(_1a1), .s3(codificador_bcd_a_binario_1_s3),
    .s2(codificador_bcd_a_binario_1_s2), .s1(codificador_bcd_a_binario_1_s1),
    .s0(codificador_bcd_a_binario_1_s0));
  codificador_flotante codificador_flotante_1 (
    .b0(_1c0), .b1(_1c1), .b2(_1c2), .b3(_1c3), .flotante(codificador_flotante_1_flotante));
  Rd_DaI_serie_y_paralela_habilitacion_5 rd_dai_serie_y_paralela_habilitacion_5_1 (
    .paso(condicion_1), .Pa0(ac), .b4(codificador_bcd_a_binario_1_s3), .b3(codificador_bcd_a_binario_1_s2),
    .b2(codificador_bcd_a_binario_1_s1), .b1(codificador_bcd_a_binario_1_s0),
    .b0(codificador_flotante_1_flotante), .b4_2(_1a4_2), .b3_2(_1a3_2), .b2_2(_1a2_2), .b1_2(_1a1_2),
    .b0_2(_1a0));  // open: Ss, pulso, Es
  codificador_bcd_a_binario codificador_bcd_a_binario_2 (
    .a4(_2b3), .a3(_2a4), .a2(_2a3), .a1(_2a2), .a0(_2a1), .s3(codificador_bcd_a_binario_2_s3),
    .s2(codificador_bcd_a_binario_2_s2), .s1(codificador_bcd_a_binario_2_s1),
    .s0(codificador_bcd_a_binario_2_s0));
  Rd_DaI_serie_y_paralela_habilitacion_5 rd_dai_serie_y_paralela_habilitacion_5_2 (
    .paso(condicion_1), .Pa0(ac), .b4(codificador_bcd_a_binario_2_s3), .b3(codificador_bcd_a_binario_2_s2),
    .b2(codificador_bcd_a_binario_2_s1), .b1(codificador_bcd_a_binario_2_s0),
    .b0(codificador_flotante_2_flotante), .b4_2(_2a4_2), .b3_2(_2a3_2), .b2_2(_2a2_2), .b1_2(_2a1_2),
    .b0_2(_2a0));  // open: Ss, pulso, Es
  codificador_flotante codificador_flotante_2 (
    .b0(_2c0), .b1(_2c1), .b2(_2c2), .b3(_2c3), .flotante(codificador_flotante_2_flotante));

  // Other names for the same wires on the sheet: _1 = condicion_1
endmodule

module _0_divisor (
  input  a4,
  input  a3,
  input  a2,
  input  a1,
  input  a0,
  output _0
);

  wire es_cero_1_r;

  es_cero es_cero_1 (.s3(a4), .s2(a3), .s1(a2), .s0(a1), .R(es_cero_1_r));
  and and_1 (_0, es_cero_1_r, ~a0);  // AND_Gate
endmodule

// RD D/I
module RD_Der_Izq_24 (
  input  Pa0,
  input  On,
  input  a3,
  input  a2,
  input  a1,
  input  a0,
  input  dir,
  input  Ck,
  output out_9,
  output S23,
  output S22,
  output S21,
  output S20,
  output S19,
  output S18,
  output S17,
  output S16,
  output S15,
  output S14,
  output S13,
  output S12,
  output S11,
  output S10,
  output S9,
  output S8,
  output S7,
  output S6,
  output S5,
  output S4,
  output S3,
  output S2,
  output S1,
  output S0
);

  wire and_1_out, and_2_out, and_3_out, and_4_out, and_5_out, and_6_out, and_7_out, and_8_out, and_9_out,
       and_10_out, and_11_out, and_12_out, and_13_out, and_14_out, and_15_out, and_16_out, and_17_out,
       and_18_out, and_19_out, and_20_out, and_21_out, and_22_out, and_23_out, and_24_out, and_25_out,
       and_26_out, and_27_out, and_28_out, and_29_out, and_30_out, and_31_out, and_32_out, and_33_out,
       and_34_out, and_35_out, and_36_out, and_37_out, and_38_out, and_39_out, and_40_out, and_41_out,
       and_42_out, and_43_out, and_44_out, and_45_out, and_46_out, and_47_out, and_48_out, and_50_out,
       and_51_out, and_52_out, and_53_out, contador_0_15_1__2_0, contador_0_15_1__2_1, contador_0_15_1__2_2,
       contador_0_15_1_estatus_contador, controlled_buffer_1_out, I_D_y_pulso_out, off_cont, or_1_out,
       or_2_out, or_3_out, or_4_out, or_5_out, or_6_out, or_7_out, or_8_out, or_9_out, or_10_out, or_11_out,
       or_12_out, or_13_out, or_14_out, or_15_out, or_16_out, or_17_out, or_18_out, or_19_out, or_20_out,
       or_21_out, or_22_out, or_23_out, or_24_out, s_r_ff_1_q;

  S_R_Flip_Flop s_r_ff_1 (.Q(s_r_ff_1_q), .preset(dir), .reset(off_cont));  // open: S, clk, R, Qn, en
  and and_1 (and_1_out, 1'b0, s_r_ff_1_q);
  and and_2 (and_2_out, ~s_r_ff_1_q, S22);  // AND_Gate
  or or_1 (or_1_out, and_1_out, and_2_out);
  and and_3 (and_3_out, S23, s_r_ff_1_q);
  D_Flip_Flop d_ff_1 (.clk(controlled_buffer_1_out), .D(or_1_out), .Q(S23), .reset(Pa0));  // open: Qn, preset, en
  and and_4 (and_4_out, ~s_r_ff_1_q, S21);  // AND_Gate
  or or_2 (or_2_out, and_3_out, and_4_out);
  D_Flip_Flop d_ff_2 (.clk(controlled_buffer_1_out), .D(or_2_out), .Q(S22), .reset(Pa0));  // open: Qn, preset, en
  and and_5 (and_5_out, ~s_r_ff_1_q, S20);  // AND_Gate
  and and_6 (and_6_out, S22, s_r_ff_1_q);
  or or_3 (or_3_out, and_6_out, and_5_out);
  and and_7 (and_7_out, S21, s_r_ff_1_q);
  D_Flip_Flop d_ff_3 (.clk(controlled_buffer_1_out), .D(or_3_out), .Q(S21), .reset(Pa0));  // open: Qn, preset, en
  and and_8 (and_8_out, ~s_r_ff_1_q, S19);  // AND_Gate
  or or_4 (or_4_out, and_7_out, and_8_out);
  D_Flip_Flop d_ff_4 (.clk(controlled_buffer_1_out), .D(or_4_out), .Q(S20), .reset(Pa0));  // open: Qn, preset, en
  and and_9 (and_9_out, S20, s_r_ff_1_q);
  or or_5 (or_5_out, and_9_out, and_10_out);
  and and_10 (and_10_out, ~s_r_ff_1_q, S18);  // AND_Gate
  D_Flip_Flop d_ff_5 (.clk(controlled_buffer_1_out), .D(or_5_out), .Q(S19), .reset(Pa0));  // open: Qn, preset, en
  and and_11 (and_11_out, S19, s_r_ff_1_q);
  or or_6 (or_6_out, and_11_out, and_12_out);
  and and_12 (and_12_out, ~s_r_ff_1_q, S17);  // AND_Gate
  D_Flip_Flop d_ff_6 (.clk(controlled_buffer_1_out), .D(or_6_out), .Q(S18), .reset(Pa0));  // open: Qn, preset, en
  and and_13 (and_13_out, ~s_r_ff_1_q, S16);  // AND_Gate
  and and_14 (and_14_out, S18, s_r_ff_1_q);
  or or_7 (or_7_out, and_14_out, and_13_out);
  and and_15 (and_15_out, S17, s_r_ff_1_q);
  D_Flip_Flop d_ff_7 (.clk(controlled_buffer_1_out), .D(or_7_out), .Q(S17), .reset(Pa0));  // open: Qn, preset, en
  and and_16 (and_16_out, ~s_r_ff_1_q, S15);  // AND_Gate
  or or_8 (or_8_out, and_15_out, and_16_out);
  D_Flip_Flop d_ff_8 (.clk(controlled_buffer_1_out), .D(or_8_out), .Q(S16), .reset(Pa0));  // open: Qn, preset, en
  and and_17 (and_17_out, ~s_r_ff_1_q, S14);  // AND_Gate
  and and_18 (and_18_out, S16, s_r_ff_1_q);
  or or_9 (or_9_out, and_18_out, and_17_out);
  and and_19 (and_19_out, S15, s_r_ff_1_q);
  D_Flip_Flop d_ff_9 (.clk(controlled_buffer_1_out), .D(or_9_out), .Q(S15), .reset(Pa0));  // open: Qn, preset, en
  and and_20 (and_20_out, ~s_r_ff_1_q, S13);  // AND_Gate
  or or_10 (or_10_out, and_19_out, and_20_out);
  and and_21 (and_21_out, S14, s_r_ff_1_q);
  or or_11 (or_11_out, and_21_out, and_22_out);
  D_Flip_Flop d_ff_10 (.clk(controlled_buffer_1_out), .D(or_10_out), .Q(S14), .reset(Pa0));  // open: Qn, preset, en
  and and_22 (and_22_out, ~s_r_ff_1_q, S12);  // AND_Gate
  D_Flip_Flop d_ff_11 (.clk(controlled_buffer_1_out), .D(or_11_out), .Q(S13), .reset(Pa0));  // open: Qn, preset, en
  and and_23 (and_23_out, S13, s_r_ff_1_q);
  or or_12 (or_12_out, and_23_out, and_24_out);
  and and_24 (and_24_out, ~s_r_ff_1_q, S11);  // AND_Gate
  D_Flip_Flop d_ff_12 (.clk(controlled_buffer_1_out), .D(or_12_out), .Q(S12), .reset(Pa0));  // open: Qn, preset, en
  and and_25 (and_25_out, S12, s_r_ff_1_q);
  or or_13 (or_13_out, and_25_out, and_26_out);
  and and_26 (and_26_out, ~s_r_ff_1_q, S10);  // AND_Gate
  D_Flip_Flop d_ff_13 (.clk(controlled_buffer_1_out), .D(or_13_out), .Q(S11), .reset(Pa0));  // open: Qn, preset, en
  and and_27 (and_27_out, ~s_r_ff_1_q, S9);  // AND_Gate
  and and_28 (and_28_out, S11, s_r_ff_1_q);
  or or_14 (or_14_out, and_28_out, and_27_out);
  and and_29 (and_29_out, S10, s_r_ff_1_q);
  D_Flip_Flop d_ff_14 (.clk(controlled_buffer_1_out), .D(or_14_out), .Q(S10), .reset(Pa0));  // open: Qn, preset, en
  and and_30 (and_30_out, ~s_r_ff_1_q, S8);  // AND_Gate
  or or_15 (or_15_out, and_29_out, and_30_out);
  and and_31 (and_31_out, S9, s_r_ff_1_q);
  D_Flip_Flop d_ff_15 (.clk(controlled_buffer_1_out), .D(or_15_out), .Q(S9), .reset(Pa0));  // open: Qn, preset, en
  and and_32 (and_32_out, ~s_r_ff_1_q, S7);  // AND_Gate
  or or_16 (or_16_out, and_31_out, and_32_out);
  D_Flip_Flop d_ff_16 (.clk(controlled_buffer_1_out), .D(or_16_out), .Q(S8), .reset(Pa0));  // open: Qn, preset, en
  and and_33 (and_33_out, S8, s_r_ff_1_q);
  and and_34 (and_34_out, ~s_r_ff_1_q, S6);  // AND_Gate
  or or_17 (or_17_out, and_33_out, and_34_out);
  D_Flip_Flop d_ff_17 (.clk(controlled_buffer_1_out), .D(or_17_out), .Q(S7), .reset(Pa0));  // open: Qn, preset, en
  and and_35 (and_35_out, ~s_r_ff_1_q, S5);  // AND_Gate
  and and_36 (and_36_out, S7, s_r_ff_1_q);
  or or_18 (or_18_out, and_36_out, and_35_out);
  and and_37 (and_37_out, S6, s_r_ff_1_q);
  D_Flip_Flop d_ff_18 (.clk(controlled_buffer_1_out), .D(or_18_out), .Q(S6), .reset(Pa0));  // open: Qn, preset, en
  and and_38 (and_38_out, ~s_r_ff_1_q, S4);  // AND_Gate
  or or_19 (or_19_out, and_37_out, and_38_out);
  D_Flip_Flop d_ff_19 (.clk(controlled_buffer_1_out), .D(or_19_out), .Q(S5), .reset(Pa0));  // open: Qn, preset, en
  and and_39 (and_39_out, S5, s_r_ff_1_q);
  and and_40 (and_40_out, ~s_r_ff_1_q, S3);  // AND_Gate
  or or_20 (or_20_out, and_39_out, and_40_out);
  D_Flip_Flop d_ff_20 (.clk(controlled_buffer_1_out), .D(or_20_out), .Q(S4), .reset(Pa0));  // open: Qn, preset, en
  and and_41 (and_41_out, ~s_r_ff_1_q, S2);  // AND_Gate
  and and_42 (and_42_out, S4, s_r_ff_1_q);
  or or_21 (or_21_out, and_42_out, and_41_out);
  D_Flip_Flop d_ff_21 (.clk(controlled_buffer_1_out), .D(or_21_out), .Q(S3), .reset(Pa0));  // open: Qn, preset, en
  and and_43 (and_43_out, S3, s_r_ff_1_q);
  and and_44 (and_44_out, ~s_r_ff_1_q, S1);  // AND_Gate
  or or_22 (or_22_out, and_43_out, and_44_out);
  and and_45 (and_45_out, S2, s_r_ff_1_q);
  D_Flip_Flop d_ff_22 (.clk(controlled_buffer_1_out), .D(or_22_out), .Q(S2), .reset(Pa0));  // open: Qn, preset, en
  and and_46 (and_46_out, ~s_r_ff_1_q, S0);  // AND_Gate
  or or_23 (or_23_out, and_45_out, and_46_out);
  and and_47 (and_47_out, S1, s_r_ff_1_q);
  D_Flip_Flop d_ff_23 (.clk(controlled_buffer_1_out), .D(or_23_out), .Q(S1), .reset(Pa0));  // open: Qn, preset, en
  and and_48 (and_48_out, ~s_r_ff_1_q, out_9);  // AND_Gate
  or or_24 (or_24_out, and_47_out, and_48_out);
  assign controlled_buffer_1_out = contador_0_15_1_estatus_contador ? Ck : 1'bz;  // Controlled_Buffer controlled_buffer_1
  D_Flip_Flop d_ff_24 (.clk(controlled_buffer_1_out), .D(or_24_out), .Q(S0), .reset(Pa0));  // open: Qn, preset, en
  or I_D_y_pulso (I_D_y_pulso_out, s_r_ff_1_q, On);
  contador_0_15 contador_0_15_1 (
    .Ck(Ck), .On(I_D_y_pulso_out), .estatus_contador(contador_0_15_1_estatus_contador), .Off(off_cont),
    ._2_0(contador_0_15_1__2_0), ._2_1(contador_0_15_1__2_1), ._2_2(contador_0_15_1__2_2));  // open: _2, _2_3
  and and_49 (off_cont, ~contador_0_15_1__2_0, ~contador_0_15_1__2_1, contador_0_15_1__2_2);  // AND_Gate
  and and_50 (and_50_out, ~contador_0_15_1__2_0, ~contador_0_15_1__2_1, a3);  // AND_Gate
  and and_51 (and_51_out, contador_0_15_1__2_0, ~contador_0_15_1__2_1, a2);  // AND_Gate
  and and_52 (and_52_out, ~contador_0_15_1__2_0, contador_0_15_1__2_1, a1);  // AND_Gate
  and and_53 (and_53_out, contador_0_15_1__2_0, contador_0_15_1__2_1, a0);
  or or_25 (out_9, and_50_out, and_51_out, and_52_out, and_53_out);
endmodule

// RD
module DIR_I_D (
  input  Rst,
  input  PulsoOn,
  input  a3,
  input  a2,
  input  a1,
  input  a0,
  input  Dir,
  input  ck,
  output s23,
  output s22,
  output s21,
  output s20,
  output s19,
  output s18,
  output s17,
  output s16,
  output s15,
  output s14,
  output s13,
  output s12,
  output s11,
  output s10,
  output s9,
  output s8,
  output s7,
  output s6,
  output s5,
  output s4,
  output s3,
  output s2,
  output s1,
  output s0
);

  wire rd_der_izq_24_1_out_9;

  RD_Der_Izq_24 rd_der_izq_24_1 (
    .dir(Dir), .Ck(ck), .Pa0(Rst), .On(PulsoOn), .a3(a3), .a2(a2), .a1(a1), .a0(a0), .S23(s23), .S22(s22),
    .S21(s21), .S20(s20), .S19(s19), .S18(s18), .S17(s17), .S16(s16), .S15(s15), .S14(s14), .S13(s13),
    .S12(s12), .S11(s11), .S10(s10), .S9(s9), .S8(s8), .S7(s7), .S6(s6), .S5(s5), .S4(s4), .S3(s3), .S2(s2),
    .S1(s1), .S0(s0), .out_9(rd_der_izq_24_1_out_9));
  // Probe on rd_der_izq_24_1_out_9
endmodule

module D_A_E (
  input  pa1,
  input  Es,
  input  CK,
  input  PA0,
  output Q,
  output minus_Q
);

  wire d_ff_1_q, d_ff_1_qn, not_1_out;

  D_Flip_Flop d_ff_1 (.clk(CK), .D(Es), .Q(d_ff_1_q), .Qn(d_ff_1_qn), .preset(pa1), .reset(PA0));  // open: en
  not not_1 (not_1_out, CK);
  S_R_Flip_Flop s_r_ff_1 (
    .S(d_ff_1_q), .clk(not_1_out), .R(d_ff_1_qn), .Q(Q), .Qn(minus_Q), .preset(pa1), .reset(PA0));  // open: en
endmodule

module Rd_D_E_S_serie_y_paralela (
  input  d4,
  input  d3,
  input  d2,
  input  d1,
  input  d0,
  input  habilitacion,
  input  Ess,
  input  ck,
  input  pulsador,
  input  pa0,
  output Ss,
  output d4_2,
  output d3_2,
  output d2_2,
  output d1_2,
  output d0_2
);

  wire and_1_out, and_2_out, and_3_out, and_4_out, and_5_out, and_6_out, and_7_out, and_8_out, and_9_out,
       and_10_out, and_11_out;

  and and_1 (and_1_out, ck, pulsador);
  and and_2 (and_2_out, habilitacion, d4);
  D_A_E d_a_e_1 (.Es(Ess), .CK(and_1_out), .pa1(and_2_out), .PA0(and_3_out), .Q(d4_2));  // open: minus_Q
  and and_3 (and_3_out, habilitacion, ~d4);  // AND_Gate
  and and_4 (and_4_out, habilitacion, d3);
  D_A_E d_a_e_2 (.Es(d4_2), .CK(and_1_out), .pa1(and_4_out), .PA0(and_5_out), .Q(d3_2));  // open: minus_Q
  and and_5 (and_5_out, habilitacion, ~d3);  // AND_Gate
  and and_6 (and_6_out, habilitacion, d2);
  and and_7 (and_7_out, habilitacion, ~d2);  // AND_Gate
  D_A_E d_a_e_3 (.Es(d3_2), .CK(and_1_out), .pa1(and_6_out), .PA0(and_7_out), .Q(d2_2));  // open: minus_Q
  and and_8 (and_8_out, habilitacion, d1);
  D_A_E d_a_e_4 (.Es(d2_2), .CK(and_1_out), .pa1(and_8_out), .PA0(and_9_out), .Q(d1_2));  // open: minus_Q
  and and_9 (and_9_out, habilitacion, ~d1);  // AND_Gate
  and and_10 (and_10_out, habilitacion, d0);
  and and_11 (and_11_out, habilitacion, ~d0);  // AND_Gate
  D_A_E d_a_e_5 (.Es(d1_2), .CK(and_1_out), .pa1(and_10_out), .PA0(and_11_out), .Q(d0_2));  // open: minus_Q

  assign Ss = d0_2;
endmodule

module RD_E_S_serie_y_paralela_correcto (
  input  d4,
  input  d3,
  input  d2,
  input  d1,
  input  d0,
  input  habilitacion,
  input  Ess,
  input  pulsador,
  input  pa0,
  output Ss,
  output d4_2,
  output d3_2,
  output d2_2,
  output d1_2,
  output d0_2
);

  wire and_1_out, and_2_out, and_3_out, and_4_out, and_5_out;

  and and_1 (and_1_out, habilitacion, d4);
  D_A_E d_a_e_1 (.Es(Ess), .CK(pulsador), .pa1(and_1_out), .PA0(pa0), .Q(d4_2));  // open: minus_Q
  and and_2 (and_2_out, habilitacion, d3);
  D_A_E d_a_e_2 (.Es(d4_2), .CK(pulsador), .pa1(and_2_out), .PA0(pa0), .Q(d3_2));  // open: minus_Q
  and and_3 (and_3_out, habilitacion, d2);
  D_A_E d_a_e_3 (.Es(d3_2), .CK(pulsador), .pa1(and_3_out), .PA0(pa0), .Q(d2_2));  // open: minus_Q
  and and_4 (and_4_out, habilitacion, d1);
  D_A_E d_a_e_4 (.Es(d2_2), .CK(pulsador), .pa1(and_4_out), .PA0(pa0), .Q(d1_2));  // open: minus_Q
  and and_5 (and_5_out, habilitacion, d0);
  D_A_E d_a_e_5 (.Es(d1_2), .CK(pulsador), .pa1(and_5_out), .PA0(pa0), .Q(d0_2));  // open: minus_Q

  assign Ss = d0_2;
endmodule

// RD DAI
module Rd_DaI_serie_y_paralela_habilitacion_5 (
  input  b4,
  input  b3,
  input  b2,
  input  b1,
  input  b0,
  input  paso,
  input  Es,
  input  pulso,
  input  Pa0,
  output Ss,
  output b4_2,
  output b3_2,
  output b2_2,
  output b1_2,
  output b0_2
);

  wire and_1_out, and_2_out, and_3_out, and_4_out, and_5_out;

  and and_1 (and_1_out, paso, b4);
  D_Flip_Flop d_ff_1 (.clk(pulso), .D(b3_2), .Q(b4_2), .preset(and_1_out), .reset(Pa0));  // open: Qn, en
  and and_2 (and_2_out, paso, b3);
  and and_3 (and_3_out, paso, b2);
  D_Flip_Flop d_ff_2 (.clk(pulso), .D(b2_2), .Q(b3_2), .preset(and_2_out), .reset(Pa0));  // open: Qn, en
  and and_4 (and_4_out, paso, b1);
  D_Flip_Flop d_ff_3 (.clk(pulso), .D(b1_2), .Q(b2_2), .preset(and_3_out), .reset(Pa0));  // open: Qn, en
  and and_5 (and_5_out, paso, b0);
  D_Flip_Flop d_ff_4 (.clk(pulso), .D(b0_2), .Q(b1_2), .preset(and_4_out), .reset(Pa0));  // open: Qn, en
  D_Flip_Flop d_ff_5 (.clk(pulso), .D(Es), .Q(b0_2), .preset(and_5_out), .reset(Pa0));  // open: Qn, en

  assign Ss = b4_2;
endmodule

module division (
  input  ac,
  input  dd4,
  input  dd3,
  input  dd2,
  input  dd1,
  input  dd0,
  input  d4,
  input  d3,
  input  d2,
  input  d1,
  input  d0,
  input  in_12,
  input  in_13,
  input  condicion,
  input  ck,
  output s6,
  output s5,
  output s4,
  output s3,
  output s2,
  output s1,
  output Sfloat,
  output out_23,
  output ERR
);

  wire _1, _2, acarr, and_5_out, and_6_out, and_7_out, and_13_out, and_14_out, cnt, cond,
       contador_0_15_1__2_0, contador_0_15_1__2_1, contador_0_15_1__2_2, contador_0_15_1__2_3,
       contador_0_15_2__2_0, contador_0_15_2__2_1, contador_ampliado_63_1__2_6, d0_t, d1_t, d2_t, d3_t, d4_t,
       dd0_t, dd1_t, dd2_t, dd3_t, dd4_t, igual, off, on, or_1_out, or_2_out, or_3_out, or_5_out, or_6_out,
       or_7_out, pa0, paso, s_r_ff_2_q, s_r_ff_3_q, s_r_ff_5_q, Ss, Sumar, tunnel, tunnel_t_t, tunnel_t_t_t,
       tunnel_t_t_t_t, ultimo_pulso, x_multi_5bits_1_b0_2, x_multi_5bits_1_b1_2, x_multi_5bits_1_b2_2,
       x_multi_5bits_1_b3_2, x_multi_5bits_1_b4_2;
  wire [4:0] not_1_out, rd_dai_serie_y_paralela_habilitacion_5_1_b0_2, y_paso_2_b0_2, y_paso_3_b0_2,
       y_paso_4_b0_2;

  and and_1 (tunnel_t_t, condicion, in_12);
  and and_2 (tunnel, in_13, condicion);
  contador_0_15 contador_0_15_1 (
    .Ck(ck), .On(on), .estatus_contador(Sumar), .Off(pa0), ._2_0(contador_0_15_1__2_0),
    ._2_1(contador_0_15_1__2_1), ._2_2(contador_0_15_1__2_2), ._2_3(contador_0_15_1__2_3));  // open: _2
  and and_3 (_1, ~contador_0_15_1__2_3, ~contador_0_15_1__2_2, ~contador_0_15_1__2_1, contador_0_15_1__2_0);  // AND_Gate
  and and_4 (_2, ~contador_0_15_1__2_3, ~contador_0_15_1__2_2, contador_0_15_1__2_1, ~contador_0_15_1__2_0);  // AND_Gate
  and and_5 (and_5_out, ~contador_0_15_1__2_3, contador_0_15_1__2_2, ~contador_0_15_1__2_1, ~contador_0_15_1__2_0);  // AND_Gate
  and and_6 (and_6_out, ~contador_0_15_1__2_3, contador_0_15_1__2_2, contador_0_15_1__2_1, ~contador_0_15_1__2_0);  // AND_Gate
  and and_7 (and_7_out, contador_0_15_1__2_3, ~contador_0_15_1__2_2, ~contador_0_15_1__2_1, ~contador_0_15_1__2_0);  // AND_Gate
  and and_8 (ultimo_pulso, contador_0_15_1__2_3, ~contador_0_15_1__2_2, contador_0_15_1__2_1, ~contador_0_15_1__2_0);  // AND_Gate
  and and_9 (pa0, contador_0_15_1__2_3, ~contador_0_15_1__2_2, contador_0_15_1__2_1, contador_0_15_1__2_0);  // AND_Gate
  S_R_Flip_Flop s_r_ff_1 (.Q(tunnel_t_t_t), .preset(tunnel_t_t), .reset(or_1_out));  // open: S, clk, R, Qn, en
  or or_1 (or_1_out, ac, off);
  S_R_Flip_Flop s_r_ff_2 (.Q(s_r_ff_2_q), .preset(pa0), .reset(or_2_out));  // open: S, clk, R, Qn, en
  or or_2 (or_2_out, ac, off);
  ExactlyOne xor_1 (.out(cnt), .in0(_2), .in1(and_5_out), .in2(and_6_out), .in3(and_7_out), .in4(ultimo_pulso));
  or or_3 (or_3_out, _1, ac);
  or or_4 (cond, tunnel_t_t_t, s_r_ff_2_q);
  Rd_DaI_serie_y_paralela_habilitacion_5 rd_dai_serie_y_paralela_habilitacion_5_1 (
    .paso(tunnel), .pulso(cnt), .Pa0(or_3_out), .b4(dd4), .b3(dd3), .b2(dd2), .b1(dd1), .b0(dd0),
    .b4_2(rd_dai_serie_y_paralela_habilitacion_5_1_b0_2[4]),
    .b3_2(rd_dai_serie_y_paralela_habilitacion_5_1_b0_2[3]),
    .b2_2(rd_dai_serie_y_paralela_habilitacion_5_1_b0_2[2]),
    .b1_2(rd_dai_serie_y_paralela_habilitacion_5_1_b0_2[1]),
    .b0_2(rd_dai_serie_y_paralela_habilitacion_5_1_b0_2[0]), .Es(Ss));  // open: Ss
  y_paso y_paso_1 (
    .b0(rd_dai_serie_y_paralela_habilitacion_5_1_b0_2[0]),
    .b1(rd_dai_serie_y_paralela_habilitacion_5_1_b0_2[1]),
    .b2(rd_dai_serie_y_paralela_habilitacion_5_1_b0_2[2]),
    .b3(rd_dai_serie_y_paralela_habilitacion_5_1_b0_2[3]),
    .b4(rd_dai_serie_y_paralela_habilitacion_5_1_b0_2[4]), .habiltacion(cond), .b0_2(dd0_t), .b1_2(dd1_t),
    .b2_2(dd2_t), .b3_2(dd3_t), .b4_2(dd4_t));
  contador_ampliado_63 contador_ampliado_63_1 (
    .Ck(ck), ._2(_2), .On(_1), .Off(ac), ._2_0(s1), ._2_1(s2), ._2_2(s3), ._2_3(s4), ._2_4(s5), ._2_5(s6),
    ._2_6(contador_ampliado_63_1__2_6));  // open: estatus_contador
  assign not_1_out = ~{d4, d3, d2, d1, d0};  // NOT_Gate not_1, 5 bits wide
  Comparator #(.width(5), .mode("unsigned")) comparator_1 (
    .a({dd4_t, dd3_t, dd2_t, dd1_t, dd0_t}), .b(y_paso_2_b0_2), .gt(tunnel_t_t_t_t), .eq(igual), .lt(out_23));
  S_R_Flip_Flop s_r_ff_3 (.Q(s_r_ff_3_q), .preset(acarr), .reset(on));  // open: S, clk, R, Qn, en
  S_R_Flip_Flop s_r_ff_4 (.Q(ERR), .preset(contador_ampliado_63_1__2_6), .reset(ac));  // open: S, clk, R, Qn, en
  RD_E_S_serie_y_paralela_correcto rd_e_s_serie_y_paralela_correcto_1 (
    .habilitacion(tunnel_t_t), .pa0(ac), .d4(not_1_out[4]), .d3(not_1_out[3]), .d2(not_1_out[2]),
    .d1(not_1_out[1]), .d0(not_1_out[0]), .d4_2(d4_t), .d3_2(d3_t), .d2_2(d2_t), .d1_2(d1_t), .d0_2(d0_t));  // open: Ess, pulsador, Ss
  contador_0_15 contador_0_15_2 (
    .Ck(ck), .On(s_r_ff_3_q), .Off(on), ._2_0(contador_0_15_2__2_0), ._2_1(contador_0_15_2__2_1));  // open: _2, estatus_contador, _2_2, _2_3
  y_paso y_paso_2 (
    .b0(d0), .b1(d1), .b2(d2), .b3(d3), .b4(d4), .habiltacion(cond), .b0_2(y_paso_2_b0_2[0]),
    .b1_2(y_paso_2_b0_2[1]), .b2_2(y_paso_2_b0_2[2]), .b3_2(y_paso_2_b0_2[3]), .b4_2(y_paso_2_b0_2[4]));
  and and_10 (paso, ~contador_0_15_2__2_1, contador_0_15_2__2_0);  // AND_Gate
  and and_11 (off, contador_0_15_2__2_1, ~contador_0_15_2__2_0);  // AND_Gate
  and and_12 (on, contador_0_15_2__2_1, contador_0_15_2__2_0);
  S_R_Flip_Flop s_r_ff_5 (.Q(s_r_ff_5_q), .preset(or_6_out), .reset(or_5_out));  // open: S, clk, R, Qn, en
  or or_5 (or_5_out, ac, off);
  or or_6 (or_6_out, tunnel_t_t_t_t, and_13_out);
  and and_13 (and_13_out, igual, cond);
  y_paso y_paso_3 (
    .b0(dd0_t), .b1(dd1_t), .b2(dd2_t), .b3(dd3_t), .b4(dd4_t), .habiltacion(s_r_ff_5_q),
    .b0_2(y_paso_3_b0_2[0]), .b1_2(y_paso_3_b0_2[1]), .b2_2(y_paso_3_b0_2[2]), .b3_2(y_paso_3_b0_2[3]),
    .b4_2(y_paso_3_b0_2[4]));
  X_multi_5bits x_multi_5bits_1 (
    .a4(y_paso_3_b0_2[4]), .a3(y_paso_3_b0_2[3]), .a2(y_paso_3_b0_2[2]), .a1(y_paso_3_b0_2[1]),
    .a0(y_paso_3_b0_2[0]), .b4(y_paso_4_b0_2[4]), .b3(y_paso_4_b0_2[3]), .b2(y_paso_4_b0_2[2]),
    .b1(y_paso_4_b0_2[1]), .b0(y_paso_4_b0_2[0]), .acarreo_0(and_14_out), .acarreo(acarr),
    .b4_2(x_multi_5bits_1_b4_2), .b3_2(x_multi_5bits_1_b3_2), .b2_2(x_multi_5bits_1_b2_2),
    .b1_2(x_multi_5bits_1_b1_2), .b0_2(x_multi_5bits_1_b0_2));
  or or_7 (or_7_out, pa0, ac);
  y_paso y_paso_4 (
    .b0(d0_t), .b1(d1_t), .b2(d2_t), .b3(d3_t), .b4(d4_t), .habiltacion(s_r_ff_5_q), .b0_2(y_paso_4_b0_2[0]),
    .b1_2(y_paso_4_b0_2[1]), .b2_2(y_paso_4_b0_2[2]), .b3_2(y_paso_4_b0_2[3]), .b4_2(y_paso_4_b0_2[4]));
  and and_14 (and_14_out, s_r_ff_5_q, 1'b1);
  Rd_DaI_serie_y_paralela_habilitacion_5 rd_dai_serie_y_paralela_habilitacion_5_2 (
    .paso(paso), .Ss(Ss), .pulso(cnt), .Pa0(or_7_out), .b4(x_multi_5bits_1_b4_2), .b3(x_multi_5bits_1_b3_2),
    .b2(x_multi_5bits_1_b2_2), .b1(x_multi_5bits_1_b1_2), .b0(x_multi_5bits_1_b0_2), .Es(1'b0));  // open: b4_2, b3_2, b2_2, b1_2, b0_2
  X_multi_5bits x_multi_5bits_2 (
    .a4(dd3_t), .a3(dd2_t), .a2(dd1_t), .a1(dd0_t), .a0(1'b0), .b4(d4_t), .b3(d3_t), .b2(d2_t), .b1(d1_t),
    .b0(d0_t), .acarreo_0(1'b1), .acarreo(Sfloat));  // open: b4_2, b3_2, b2_2, b1_2, b0_2

  // Other names for the same wires on the sheet: float = Sfloat; tunnel_t = out_23

  // Notes on the sheet:
  //   dividendo
  //   divisor
  //   OPERACION FLOTANTE
endmodule

module divisor_logisim (
  input  [4:0] in_1,
  input  [4:0] in_2,
  input  [4:0] in_3,
  input  [4:0] in_4,
  output [4:0] out_5,
  output [4:0] out_6,
  output [4:0] out_7,
  output [4:0] out_8
);

  Divider #(.width(5)) divider_1 (.a(in_2), .b(in_3), .out(out_5), .upper(in_1), .rem(out_6));
  Divider #(.width(5)) divider_2 (.a(out_6), .b(in_3), .out(out_7), .upper(in_4), .rem(out_8));
endmodule

module Rd_divisor_No_q (
  input  b4,
  input  b3,
  input  b2,
  input  b1,
  input  b0,
  input  paso,
  input  Es,
  input  pulso,
  input  Pa0,
  output Ss,
  output b4_2,
  output b3_2,
  output b2_2,
  output b1_2,
  output b0_2
);

  wire and_1_out, and_2_out, and_3_out, and_4_out, and_5_out;

  and and_1 (and_1_out, paso, b4);
  D_Flip_Flop d_ff_1 (.clk(pulso), .D(b3_2), .Qn(b4_2), .preset(and_1_out), .reset(Pa0));  // open: Q, en
  and and_2 (and_2_out, paso, b3);
  and and_3 (and_3_out, paso, b2);
  D_Flip_Flop d_ff_2 (.clk(pulso), .D(b2_2), .Qn(b3_2), .preset(and_2_out), .reset(Pa0));  // open: Q, en
  and and_4 (and_4_out, paso, b1);
  D_Flip_Flop d_ff_3 (.clk(pulso), .D(b1_2), .Qn(b2_2), .preset(and_3_out), .reset(Pa0));  // open: Q, en
  and and_5 (and_5_out, paso, b0);
  D_Flip_Flop d_ff_4 (.clk(pulso), .D(b0_2), .Qn(b1_2), .preset(and_4_out), .reset(Pa0));  // open: Q, en
  D_Flip_Flop d_ff_5 (.clk(pulso), .D(Es), .Qn(b0_2), .preset(and_5_out), .reset(Pa0));  // open: Q, en

  assign Ss = b4_2;
endmodule

module RD_der_izq_prototipo (
  input  S,
  input  Esi,
  input  a0,
  input  a1,
  input  a2,
  input  a3,
  input  S1,
  input  S0,
  input  in_9,
  input  Esd,
  output Ssd,
  output Ssi,
  output out_13,
  output S3,
  output S2,
  output S1_2,
  output S0_2,
  output S0_3,
  output S0_4,
  output S3_2,
  output S2_2,
  output S1_3,
  output S0_5,
  output S0_6,
  output S0_7,
  output Ssd_2
);

  wire and_1_out, and_2_out, and_3_out, and_4_out, and_5_out, and_6_out, and_7_out, and_8_out, and_9_out,
       and_10_out, and_11_out, and_12_out, and_13_out, and_14_out, and_15_out, and_16_out, and_17_out,
       and_18_out, and_19_out, and_20_out, and_21_out, and_22_out, and_23_out, and_24_out, and_25_out,
       and_26_out, and_27_out, and_28_out, clock_1_out, or_1_out, or_2_out, or_3_out, or_4_out, or_5_out,
       or_6_out, or_7_out, or_8_out, or_9_out, or_10_out, or_11_out, or_12_out;
  wire [1:0] counter_1_q;

  and and_1 (and_1_out, Esi, S);
  and and_2 (and_2_out, ~S, S2);  // AND_Gate
  or or_1 (or_1_out, and_1_out, and_2_out);
  and and_3 (and_3_out, S3, S);
  or or_2 (or_2_out, and_3_out, and_4_out);
  D_Flip_Flop d_ff_1 (.clk(clock_1_out), .D(or_1_out), .Q(S3), .reset(in_9));  // open: Qn, preset, en
  and and_4 (and_4_out, ~S, S1_2);  // AND_Gate
  D_Flip_Flop d_ff_2 (.clk(clock_1_out), .D(or_2_out), .Q(S2), .reset(in_9));  // open: Qn, preset, en
  and and_5 (and_5_out, S2, S);
  and and_6 (and_6_out, ~S, S0_2);  // AND_Gate
  or or_3 (or_3_out, and_5_out, and_6_out);
  and and_7 (and_7_out, S1_2, S);
  or or_4 (or_4_out, and_7_out, and_8_out);
  D_Flip_Flop d_ff_3 (.clk(clock_1_out), .D(or_3_out), .Q(S1_2), .reset(in_9));  // open: Qn, preset, en
  and and_8 (and_8_out, ~S, S0_3);  // AND_Gate
  D_Flip_Flop d_ff_4 (.clk(clock_1_out), .D(or_4_out), .Q(S0_2), .reset(in_9));  // open: Qn, preset, en
  and and_9 (and_9_out, ~S, S0_4);  // AND_Gate
  and and_10 (and_10_out, S0_2, S);
  or or_5 (or_5_out, and_10_out, and_9_out);
  D_Flip_Flop d_ff_5 (.clk(clock_1_out), .D(or_5_out), .Q(S0_3), .reset(in_9));  // open: Qn, preset, en
  and and_11 (and_11_out, S0_3, S);
  and and_12 (and_12_out, ~S, S3_2);  // AND_Gate
  or or_6 (or_6_out, and_11_out, and_12_out);
  D_Flip_Flop d_ff_6 (.clk(clock_1_out), .D(or_6_out), .Q(S0_4), .reset(in_9));  // open: Qn, preset, en
  and and_13 (and_13_out, S0_4, S);
  and and_14 (and_14_out, ~S, S2_2);  // AND_Gate
  or or_7 (or_7_out, and_13_out, and_14_out);
  and and_15 (and_15_out, S3_2, S);
  D_Flip_Flop d_ff_7 (.clk(clock_1_out), .D(or_7_out), .Q(S3_2), .reset(in_9));  // open: Qn, preset, en
  and and_16 (and_16_out, ~S, S1_3);  // AND_Gate
  or or_8 (or_8_out, and_15_out, and_16_out);
  D_Flip_Flop d_ff_8 (.clk(clock_1_out), .D(or_8_out), .Q(S2_2), .reset(in_9));  // open: Qn, preset, en
  and and_17 (and_17_out, ~S, S0_5);  // AND_Gate
  and and_18 (and_18_out, S2_2, S);
  or or_9 (or_9_out, and_18_out, and_17_out);
  and and_19 (and_19_out, S1_3, S);
  D_Flip_Flop d_ff_9 (.clk(clock_1_out), .D(or_9_out), .Q(S1_3), .reset(in_9));  // open: Qn, preset, en
  and and_20 (and_20_out, ~S, S0_6);  // AND_Gate
  or or_10 (or_10_out, and_19_out, and_20_out);
  D_Flip_Flop d_ff_10 (.clk(clock_1_out), .D(or_10_out), .Q(S0_5), .reset(in_9));  // open: Qn, preset, en
  and and_21 (and_21_out, S0_5, S);
  or or_11 (or_11_out, and_21_out, and_22_out);
  and and_22 (and_22_out, ~S, S0_7);  // AND_Gate
  D_Flip_Flop d_ff_11 (.clk(clock_1_out), .D(or_11_out), .Q(S0_6), .reset(in_9));  // open: Qn, preset, en
  and and_23 (and_23_out, S0_6, S);
  or or_12 (or_12_out, and_23_out, and_24_out);
  Clock clock_1 (.out(clock_1_out));
  and and_24 (and_24_out, ~S, out_13);  // AND_Gate
  D_Flip_Flop d_ff_12 (.clk(clock_1_out), .D(or_12_out), .Q(S0_7), .reset(in_9));  // open: Qn, preset, en
  Counter #(.width(2), .max('h3)) counter_1 (.Q(counter_1_q), .clk(clock_1_out));  // open: load, D, count, carry, clr
  and and_25 (and_25_out, ~counter_1_q[0], ~counter_1_q[1], a0);  // AND_Gate
  and and_26 (and_26_out, counter_1_q[0], ~counter_1_q[1], a1);  // AND_Gate
  and and_27 (and_27_out, ~counter_1_q[0], counter_1_q[1], a2);  // AND_Gate
  and and_28 (and_28_out, counter_1_q[0], counter_1_q[1], a3);
  or or_13 (out_13, and_25_out, and_26_out, and_27_out, and_28_out);

  assign Ssd = S0_7;
  assign Ssi = S3;
endmodule

module bien (
  input  in_1,
  input  dd4,
  input  dd3,
  input  dd2,
  input  dd1,
  input  dd0,
  input  d4,
  input  d3,
  input  d2,
  input  d1,
  input  d0,
  input  in_12,
  input  ac,
  output s4,
  output s3,
  output s2,
  output s1
);

  wire _1, _2, acarr, and_3_out, and_4_out, and_5_out, and_11_out, and_12_out, ck, cnt, cond,
       contador_0_15_1__2_0, contador_0_15_1__2_1, contador_0_15_1__2_2, contador_0_15_1__2_3,
       contador_0_15_3__2_0, contador_0_15_3__2_1, d0_t, d1_t, d2_t, d3_t, d4_t, dd0_t, dd1_t, dd2_t, dd3_t,
       dd4_t, igual, off, on, or_1_out, or_2_out, or_4_out, or_5_out, pa0, paso, s_r_ff_2_q, s_r_ff_3_q,
       s_r_ff_4_q, Ss, Sumar, tunnel_t, tunnel_t_t_t, tunnel_t_t_t_t, ultimo_pulso, x_multi_5bits_1_b0_2,
       x_multi_5bits_1_b1_2, x_multi_5bits_1_b2_2, x_multi_5bits_1_b3_2, x_multi_5bits_1_b4_2;
  wire [4:0] not_1_out, rd_dai_serie_y_paralela_habilitacion_5_1_b0_2, y_paso_2_b0_2, y_paso_3_b0_2,
       y_paso_4_b0_2;

  contador_0_15 contador_0_15_1 (
    .Ck(ck), .On(on), .estatus_contador(Sumar), .Off(pa0), ._2_0(contador_0_15_1__2_0),
    ._2_1(contador_0_15_1__2_1), ._2_2(contador_0_15_1__2_2), ._2_3(contador_0_15_1__2_3));  // open: _2
  S_R_Flip_Flop s_r_ff_1 (.Q(tunnel_t_t_t), .preset(in_12), .reset(or_1_out));  // open: S, clk, R, Qn, en
  or or_1 (or_1_out, ac, off);
  and and_1 (_1, ~contador_0_15_1__2_3, ~contador_0_15_1__2_2, ~contador_0_15_1__2_1, contador_0_15_1__2_0);  // AND_Gate
  and and_2 (_2, ~contador_0_15_1__2_3, ~contador_0_15_1__2_2, contador_0_15_1__2_1, ~contador_0_15_1__2_0);  // AND_Gate
  and and_3 (and_3_out, ~contador_0_15_1__2_3, contador_0_15_1__2_2, ~contador_0_15_1__2_1, ~contador_0_15_1__2_0);  // AND_Gate
  and and_4 (and_4_out, ~contador_0_15_1__2_3, contador_0_15_1__2_2, contador_0_15_1__2_1, ~contador_0_15_1__2_0);  // AND_Gate
  and and_5 (and_5_out, contador_0_15_1__2_3, ~contador_0_15_1__2_2, ~contador_0_15_1__2_1, ~contador_0_15_1__2_0);  // AND_Gate
  and and_6 (ultimo_pulso, contador_0_15_1__2_3, ~contador_0_15_1__2_2, contador_0_15_1__2_1, ~contador_0_15_1__2_0);  // AND_Gate
  and and_7 (pa0, contador_0_15_1__2_3, ~contador_0_15_1__2_2, contador_0_15_1__2_1, contador_0_15_1__2_0);  // AND_Gate
  S_R_Flip_Flop s_r_ff_2 (.Q(s_r_ff_2_q), .preset(pa0), .reset(off));  // open: S, clk, R, Qn, en
  ExactlyOne xor_1 (.out(cnt), .in0(_2), .in1(and_3_out), .in2(and_4_out), .in3(and_5_out), .in4(ultimo_pulso));
  or or_2 (or_2_out, _1, ac);
  or or_3 (cond, tunnel_t_t_t, s_r_ff_2_q);
  Rd_DaI_serie_y_paralela_habilitacion_5 rd_dai_serie_y_paralela_habilitacion_5_1 (
    .paso(in_1), .pulso(cnt), .Pa0(or_2_out), .b4(dd4), .b3(dd3), .b2(dd2), .b1(dd1), .b0(dd0),
    .b4_2(rd_dai_serie_y_paralela_habilitacion_5_1_b0_2[4]),
    .b3_2(rd_dai_serie_y_paralela_habilitacion_5_1_b0_2[3]),
    .b2_2(rd_dai_serie_y_paralela_habilitacion_5_1_b0_2[2]),
    .b1_2(rd_dai_serie_y_paralela_habilitacion_5_1_b0_2[1]),
    .b0_2(rd_dai_serie_y_paralela_habilitacion_5_1_b0_2[0]), .Es(Ss));  // open: Ss
  y_paso y_paso_1 (
    .b0(rd_dai_serie_y_paralela_habilitacion_5_1_b0_2[0]),
    .b1(rd_dai_serie_y_paralela_habilitacion_5_1_b0_2[1]),
    .b2(rd_dai_serie_y_paralela_habilitacion_5_1_b0_2[2]),
    .b3(rd_dai_serie_y_paralela_habilitacion_5_1_b0_2[3]),
    .b4(rd_dai_serie_y_paralela_habilitacion_5_1_b0_2[4]), .habiltacion(cond), .b0_2(dd0_t), .b1_2(dd1_t),
    .b2_2(dd2_t), .b3_2(dd3_t), .b4_2(dd4_t));
  contador_0_15 contador_0_15_2 (
    .Ck(ck), ._2(_2), .On(_1), .Off(ac), ._2_0(s1), ._2_1(s2), ._2_2(s3), ._2_3(s4));  // open: estatus_contador
  assign not_1_out = ~{d4, d3, d2, d1, d0};  // NOT_Gate not_1, 5 bits wide
  Comparator #(.width(5), .mode("unsigned")) comparator_1 (
    .a({dd4_t, dd3_t, dd2_t, dd1_t, dd0_t}), .b(y_paso_2_b0_2), .gt(tunnel_t_t_t_t), .eq(igual), .lt(tunnel_t));
  S_R_Flip_Flop s_r_ff_3 (.Q(s_r_ff_3_q), .preset(acarr), .reset(on));  // open: S, clk, R, Qn, en
  contador_0_15 contador_0_15_3 (
    .Ck(ck), .On(s_r_ff_3_q), .Off(on), ._2_0(contador_0_15_3__2_0), ._2_1(contador_0_15_3__2_1));  // open: _2, estatus_contador, _2_2, _2_3
  RD_E_S_serie_y_paralela_correcto rd_e_s_serie_y_paralela_correcto_1 (
    .habilitacion(in_12), .pa0(ac), .d4(not_1_out[4]), .d3(not_1_out[3]), .d2(not_1_out[2]),
    .d1(not_1_out[1]), .d0(not_1_out[0]), .d4_2(d4_t), .d3_2(d3_t), .d2_2(d2_t), .d1_2(d1_t), .d0_2(d0_t));  // open: Ess, pulsador, Ss
  Clock clock_1 (.out(ck));
  and and_8 (paso, ~contador_0_15_3__2_1, contador_0_15_3__2_0);  // AND_Gate
  and and_9 (off, contador_0_15_3__2_1, ~contador_0_15_3__2_0);  // AND_Gate
  and and_10 (on, contador_0_15_3__2_1, contador_0_15_3__2_0);
  y_paso y_paso_2 (
    .b0(d0), .b1(d1), .b2(d2), .b3(d3), .b4(d4), .habiltacion(cond), .b0_2(y_paso_2_b0_2[0]),
    .b1_2(y_paso_2_b0_2[1]), .b2_2(y_paso_2_b0_2[2]), .b3_2(y_paso_2_b0_2[3]), .b4_2(y_paso_2_b0_2[4]));
  S_R_Flip_Flop s_r_ff_4 (.Q(s_r_ff_4_q), .preset(or_4_out), .reset(off));  // open: S, clk, R, Qn, en
  or or_4 (or_4_out, tunnel_t_t_t_t, and_11_out);
  and and_11 (and_11_out, igual, cond);
  y_paso y_paso_3 (
    .b0(dd0_t), .b1(dd1_t), .b2(dd2_t), .b3(dd3_t), .b4(dd4_t), .habiltacion(s_r_ff_4_q),
    .b0_2(y_paso_3_b0_2[0]), .b1_2(y_paso_3_b0_2[1]), .b2_2(y_paso_3_b0_2[2]), .b3_2(y_paso_3_b0_2[3]),
    .b4_2(y_paso_3_b0_2[4]));
  X_multi_5bits x_multi_5bits_1 (
    .a4(y_paso_3_b0_2[4]), .a3(y_paso_3_b0_2[3]), .a2(y_paso_3_b0_2[2]), .a1(y_paso_3_b0_2[1]),
    .a0(y_paso_3_b0_2[0]), .b4(y_paso_4_b0_2[4]), .b3(y_paso_4_b0_2[3]), .b2(y_paso_4_b0_2[2]),
    .b1(y_paso_4_b0_2[1]), .b0(y_paso_4_b0_2[0]), .acarreo_0(and_12_out), .acarreo(acarr),
    .b4_2(x_multi_5bits_1_b4_2), .b3_2(x_multi_5bits_1_b3_2), .b2_2(x_multi_5bits_1_b2_2),
    .b1_2(x_multi_5bits_1_b1_2), .b0_2(x_multi_5bits_1_b0_2));
  or or_5 (or_5_out, pa0, ac);
  y_paso y_paso_4 (
    .b0(d0_t), .b1(d1_t), .b2(d2_t), .b3(d3_t), .b4(d4_t), .habiltacion(s_r_ff_4_q), .b0_2(y_paso_4_b0_2[0]),
    .b1_2(y_paso_4_b0_2[1]), .b2_2(y_paso_4_b0_2[2]), .b3_2(y_paso_4_b0_2[3]), .b4_2(y_paso_4_b0_2[4]));
  and and_12 (and_12_out, s_r_ff_4_q, 1'b1);
  Rd_DaI_serie_y_paralela_habilitacion_5 rd_dai_serie_y_paralela_habilitacion_5_2 (
    .paso(paso), .Ss(Ss), .pulso(cnt), .Pa0(or_5_out), .b4(x_multi_5bits_1_b4_2), .b3(x_multi_5bits_1_b3_2),
    .b2(x_multi_5bits_1_b2_2), .b1(x_multi_5bits_1_b1_2), .b0(x_multi_5bits_1_b0_2), .Es(1'b0));  // open: b4_2, b3_2, b2_2, b1_2, b0_2

  // Other names for the same wires on the sheet: tunnel = in_1; tunnel_t_t = in_12

  // Notes on the sheet:
  //   dividendo
  //   Resultado
  //   divisor
endmodule
