// Logisim project contadores.circ as structural Verilog: 12 circuits, main circuit contador johnson D
module contador_johnson_D (
  input  pa0,
  input  e,
  input  pa0_2,
  output out_4,
  output out_5,
  output out_6,
  output out_7,
  output out_8,
  output out_9,
  output out_10,
  output out_11
);

  wire and_1_out, and_2_out, and_3_out, and_4_out, and_5_out, and_6_out, and_7_out, and_8_out, clock_1_out,
       clock_2_out, d_ff_5_qn, or_1_out, or_2_out, or_3_out, or_4_out;

  Clock clock_1 (.out(clock_1_out));
  Clock clock_2 (.out(clock_2_out));
  and and_1 (and_1_out, ~out_8, e);  // AND_Gate
  and and_2 (and_2_out, ~e, out_10);  // AND_Gate
  D_Flip_Flop d_ff_1 (.clk(clock_1_out), .D(d_ff_5_qn), .Q(out_7), .reset(pa0));  // open: Qn, preset, en
  or or_1 (or_1_out, and_1_out, and_2_out);
  D_Flip_Flop d_ff_2 (.clk(clock_1_out), .D(out_7), .Q(out_6), .reset(pa0));  // open: Qn, preset, en
  D_Flip_Flop d_ff_3 (.clk(clock_2_out), .D(or_1_out), .Q(out_11), .reset(pa0_2));  // open: Qn, preset, en
  D_Flip_Flop d_ff_4 (.clk(clock_1_out), .D(out_6), .Q(out_5), .reset(pa0));  // open: Qn, preset, en
  and and_3 (and_3_out, out_11, e);
  or or_2 (or_2_out, and_3_out, and_4_out);
  and and_4 (and_4_out, ~e, out_9);  // AND_Gate
  D_Flip_Flop d_ff_5 (.clk(clock_1_out), .D(out_5), .Q(out_4), .Qn(d_ff_5_qn), .reset(pa0));  // open: preset, en
  D_Flip_Flop d_ff_6 (.clk(clock_2_out), .D(or_2_out), .Q(out_10), .reset(pa0_2));  // open: Qn, preset, en
  and and_5 (and_5_out, out_10, e);
  or or_3 (or_3_out, and_5_out, and_6_out);
  and and_6 (and_6_out, ~e, out_8);  // AND_Gate
  D_Flip_Flop d_ff_7 (.clk(clock_2_out), .D(or_3_out), .Q(out_9), .reset(pa0_2));  // open: Qn, preset, en
  and and_7 (and_7_out, out_9, e);
  or or_4 (or_4_out, and_7_out, and_8_out);
  and and_8 (and_8_out, ~e, ~out_11);  // AND_Gate
  D_Flip_Flop d_ff_8 (.clk(clock_2_out), .D(or_4_out), .Q(out_8), .reset(pa0_2));  // open: Qn, preset, en
endmodule

module intento_cnt_binario_D (
  input  D,
  input  A,
  input  pa0,
  output out_4,
  output out_5,
  output out_6,
  output out_7
);

  wire and_1_out, and_2_out, and_3_out, and_4_out, and_5_out, and_6_out, and_7_out, and_8_out, and_9_out,
       and_10_out, and_11_out, and_12_out, and_13_out, and_14_out, and_15_out, and_16_out, and_17_out,
       and_18_out, and_19_out, and_20_out, and_21_out, and_22_out, and_23_out, and_24_out, clock_1_out,
       d_ff_1_qn, or_1_out, or_2_out, or_3_out, or_4_out, or_5_out, xor_1_out, xor_2_out, xor_3_out,
       xor_4_out, xor_5_out;

  and and_1 (and_1_out, d_ff_1_qn, D);
  and and_2 (and_2_out, A, d_ff_1_qn);
  xor xor_1 (xor_1_out, and_2_out, and_1_out);
  Clock clock_1 (.out(clock_1_out));
  D_Flip_Flop d_ff_1 (.clk(clock_1_out), .D(xor_1_out), .Q(out_7), .Qn(d_ff_1_qn), .reset(pa0));  // open: preset, en
  xor xor_2 (xor_2_out, out_7, out_6);
  and and_3 (and_3_out, ~out_6, d_ff_1_qn);  // AND_Gate
  and and_4 (and_4_out, ~d_ff_1_qn, out_6);  // AND_Gate
  and and_5 (and_5_out, xor_2_out, A);
  and and_6 (and_6_out, or_1_out, D);
  or or_1 (or_1_out, and_3_out, and_4_out);
  xor xor_3 (xor_3_out, and_5_out, and_6_out);
  D_Flip_Flop d_ff_2 (.clk(clock_1_out), .D(xor_3_out), .Q(out_6), .reset(pa0));  // open: Qn, preset, en
  and and_7 (and_7_out, ~out_5, out_6, out_7);  // AND_Gate
  and and_8 (and_8_out, ~out_6, out_5);  // AND_Gate
  and and_9 (and_9_out, ~out_7, out_5);  // AND_Gate
  and and_10 (and_10_out, ~out_5, ~out_7, ~out_6);  // AND_Gate
  and and_11 (and_11_out, out_5, out_7);
  and and_12 (and_12_out, out_5, out_6);
  or or_2 (or_2_out, and_7_out, and_8_out, and_9_out);
  and and_13 (and_13_out, or_2_out, A);
  and and_14 (and_14_out, D, or_3_out);
  or or_3 (or_3_out, and_10_out, and_11_out, and_12_out);
  xor xor_4 (xor_4_out, and_14_out, and_13_out);
  D_Flip_Flop d_ff_3 (.clk(clock_1_out), .D(xor_4_out), .Q(out_5), .reset(pa0));  // open: Qn, preset, en
  and and_15 (and_15_out, ~out_5, out_4);  // AND_Gate
  and and_16 (and_16_out, ~out_6, out_4);  // AND_Gate
  and and_17 (and_17_out, ~out_7, out_4, out_6);  // AND_Gate
  and and_18 (and_18_out, ~out_4, and_10_out);  // AND_Gate
  buf and_19 (and_19_out, out_4);  // AND_Gate
  buf and_20 (and_20_out, out_4);  // AND_Gate
  buf and_21 (and_21_out, out_4);  // AND_Gate
  and and_22 (and_22_out, ~out_4, out_5, out_6, out_7);  // AND_Gate
  or or_4 (or_4_out, and_15_out, and_16_out, and_17_out, and_22_out);
  or or_5 (or_5_out, and_18_out, and_19_out, and_20_out, and_21_out);
  and and_23 (and_23_out, or_4_out, A);
  and and_24 (and_24_out, D, or_5_out);
  xor xor_5 (xor_5_out, and_23_out, and_24_out);
  D_Flip_Flop d_ff_4 (.clk(clock_1_out), .D(xor_5_out), .Q(out_4), .reset(pa0));  // open: Qn, preset, en
endmodule

// cnt
module cnt_modulo_maximo (
  input  cnt,
  input  D,
  input  A,
  input  pa0,
  output s4,
  output s3,
  output s2,
  output s1,
  output s0
);

  wire and_1_out, and_2_out, and_3_out, and_4_out, and_5_out, and_6_out, and_7_out, and_8_out, and_9_out,
       and_10_out, or_1_out, or_2_out, or_3_out, or_4_out, or_5_out, t_ff_1_q, t_ff_1_qn, t_ff_2_q,
       t_ff_2_qn, t_ff_3_qn, t_ff_4_qn, xor_1_out;

  xor xor_1 (xor_1_out, A, D);
  and and_1 (and_1_out, A, xor_1_out);
  and and_2 (and_2_out, xor_1_out, D);
  or or_1 (or_1_out, and_1_out, and_2_out);
  T_Flip_Flop t_ff_1 (.clk(cnt), .T(or_1_out), .Q(t_ff_1_q), .Qn(t_ff_1_qn), .reset(pa0));  // open: preset, en
  and and_3 (and_3_out, and_1_out, t_ff_1_q);
  and and_4 (and_4_out, t_ff_1_qn, and_2_out);
  or or_2 (or_2_out, and_3_out, and_4_out);
  not not_1 (s0, t_ff_1_qn);
  not not_2 (s1, t_ff_2_qn);
  and and_5 (and_5_out, and_3_out, t_ff_2_q);
  T_Flip_Flop t_ff_2 (.clk(cnt), .T(or_2_out), .Q(t_ff_2_q), .Qn(t_ff_2_qn), .reset(pa0));  // open: preset, en
  and and_6 (and_6_out, t_ff_2_qn, and_4_out);
  or or_3 (or_3_out, and_5_out, and_6_out);
  T_Flip_Flop t_ff_3 (.clk(cnt), .T(or_3_out), .Q(s2), .Qn(t_ff_3_qn), .reset(pa0));  // open: preset, en
  and and_7 (and_7_out, and_5_out, s2);
  and and_8 (and_8_out, t_ff_3_qn, and_6_out);
  T_Flip_Flop t_ff_4 (.clk(cnt), .T(or_4_out), .Q(s3), .Qn(t_ff_4_qn), .reset(pa0));  // open: preset, en
  or or_4 (or_4_out, and_7_out, and_8_out);
  and and_9 (and_9_out, and_7_out, s3);
  or or_5 (or_5_out, and_9_out, and_10_out);
  and and_10 (and_10_out, t_ff_4_qn, and_8_out);
  T_Flip_Flop t_ff_5 (.clk(cnt), .T(or_5_out), .Q(s4), .reset(pa0));  // open: Qn, preset, en
endmodule

module gray (
  output out_1,
  output out_2,
  output out_3,
  output out_4
);

  wire and_1_out, and_2_out, and_3_out, and_4_out, and_5_out, and_6_out, and_7_out, and_8_out, and_9_out,
       and_10_out, and_11_out, and_12_out, and_13_out, clock_1_out, or_1_out, or_2_out, or_3_out, or_4_out;

  and and_1 (and_1_out, ~out_1, ~out_2, ~out_3);  // AND_Gate
  and and_2 (and_2_out, ~out_1, out_2, out_3);  // AND_Gate
  and and_3 (and_3_out, out_1, ~out_2, out_3);  // AND_Gate
  and and_4 (and_4_out, out_1, out_2, ~out_3);  // AND_Gate
  Clock clock_1 (.out(clock_1_out));
  or or_1 (or_1_out, and_1_out, and_2_out, and_3_out, and_4_out);
  D_Flip_Flop d_ff_1 (.clk(clock_1_out), .D(or_1_out), .Q(out_4));  // open: Qn, preset, en, reset
  and and_5 (and_5_out, ~out_4, out_3);  // AND_Gate
  and and_6 (and_6_out, ~out_2, ~out_1, out_4);  // AND_Gate
  and and_7 (and_7_out, out_2, out_1, out_4);
  or or_2 (or_2_out, and_5_out, and_6_out, and_7_out);
  D_Flip_Flop d_ff_2 (.clk(clock_1_out), .D(or_2_out), .Q(out_3));  // open: Qn, preset, en, reset
  and and_8 (and_8_out, ~out_3, out_2);  // AND_Gate
  and and_9 (and_9_out, out_2, out_4);
  and and_10 (and_10_out, ~out_1, ~out_4, out_3);  // AND_Gate
  or or_3 (or_3_out, and_8_out, and_9_out, and_10_out);
  D_Flip_Flop d_ff_3 (.clk(clock_1_out), .D(or_3_out), .Q(out_2));  // open: Qn, preset, en, reset
  and and_11 (and_11_out, out_1, out_3);
  and and_12 (and_12_out, out_1, out_4);
  and and_13 (and_13_out, ~out_3, ~out_4, out_2);  // AND_Gate
  D_Flip_Flop d_ff_4 (.clk(clock_1_out), .D(or_4_out), .Q(out_1));  // open: Qn, preset, en, reset
  or or_4 (or_4_out, and_11_out, and_12_out, and_13_out);
endmodule

module secuencia (
  output out_1,
  output out_2,
  output out_3
);

  wire and_1_out, and_2_out, and_3_out, and_4_out, and_5_out, and_6_out, and_7_out, and_8_out, and_9_out,
       and_10_out, and_11_out, and_12_out, clock_1_out, d1, d2, d3, d_ff_1_qn, not_1_out, not_2_out,
       or_1_out, or_2_out, or_3_out, or_4_out;

  Clock clock_1 (.out(clock_1_out));
  and and_1 (and_1_out, ~out_3, out_2);  // AND_Gate
  or or_1 (or_1_out, and_1_out, and_2_out);
  and and_2 (and_2_out, out_1, out_3);
  D_Flip_Flop d_ff_1 (.clk(clock_1_out), .D(or_1_out), .Q(out_3), .Qn(d_ff_1_qn));  // open: preset, en, reset
  and and_3 (and_3_out, out_1, out_2, out_3);
  and and_4 (and_4_out, ~out_1, ~out_2, out_3);  // AND_Gate
  and and_5 (and_5_out, ~out_1, out_2, ~out_3);  // AND_Gate
  and and_6 (and_6_out, out_1, ~out_2, ~out_3);  // AND_Gate
  or or_2 (or_2_out, and_3_out, and_4_out, and_5_out, and_6_out);
  D_Flip_Flop d_ff_2 (.clk(clock_1_out), .D(or_2_out), .Q(out_2));  // open: Qn, preset, en, reset
  D_Flip_Flop d_ff_3 (.clk(clock_1_out), .D(d_ff_1_qn), .Q(out_1));  // open: Qn, preset, en, reset
  // Probe on d3
  // Probe on d2
  // Probe on d1
  not not_1 (not_1_out, clock_1_out);
  and and_7 (and_7_out, ~d1, d2);  // AND_Gate
  and and_8 (and_8_out, d1, d3);
  or or_3 (or_3_out, and_7_out, and_8_out);
  and and_9 (and_9_out, d1, d2, d3);
  D_Flip_Flop d_ff_4 (.clk(not_1_out), .D(or_3_out), .Q(d1));  // open: Qn, preset, en, reset
  or or_4 (or_4_out, and_9_out, and_11_out, and_10_out, and_12_out);
  and and_10 (and_10_out, ~d1, d2, ~d3);  // AND_Gate
  and and_11 (and_11_out, ~d1, ~d2, d3);  // AND_Gate
  D_Flip_Flop d_ff_5 (.clk(not_1_out), .D(or_4_out), .Q(d2));  // open: Qn, preset, en, reset
  not not_2 (not_2_out, d1);
  and and_12 (and_12_out, d1, ~d2, ~d3);  // AND_Gate
  D_Flip_Flop d_ff_6 (.clk(not_1_out), .D(not_2_out), .Q(d3));  // open: Qn, preset, en, reset
endmodule

module registro_reversible (
  input  izq_der,
  input  esi,
  input  esd,
  input  pa0,
  input  pa1,
  output out_6,
  output out_7,
  output out_8,
  output out_9
);

  wire and_1_out, and_2_out, and_3_out, and_4_out, and_5_out, and_6_out, and_7_out, and_8_out, clock_1_out,
       or_1_out, or_2_out, or_3_out, or_4_out;

  and and_1 (and_1_out, esi, izq_der);
  Clock clock_1 (.out(clock_1_out));
  and and_2 (and_2_out, ~izq_der, out_7);  // AND_Gate
  or or_1 (or_1_out, and_1_out, and_2_out);
  D_Flip_Flop d_ff_1 (.clk(clock_1_out), .D(or_1_out), .Q(out_6), .preset(pa1), .reset(pa0));  // open: Qn, en
  and and_3 (and_3_out, out_6, izq_der);
  or or_2 (or_2_out, and_3_out, and_4_out);
  and and_4 (and_4_out, ~izq_der, out_8);  // AND_Gate
  and and_5 (and_5_out, out_7, izq_der);
  D_Flip_Flop d_ff_2 (.clk(clock_1_out), .D(or_2_out), .Q(out_7), .preset(pa1), .reset(pa0));  // open: Qn, en
  and and_6 (and_6_out, ~izq_der, out_9);  // AND_Gate
  or or_3 (or_3_out, and_5_out, and_6_out);
  D_Flip_Flop d_ff_3 (.clk(clock_1_out), .D(or_3_out), .Q(out_8), .preset(pa1), .reset(pa0));  // open: Qn, en
  and and_7 (and_7_out, out_8, izq_der);
  or or_4 (or_4_out, and_7_out, and_8_out);
  and and_8 (and_8_out, ~izq_der, esd);  // AND_Gate
  D_Flip_Flop d_ff_4 (.clk(clock_1_out), .D(or_4_out), .Q(out_9), .preset(pa1), .reset(pa0));  // open: Qn, en
endmodule

module ej30 (
  input  E
);

  wire and_1_out, and_2_out, and_3_out, and_4_out, and_5_out, and_6_out, and_7_out, and_8_out, and_9_out,
       and_10_out, and_11_out, clock_1_out, or_1_out, or_2_out, or_3_out, or_4_out, or_5_out, or_6_out, q1,
       q2, q3;

  and and_1 (and_1_out, q2, q3);
  or or_1 (or_1_out, and_1_out, and_2_out);
  and and_2 (and_2_out, ~q3, ~q2, ~q1);  // AND_Gate
  and and_3 (and_3_out, E, or_1_out);
  and and_4 (and_4_out, ~E, q1);  // AND_Gate
  Clock clock_1 (.out(clock_1_out));
  or or_2 (or_2_out, and_3_out, and_4_out);
  D_Flip_Flop d_ff_1 (.clk(clock_1_out), .D(or_2_out), .Q(q1));  // open: Qn, preset, en, reset
  and and_5 (and_5_out, ~q3, q1);  // AND_Gate
  or or_3 (or_3_out, and_5_out, and_6_out);
  and and_6 (and_6_out, ~q3, q2);  // AND_Gate
  // Probe on q2
  // Probe on q1
  // Probe on q3
  and and_7 (and_7_out, E, or_3_out);
  or or_4 (or_4_out, and_7_out, and_8_out);
  and and_8 (and_8_out, ~E, q2);  // AND_Gate
  D_Flip_Flop d_ff_2 (.clk(clock_1_out), .D(or_4_out), .Q(q2));  // open: Qn, preset, en, reset
  or or_5 (or_5_out, q2, and_9_out);
  and and_9 (and_9_out, q3, q1);
  and and_10 (and_10_out, E, or_5_out);
  or or_6 (or_6_out, and_10_out, and_11_out);
  and and_11 (and_11_out, ~E, q3);  // AND_Gate
  D_Flip_Flop d_ff_3 (.clk(clock_1_out), .D(or_6_out), .Q(q3));  // open: Qn, preset, en, reset
endmodule

module ej32 (
  input  in_1,
  output out_2
);

  wire and_1_out, and_2_out, and_3_out, clock_1_out, d_ff_1_q, d_ff_2_q, d_ff_3_q;

  Clock clock_1 (.out(clock_1_out));
  D_Flip_Flop d_ff_1 (.clk(clock_1_out), .D(in_1), .Q(d_ff_1_q), .reset(and_1_out));  // open: Qn, preset, en
  and and_1 (and_1_out, ~clock_1_out, and_3_out);  // AND_Gate
  // Probe on d_ff_2_q
  // Probe on d_ff_1_q
  // Probe on d_ff_3_q
  D_Flip_Flop d_ff_2 (.clk(clock_1_out), .D(d_ff_1_q), .Q(d_ff_2_q), .reset(and_1_out));  // open: Qn, preset, en
  and and_2 (and_2_out, d_ff_1_q, ~d_ff_2_q, d_ff_3_q);  // AND_Gate
  and and_3 (and_3_out, ~d_ff_1_q, d_ff_2_q, d_ff_3_q);  // AND_Gate
  or or_1 (out_2, and_2_out, and_3_out);
  D_Flip_Flop d_ff_3 (.clk(clock_1_out), .D(d_ff_2_q), .Q(d_ff_3_q), .reset(and_1_out));  // open: Qn, preset, en
endmodule

module ej_33_b (
  input  ck,
  input  in_2,
  input  in_3,
  output out_4,
  output out_5,
  output out_6,
  output out_7,
  output out_8
);

  wire and_como_nand_1_out_3, and_como_nand_2_out_3, and_como_nand_3_out_3, and_como_nand_4_out_3;

  T_Flip_Flop t_ff_1 (.clk(ck), .T(in_2), .Q(out_8), .reset(in_3));  // open: Qn, preset, en
  and_como_nand and_como_nand_1 (.in_1(in_2), .in_2(out_8), .out_3(and_como_nand_1_out_3));
  and_como_nand and_como_nand_2 (.in_1(and_como_nand_1_out_3), .in_2(out_7), .out_3(and_como_nand_2_out_3));
  T_Flip_Flop t_ff_2 (.clk(ck), .T(and_como_nand_1_out_3), .Q(out_7), .reset(in_3));  // open: Qn, preset, en
  T_Flip_Flop t_ff_3 (.clk(ck), .T(and_como_nand_2_out_3), .Q(out_6), .reset(in_3));  // open: Qn, preset, en
  and_como_nand and_como_nand_3 (.in_1(and_como_nand_2_out_3), .in_2(out_6), .out_3(and_como_nand_3_out_3));
  T_Flip_Flop t_ff_4 (.clk(ck), .T(and_como_nand_3_out_3), .Q(out_5), .reset(in_3));  // open: Qn, preset, en
  and_como_nand and_como_nand_4 (.in_1(and_como_nand_3_out_3), .in_2(out_5), .out_3(and_como_nand_4_out_3));
  T_Flip_Flop t_ff_5 (.clk(ck), .T(and_como_nand_4_out_3), .Q(out_4), .reset(in_3));  // open: Qn, preset, en
endmodule

module ej33b2 (
  input  in_1
);

  wire clock_1_out, d_ff_1_q, d_ff_2_q, d_ff_3_q, d_ff_4_q, ej_33_b_1_out_4, ej_33_b_1_out_5,
       ej_33_b_1_out_6, ej_33_b_1_out_7, ej_33_b_1_out_8, nand_1_out, nor_1_out, not_1_out, not_2_out,
       not_3_out;

  Clock clock_1 (.out(clock_1_out));
  D_Flip_Flop d_ff_1 (.clk(clock_1_out), .D(in_1), .Q(d_ff_1_q));  // open: Qn, preset, en, reset
  D_Flip_Flop d_ff_2 (.clk(clock_1_out), .D(d_ff_1_q), .Q(d_ff_2_q));  // open: Qn, preset, en, reset
  D_Flip_Flop d_ff_3 (.clk(clock_1_out), .D(d_ff_2_q), .Q(d_ff_3_q));  // open: Qn, preset, en, reset
  D_Flip_Flop d_ff_4 (.clk(clock_1_out), .D(d_ff_3_q), .Q(d_ff_4_q));  // open: Qn, preset, en, reset
  // Probe on not_3_out
  ej_33_b ej_33_b_1 (
    .ck(clock_1_out), .in_2(not_1_out), .in_3(d_ff_4_q), .out_4(ej_33_b_1_out_4), .out_5(ej_33_b_1_out_5),
    .out_6(ej_33_b_1_out_6), .out_7(ej_33_b_1_out_7), .out_8(ej_33_b_1_out_8));
  not not_1 (not_1_out, d_ff_4_q);
  nand nand_1 (nand_1_out, ej_33_b_1_out_5, ej_33_b_1_out_6, ej_33_b_1_out_7, ej_33_b_1_out_8);
  not not_2 (not_2_out, nand_1_out);
  nor nor_1 (nor_1_out, ej_33_b_1_out_4, not_2_out);
  not not_3 (not_3_out, nor_1_out);
endmodule

module semaforos (
);

  wire _0_out, _14_out, _15_out, _16_out, _27_out, _28_out, clock_1_out, cnt_modulo_maximo_1_s0,
       cnt_modulo_maximo_1_s1, cnt_modulo_maximo_1_s2, cnt_modulo_maximo_1_s3, cnt_modulo_maximo_1_s4,
       d_ff_1_q, d_ff_2_q, d_ff_3_q, d_ff_4_q, d_ff_5_q, d_ff_6_q, d_ff_7_q, d_ff_8_q, d_ff_9_q, not_1_out;

  Clock clock_1 (.out(clock_1_out));
  // Probe on cnt_modulo_maximo_1_s4
  // Probe on cnt_modulo_maximo_1_s3
  not not_1 (not_1_out, 1'b1);
  cnt_modulo_maximo cnt_modulo_maximo_1 (
    .cnt(clock_1_out), .pa0(_28_out), .D(not_1_out), .A(1'b1), .s4(cnt_modulo_maximo_1_s4),
    .s3(cnt_modulo_maximo_1_s3), .s2(cnt_modulo_maximo_1_s2), .s1(cnt_modulo_maximo_1_s1),
    .s0(cnt_modulo_maximo_1_s0));
  // Probe on cnt_modulo_maximo_1_s2
  // Probe on cnt_modulo_maximo_1_s0
  // Probe on cnt_modulo_maximo_1_s1
  and _0 (_0_out, ~cnt_modulo_maximo_1_s4, ~cnt_modulo_maximo_1_s3, ~cnt_modulo_maximo_1_s2, ~cnt_modulo_maximo_1_s1, ~cnt_modulo_maximo_1_s0);  // AND_Gate
  // AND_Gate _11 has open pins: in0=cnt_modulo_maximo_1_s4, in1=cnt_modulo_maximo_1_s3, in2=cnt_modulo_maximo_1_s2, in3=cnt_modulo_maximo_1_s1, in4=cnt_modulo_maximo_1_s0, out=open
  and _14 (_14_out, ~cnt_modulo_maximo_1_s4, cnt_modulo_maximo_1_s3, cnt_modulo_maximo_1_s2, cnt_modulo_maximo_1_s1, ~cnt_modulo_maximo_1_s0);  // AND_Gate
  and _15 (_15_out, ~cnt_modulo_maximo_1_s4, cnt_modulo_maximo_1_s3, cnt_modulo_maximo_1_s2, cnt_modulo_maximo_1_s1, cnt_modulo_maximo_1_s0);  // AND_Gate
  and _16 (_16_out, cnt_modulo_maximo_1_s4, ~cnt_modulo_maximo_1_s3, ~cnt_modulo_maximo_1_s2, ~cnt_modulo_maximo_1_s1, ~cnt_modulo_maximo_1_s0);  // AND_Gate
  and _27 (_27_out, cnt_modulo_maximo_1_s4, cnt_modulo_maximo_1_s3, ~cnt_modulo_maximo_1_s2, cnt_modulo_maximo_1_s1, cnt_modulo_maximo_1_s0);  // AND_Gate
  and _28 (_28_out, cnt_modulo_maximo_1_s4, cnt_modulo_maximo_1_s3, cnt_modulo_maximo_1_s2, ~cnt_modulo_maximo_1_s1, ~cnt_modulo_maximo_1_s0);  // AND_Gate
  D_Flip_Flop d_ff_1 (.Q(d_ff_1_q), .preset(_0_out), .reset(_15_out));  // open: clk, D, Qn, en
  LED led_1 (.in(d_ff_1_q));
  D_Flip_Flop d_ff_2 (.Q(d_ff_2_q), .preset(_15_out), .reset(_16_out));  // open: clk, D, Qn, en
  LED led_2 (.in(d_ff_3_q));
  D_Flip_Flop d_ff_3 (.Q(d_ff_3_q), .preset(_0_out), .reset(_14_out));  // open: clk, D, Qn, en
  LED led_3 (.in(d_ff_2_q));
  LED led_4 (.in(d_ff_4_q));
  D_Flip_Flop d_ff_4 (.Q(d_ff_4_q), .preset(_14_out), .reset(_15_out));  // open: clk, D, Qn, en
  LED led_5 (.in(d_ff_5_q));
  D_Flip_Flop d_ff_5 (.Q(d_ff_5_q), .preset(_16_out), .reset(_27_out));  // open: clk, D, Qn, en
  LED led_6 (.in(d_ff_6_q));
  D_Flip_Flop d_ff_6 (.Q(d_ff_6_q), .preset(_16_out), .reset(_28_out));  // open: clk, D, Qn, en
  LED led_7 (.in(d_ff_7_q));
  D_Flip_Flop d_ff_7 (.Q(d_ff_7_q), .preset(_15_out), .reset(_28_out));  // open: clk, D, Qn, en
  LED led_8 (.in(d_ff_8_q));
  D_Flip_Flop d_ff_8 (.Q(d_ff_8_q), .preset(_27_out), .reset(_28_out));  // open: clk, D, Qn, en
  D_Flip_Flop d_ff_9 (.Q(d_ff_9_q), .preset(_0_out), .reset(_16_out));  // open: clk, D, Qn, en
  LED led_9 (.in(d_ff_9_q));

  // Notes on the sheet:
  //   semaforo 1
  //   semaforo 2
  //   semaforo 3
endmodule

module and_como_nand (
  input  in_1,
  input  in_2,
  output out_3
);

  wire and_1_out, nand_1_out, nor_1_out, not_2_out, or_1_out;

  and and_1 (and_1_out, in_1, in_2);
  nand nand_1 (nand_1_out, in_1, in_2);
  // Probe on and_1_out
  // Probe on nand_1_out
  not not_1 (out_3, nand_1_out);
  // Probe on out_3
  // Probe on or_1_out
  or or_1 (or_1_out, in_1, in_2);
  // Probe on nor_1_out
  nor nor_1 (nor_1_out, in_1, in_2);
  not not_2 (not_2_out, nor_1_out);
  // Probe on not_2_out
endmodule
