// Logisim project ej de examen.circ as structural Verilog: 8 circuits, main circuit main
module main (
  input  in_1,
  input  in_2,
  input  in_3,
  input  in_4,
  input  in_5,
  input  in_6,
  output out_7,
  output out_8,
  output bA,
  output bB
);

  wire and_1_out, and_3_out, ck, mayor_e_igual_1_out_3, mayor_e_igual_1_out_4, mayor_e_igual_2_out_3,
       mayor_e_igual_2_out_4, mayor_e_igual_3_out_3, mayor_e_igual_3_out_4;

  mayor_e_igual mayor_e_igual_1 (.A(in_1), .B(in_4), .out_3(mayor_e_igual_1_out_3), .out_4(mayor_e_igual_1_out_4));
  // Probe on in_1
  mayor_e_igual mayor_e_igual_2 (.A(in_2), .B(in_5), .out_3(mayor_e_igual_2_out_3), .out_4(mayor_e_igual_2_out_4));
  or or_1 (out_7, mayor_e_igual_1_out_4, and_1_out, and_3_out);
  // Probe on in_4
  // Probe on in_2
  // Probe on in_3
  and and_1 (and_1_out, mayor_e_igual_1_out_3, mayor_e_igual_2_out_4);
  and and_2 (out_8, mayor_e_igual_1_out_3, mayor_e_igual_2_out_3, mayor_e_igual_3_out_3);
  // Probe on in_6
  // Probe on in_5
  mayor_e_igual mayor_e_igual_3 (.A(in_3), .B(in_6), .out_3(mayor_e_igual_3_out_3), .out_4(mayor_e_igual_3_out_4));
  and and_3 (and_3_out, mayor_e_igual_2_out_3, mayor_e_igual_3_out_4);
  Clock clock_1 (.out(ck));
  or or_2 (bA, out_7, out_8);
  and and_4 (bB, ~out_7, ~out_8);  // AND_Gate

  // Other names for the same wires on the sheet: a1 = in_3; a2 = in_2; a3 = in_1; b1 = in_6; b2 = in_5; b3 = in_4;
  //   tunnel = out_8; tunnel_t = out_7
endmodule

module mayor_e_igual (
  input  A,
  input  B,
  output out_3,
  output out_4
);

  wire and_1_out, and_2_out;

  and and_1 (and_1_out, A, B);
  and and_2 (and_2_out, ~B, ~A);  // AND_Gate
  and and_3 (out_4, ~B, A);  // AND_Gate
  or or_1 (out_3, and_1_out, and_2_out);
endmodule

module semisumadores (
  input  a,
  input  b,
  input  c,
  output out_4,
  output ac
);

  wire ac_2_out, ac_out, sum_out;

  xor sum (sum_out, a, b);
  and u_ac (ac_out, a, b);
  and ac_2 (ac_2_out, sum_out, c);
  or or_1 (ac, ac_2_out, ac_out);
  xor sum_2 (out_4, sum_out, c);
endmodule

module sumador (
  input  a,
  input  b,
  input  a_2,
  input  b_2,
  input  a_3,
  input  b_3,
  input  a_4,
  input  b_4,
  input  c,
  output s5,
  output s4,
  output s3,
  output s2,
  output s1
);

  wire semisumadores_1_ac, semisumadores_3_ac, semisumadores_4_ac;

  semisumadores semisumadores_1 (.a(a_2), .b(b_2), .c(semisumadores_3_ac), .ac(semisumadores_1_ac), .out_4(s3));
  semisumadores semisumadores_2 (.a(a), .b(b), .c(semisumadores_1_ac), .ac(s5), .out_4(s4));
  semisumadores semisumadores_3 (.a(a_3), .b(b_3), .c(semisumadores_4_ac), .ac(semisumadores_3_ac), .out_4(s2));
  semisumadores semisumadores_4 (.a(a_4), .b(b_4), .c(c), .ac(semisumadores_4_ac), .out_4(s1));
endmodule

module _3n_1 (
  input  s4,
  input  s3,
  input  s2,
  input  s1,
  output s6,
  output s5,
  output s4_2,
  output s3_2,
  output s2_2,
  output s1_2
);

  wire sumador_1_s5, sumador_2_s1, sumador_2_s2, sumador_2_s3, sumador_2_s4, sumador_2_s5;

  semisumadores semisumadores_1 (.a(sumador_1_s5), .b(sumador_2_s5), .c(1'b0), .ac(s6), .out_4(s5));
  sumador sumador_1 (
    .a(s4), .b(sumador_2_s4), .a_2(s3), .b_2(sumador_2_s3), .a_3(s2), .b_3(sumador_2_s2), .a_4(s1),
    .b_4(sumador_2_s1), .c(1'b0), .s5(sumador_1_s5), .s4(s4_2), .s3(s3_2), .s2(s2_2), .s1(s1_2));
  sumador sumador_2 (
    .a(s4), .b(s4), .a_2(s3), .b_2(s3), .a_3(s2), .b_3(s2), .a_4(s1), .b_4(s1), .c(1'b1), .s5(sumador_2_s5),
    .s4(sumador_2_s4), .s3(sumador_2_s3), .s2(sumador_2_s2), .s1(sumador_2_s1));
endmodule

module ej_3n_1 (
  input  s4,
  input  s3,
  input  s2,
  input  s1
);

  wire n3n_1_1_s1_2, n3n_1_1_s2_2, n3n_1_1_s3_2, n3n_1_1_s4_2, n3n_1_1_s5, n3n_1_1_s6;

  // Probe on n3n_1_1_s6
  _3n_1 u_3n_1_1 (
    .s4(s4), .s3(s3), .s2(s2), .s1(s1), .s6(n3n_1_1_s6), .s5(n3n_1_1_s5), .s4_2(n3n_1_1_s4_2),
    .s3_2(n3n_1_1_s3_2), .s2_2(n3n_1_1_s2_2), .s1_2(n3n_1_1_s1_2));
  // Probe on n3n_1_1_s3_2
  // Probe on n3n_1_1_s4_2
  // Probe on n3n_1_1_s2_2
  // Probe on n3n_1_1_s5
  // Probe on n3n_1_1_s1_2

  // Notes on the sheet:
  //   ej del 3n+1 sumadores 
endmodule

module robot_16x16 (
  input  f3,
  input  f2,
  input  f1,
  input  f0,
  input  c3,
  input  c2,
  input  c1,
  input  c0
);

  sumador sumador_1 ();  // open: a, b, a_2, b_2, a_3, b_3, a_4, b_4, c, s5, s4, s3, s2, s1
endmodule

module circuit (
  input  a,
  input  a_2,
  input  a_3,
  input  b,
  input  b_2,
  input  b_3,
  output barera_A,
  output barera_B
);

  wire and_1_out, and_2_out, and_3_out, and_4_out, and_5_out, mayor_e_igual_1_out_3, mayor_e_igual_1_out_4,
       mayor_e_igual_2_out_3, mayor_e_igual_2_out_4, mayor_e_igual_3_out_3, mayor_e_igual_3_out_4, or_1_out;

  mayor_e_igual mayor_e_igual_1 (.A(a), .B(b), .out_3(mayor_e_igual_1_out_3), .out_4(mayor_e_igual_1_out_4));
  mayor_e_igual mayor_e_igual_2 (.A(a_3), .B(b_3), .out_3(mayor_e_igual_2_out_3), .out_4(mayor_e_igual_2_out_4));
  mayor_e_igual mayor_e_igual_3 (.A(a_2), .B(b_2), .out_3(mayor_e_igual_3_out_3), .out_4(mayor_e_igual_3_out_4));
  and and_1 (and_1_out, mayor_e_igual_1_out_3, mayor_e_igual_3_out_4);
  or or_1 (or_1_out, mayor_e_igual_1_out_4, and_1_out, and_2_out);
  and and_2 (and_2_out, mayor_e_igual_1_out_3, mayor_e_igual_3_out_3, mayor_e_igual_2_out_4);
  or or_2 (barera_A, or_1_out, and_5_out);
  and and_3 (and_3_out, ~b_3, ~b_2, ~b);  // AND_Gate
  and and_4 (and_4_out, mayor_e_igual_1_out_3, mayor_e_igual_3_out_3, mayor_e_igual_2_out_3);
  and and_5 (and_5_out, and_4_out, ~and_3_out);  // AND_Gate
  and and_6 (barera_B, ~barera_A, ~and_3_out);  // AND_Gate
endmodule
