// Logisim project triangulo eq,is,es.circ as structural Verilog: 3 circuits, main circuit main
module main (
  input  a,
  input  a_2,
  input  a_3,
  input  b,
  input  b_2,
  input  b_3,
  input  c,
  input  c_2,
  input  c_3,
  output equilatero,
  output escaleno,
  output isosceles
);

  wire and_1_out, and_2_out, and_3_out, and_4_out, or_1_out, sumador_1_acarreo, sumador_1_b0_2,
       sumador_1_b1_2, sumador_1_b2_2, sumador_2_acarreo, sumador_2_b0_2, sumador_2_b1_2, sumador_2_b2_2,
       xnor_1_out, xnor_2_out, xnor_3_out, xnor_4_out, xnor_5_out, xnor_6_out, xnor_7_out, xnor_8_out,
       xnor_9_out, xor_1_out;

  and and_1 (and_1_out, sumador_2_acarreo, sumador_1_acarreo);
  xor xor_1 (xor_1_out, sumador_2_acarreo, sumador_1_acarreo);
  // Probe on xor_1_out
  // Probe on and_1_out
  sumador sumador_1 (
    .a2(a), .b2(sumador_2_b2_2), .a1(a_2), .b1(sumador_2_b1_2), .a0(a_3), .b0(sumador_2_b0_2),
    .acarreo_0(1'b0), .acarreo(sumador_1_acarreo), .b2_2(sumador_1_b2_2), .b1_2(sumador_1_b1_2),
    .b0_2(sumador_1_b0_2));
  // Probe on sumador_1_b1_2
  // Probe on sumador_1_b2_2
  sumador sumador_2 (
    .a2(b), .b2(c), .a1(b_2), .b1(c_2), .a0(b_3), .b0(c_3), .acarreo_0(1'b0), .acarreo(sumador_2_acarreo),
    .b2_2(sumador_2_b2_2), .b1_2(sumador_2_b1_2), .b0_2(sumador_2_b0_2));
  // Probe on sumador_1_b0_2
  xnor xnor_1 (xnor_1_out, a, b);
  xnor xnor_2 (xnor_2_out, a_2, b_2);
  xnor xnor_3 (xnor_3_out, a_3, b_3);
  xnor xnor_4 (xnor_4_out, c, a);
  xnor xnor_5 (xnor_5_out, c_2, a_2);
  xnor xnor_6 (xnor_6_out, c_3, a_3);
  xnor xnor_7 (xnor_7_out, c, b);
  xnor xnor_8 (xnor_8_out, c_2, b_2);
  xnor xnor_9 (xnor_9_out, c_3, b_3);
  and and_2 (and_2_out, xnor_1_out, xnor_2_out, xnor_3_out);
  and and_3 (and_3_out, xnor_4_out, xnor_5_out, xnor_6_out);
  and and_4 (and_4_out, xnor_7_out, xnor_8_out, xnor_9_out);
  and and_5 (equilatero, and_2_out, and_3_out);
  or or_1 (or_1_out, and_2_out, and_3_out, and_4_out);
  and and_6 (isosceles, ~equilatero, or_1_out);  // AND_Gate
  and and_7 (escaleno, ~equilatero, ~isosceles);  // AND_Gate
endmodule

// +
module sumador_de_3 (
  input  A,
  input  B,
  input  C,
  output acarreo,
  output Sum
);

  wire aca0_out, aca1_out, Sum0_out;

  xor Sum0 (Sum0_out, A, B);
  and aca1 (aca1_out, C, Sum0_out);
  and aca0 (aca0_out, B, A);
  xor Sum1 (Sum, Sum0_out, C);
  or or_1 (acarreo, aca0_out, aca1_out);

  // Notes on the sheet:
  //   acarreo de sumatoria de anterior columna
  //   suma de primer numero con segundo
endmodule

module sumador (
  input  acarreo_0,
  input  a2,
  input  b2,
  input  a1,
  input  b1,
  input  a0,
  input  b0,
  output acarreo,
  output b2_2,
  output b1_2,
  output b0_2
);

  wire sumador_de_3_2_acarreo, sumador_de_3_3_acarreo;

  sumador_de_3 sumador_de_3_1 (.C(sumador_de_3_2_acarreo), .A(a2), .B(b2), .acarreo(acarreo), .Sum(b2_2));
  sumador_de_3 sumador_de_3_2 (
    .C(sumador_de_3_3_acarreo), .A(a1), .B(b1), .acarreo(sumador_de_3_2_acarreo), .Sum(b1_2));
  sumador_de_3 sumador_de_3_3 (.C(acarreo_0), .A(a0), .B(b0), .acarreo(sumador_de_3_3_acarreo), .Sum(b0_2));
endmodule
