// Logisim project Problema 11.circ as structural Verilog: 4 circuits, main circuit main
module main (
  input  [1:0] A,
  input  [1:0] B,
  output [1:0] R,
  output [1:0] C,
  output E
);

  wire d_1_1_c0, d_2_1_c0, d_2_1_r0, d_3_1_c0, d_3_1_r0;

  D_1 d_1_1 (.A1(A[1]), .A0(A[0]), .B1(B[1]), .B0(B[0]), .C1(C[1]), .C0(d_1_1_c0));
  D_2 d_2_1 (.A1(A[1]), .A0(A[0]), .B1(B[1]), .B0(B[0]), .C0(d_2_1_c0), .R0(d_2_1_r0));
  D_3 d_3_1 (.A1(A[1]), .A0(A[0]), .B1(B[1]), .B0(B[0]), .C0(d_3_1_c0), .R1(R[1]), .R0(d_3_1_r0));
  or or_1 (R[0], d_2_1_r0, d_3_1_r0);
  or or_2 (C[0], d_1_1_c0, d_2_1_c0, d_3_1_c0);
  and and_1 (E, ~B[0], ~B[1]);  // AND_Gate
endmodule

module D_1 (
  input  A1,
  input  A0,
  input  B1,
  input  B0,
  output C1,
  output C0
);

  wire and_1_out;

  and and_1 (and_1_out, ~B1, B0);  // AND_Gate
  and and_2 (C1, A1, and_1_out);
  and and_3 (C0, A0, and_1_out);
endmodule

module D_2 (
  input  A1,
  input  A0,
  input  B1,
  input  B0,
  output C0,
  output R0
);

  wire and_1_out;

  and and_1 (and_1_out, B1, ~B0);  // AND_Gate
  and and_2 (C0, A1, and_1_out);
  and and_3 (R0, A0, and_1_out);
endmodule

module D_3 (
  input  A1,
  input  A0,
  input  B1,
  input  B0,
  output C0,
  output R1,
  output R0
);

  wire and_1_out;

  and and_1 (and_1_out, B1, B0);
  and and_2 (C0, A0, A1, and_1_out);
  and and_3 (R1, A1, ~A0, and_1_out);  // AND_Gate
  and and_4 (R0, ~A1, A0, and_1_out);  // AND_Gate
endmodule
