// Logisim project contador.circ as structural Verilog: 2 circuits, main circuit main
module main (
  input  d,
  input  a,
  output out_3,
  output out_4,
  output out_5,
  output out_6
);

  wire and_1_out, and_2_out, and_3_out, and_4_out, and_5_out, and_6_out, clock_1_out, t_ff_1_qn, t_ff_2_qn,
       t_ff_3_qn, xor_1_out, xor_2_out, xor_3_out;

  Clock clock_1 (.out(clock_1_out));
  T_Flip_Flop t_ff_1 (.clk(clock_1_out), .T(1'b1), .Q(out_6), .Qn(t_ff_1_qn));  // open: preset, reset, en
  and and_1 (and_1_out, out_6, a, 1'b1);
  and and_2 (and_2_out, 1'b1, d, t_ff_1_qn);
  T_Flip_Flop t_ff_2 (.clk(clock_1_out), .T(xor_1_out), .Q(out_5), .Qn(t_ff_2_qn));  // open: preset, reset, en
  xor xor_1 (xor_1_out, and_1_out, and_2_out);
  and and_3 (and_3_out, and_1_out, out_5);
  and and_4 (and_4_out, t_ff_2_qn, and_2_out);
  xor xor_2 (xor_2_out, and_3_out, and_4_out);
  T_Flip_Flop t_ff_3 (.clk(clock_1_out), .T(xor_2_out), .Q(out_4), .Qn(t_ff_3_qn));  // open: preset, reset, en
  and and_5 (and_5_out, and_3_out, out_4);
  xor xor_3 (xor_3_out, and_5_out, and_6_out);
  and and_6 (and_6_out, t_ff_3_qn, and_4_out);
  T_Flip_Flop t_ff_4 (.clk(clock_1_out), .T(xor_3_out), .Q(out_3));  // open: Qn, preset, reset, en
endmodule

module ftrttt (
  input  q3,
  input  q2,
  input  q1,
  input  q0,
  output s3,
  output s2,
  output s1,
  output s0
);

  wire and_1_out, and_2_out, and_3_out, and_4_out, and_5_out, and_6_out, and_7_out, and_8_out, and_9_out,
       not_1_out, not_2_out, not_3_out, not_4_out, not_5_out, not_6_out, not_7_out, not_8_out, not_9_out;

  not not_1 (not_1_out, q3);
  not not_2 (not_2_out, q2);
  not not_3 (not_3_out, q1);
  not not_4 (not_4_out, q0);
  not not_5 (not_5_out, q2);
  and and_1 (and_1_out, not_5_out, q1, q0);
  and and_2 (and_2_out, q2, not_6_out);
  not not_6 (not_6_out, q1);
  and and_3 (and_3_out, q2, not_7_out);
  not not_7 (not_7_out, q0);
  not not_8 (not_8_out, q1);
  and and_4 (and_4_out, not_8_out, q0);
  and and_5 (and_5_out, q1, not_9_out);
  not not_9 (not_9_out, q0);
  not not_10 (s0, q0);
  and and_6 (and_6_out, not_1_out, q2, q1, q0);
  and and_7 (and_7_out, q3, not_2_out);
  and and_8 (and_8_out, q3, not_3_out);
  and and_9 (and_9_out, q3, not_4_out);
  or or_1 (s2, and_1_out, and_2_out, and_3_out);
  or or_2 (s1, and_4_out, and_5_out);
  or or_3 (s3, and_6_out, and_7_out, and_8_out, and_9_out);
endmodule
