// Logisim project divisible por 6.circ as structural Verilog: 8 circuits, main circuit main
module main (
  input  b7,
  input  b6,
  input  b5,
  input  b4,
  input  b3,
  input  b2,
  input  b1,
  input  b0,
  output divisible_por_6
);

  wire and_1_out, and_2_out, and_3_out, n0_3_6_9_1_s, n0_6_1_s, n1_4_7_1_s, n2_5_8_1_s, n2_8_1_s, n4_1_s;

  _0_3_6_9 u_0_3_6_9_1 (.b7(b7), .b6(b6), .b5(b5), .b4(b4), .s(n0_3_6_9_1_s));
  _1_4_7 u_1_4_7_1 (.b7(b7), .b6(b6), .b5(b5), .b4(b4), .s(n1_4_7_1_s));
  _2_5_8 u_2_5_8_1 (.b7(b7), .b6(b6), .b5(b5), .b4(b4), .s(n2_5_8_1_s));
  _0_6 u_0_6_1 (.b3(b3), .b2(b2), .b1(b1), .b0(b0), .s(n0_6_1_s));
  _2_8 u_2_8_1 (.b3(b3), .b2(b2), .b1(b1), .b0(b0), .s(n2_8_1_s));
  _4 u_4_1 (.b3(b3), .b2(b2), .b1(b1), .b0(b0), .s(n4_1_s));
  and and_1 (and_1_out, n0_3_6_9_1_s, n0_6_1_s);
  and and_2 (and_2_out, n1_4_7_1_s, n2_8_1_s);
  and and_3 (and_3_out, n2_5_8_1_s, n4_1_s);
  or or_1 (divisible_por_6, and_1_out, and_2_out, and_3_out);
endmodule

module _0_3_6_9 (
  input  b7,
  input  b6,
  input  b5,
  input  b4,
  output s
);

  wire and_1_out, and_2_out, and_3_out, and_4_out, not_1_out, not_2_out, not_3_out, not_4_out, not_5_out,
       not_6_out;

  not not_1 (not_1_out, b7);
  not not_2 (not_2_out, b6);
  not not_3 (not_3_out, b5);
  not not_4 (not_4_out, b4);
  not not_5 (not_5_out, b6);
  not not_6 (not_6_out, b4);
  and and_1 (and_1_out, not_1_out, not_2_out, not_3_out, not_4_out);
  and and_2 (and_2_out, not_5_out, b5, b4);
  and and_3 (and_3_out, b6, b5, not_6_out);
  and and_4 (and_4_out, b7, b4);
  or or_1 (s, and_1_out, and_2_out, and_3_out, and_4_out);
endmodule

module _1_4_7 (
  input  b7,
  input  b6,
  input  b5,
  input  b4,
  output s
);

  wire and_1_out, and_2_out, and_3_out, not_1_out, not_2_out, not_3_out, not_4_out, not_5_out;

  not not_1 (not_1_out, b7);
  not not_2 (not_2_out, b6);
  not not_3 (not_3_out, b5);
  not not_4 (not_4_out, b5);
  not not_5 (not_5_out, b4);
  and and_1 (and_1_out, not_1_out, not_2_out, not_3_out, b4);
  and and_2 (and_2_out, b6, not_4_out, not_5_out);
  or or_1 (s, and_1_out, and_2_out, and_3_out);
  and and_3 (and_3_out, b6, b5, b4);
endmodule

module _2_5_8 (
  input  b7,
  input  b6,
  input  b5,
  input  b4,
  output s
);

  wire and_1_out, and_2_out, and_3_out, not_1_out, not_2_out, not_3_out, not_4_out;

  not not_1 (not_1_out, b6);
  and and_1 (and_1_out, not_1_out, b5, not_2_out);
  not not_2 (not_2_out, b4);
  and and_2 (and_2_out, b6, not_3_out, b4);
  not not_3 (not_3_out, b5);
  and and_3 (and_3_out, b7, not_4_out);
  not not_4 (not_4_out, b4);
  or or_1 (s, and_1_out, and_2_out, and_3_out);
endmodule

module _0_6 (
  input  b3,
  input  b2,
  input  b1,
  input  b0,
  output s
);

  wire and_1_out, and_2_out, not_1_out, not_2_out, not_3_out, not_4_out, not_5_out;

  not not_1 (not_1_out, b3);
  not not_2 (not_2_out, b2);
  not not_3 (not_3_out, b1);
  not not_4 (not_4_out, b0);
  not not_5 (not_5_out, b0);
  and and_1 (and_1_out, not_1_out, not_2_out, not_3_out, not_4_out);
  or or_1 (s, and_1_out, and_2_out);
  and and_2 (and_2_out, b2, b1, not_5_out);
endmodule

module _2_8 (
  input  b3,
  input  b2,
  input  b1,
  input  b0,
  output s
);

  wire and_1_out, and_2_out, not_1_out, not_2_out, not_3_out;

  not not_1 (not_1_out, b2);
  and and_1 (and_1_out, not_1_out, b1, not_2_out);
  not not_2 (not_2_out, b0);
  and and_2 (and_2_out, b3, not_3_out);
  not not_3 (not_3_out, b0);
  or or_1 (s, and_1_out, and_2_out);
endmodule

module _4 (
  input  b3,
  input  b2,
  input  b1,
  input  b0,
  output s
);

  wire not_1_out, not_2_out;

  not not_1 (not_1_out, b1);
  and and_1 (s, b2, not_1_out, not_2_out);
  not not_2 (not_2_out, b0);
endmodule

module secuencia (
  input  a,
  input  b,
  input  a_2,
  input  b_2,
  output out_5,
  output out_6,
  output out_7,
  output out_8
);

  wire and_1_out, and_2_out, and_3_out, and_4_out, and_5_out, and_6_out, and_7_out, and_8_out, and_9_out,
       and_10_out, and_11_out, and_12_out, clock_1_out, clock_2_out, nor_1_out, nor_2_out, or_1_out,
       or_2_out, or_3_out, or_4_out;

  and and_1 (and_1_out, ~a, b);  // AND_Gate
  nor nor_1 (nor_1_out, a, b);
  and and_2 (and_2_out, ~a_2, b_2);  // AND_Gate
  nor nor_2 (nor_2_out, a_2, b_2);
  and and_3 (and_3_out, and_1_out, ~out_5);  // AND_Gate
  and and_4 (and_4_out, out_5, nor_1_out);
  and and_5 (and_5_out, and_2_out, ~out_7);  // AND_Gate
  and and_6 (and_6_out, out_7, nor_2_out);
  Clock clock_1 (.out(clock_1_out));
  or or_1 (or_1_out, and_3_out, and_4_out);
  Clock clock_2 (.out(clock_2_out));
  or or_2 (or_2_out, and_5_out, and_6_out);
  D_Flip_Flop d_ff_1 (.clk(clock_1_out), .D(or_1_out), .Q(out_6), .reset(and_7_out));  // open: Qn, preset, en
  and and_7 (and_7_out, b, a);
  T_Flip_Flop t_ff_1 (.clk(clock_2_out), .T(or_2_out), .Q(out_8), .reset(and_8_out));  // open: Qn, preset, en
  and and_8 (and_8_out, b_2, a_2);
  and and_9 (and_9_out, and_1_out, out_6);
  and and_10 (and_10_out, ~out_6, nor_1_out);  // AND_Gate
  and and_11 (and_11_out, and_2_out, out_8);
  and and_12 (and_12_out, ~out_8, nor_2_out);  // AND_Gate
  or or_3 (or_3_out, and_9_out, and_10_out);
  or or_4 (or_4_out, and_11_out, and_12_out);
  D_Flip_Flop d_ff_2 (.clk(clock_1_out), .D(or_3_out), .Q(out_5), .reset(and_7_out));  // open: Qn, preset, en
  T_Flip_Flop t_ff_2 (.clk(clock_2_out), .T(or_4_out), .Q(out_7), .reset(and_8_out));  // open: Qn, preset, en
endmodule
