// Logisim project fff.circ as structural Verilog
// sum
module main (
  input  A,
  input  B,
  input  C,
  output sum,
  output acarreo
);

  wire and_1_out, xor_1_out;

  and and_1 (and_1_out, A, B);
  xor xor_1 (xor_1_out, A, B);
  and and_2 (acarreo, C, and_1_out);
  xor xor_2 (sum, xor_1_out, C);
endmodule
